// Logisim project Pi Contest.circ as structural Verilog
module main (
);

  wire clock_1_out, comparator_1_eq, comparator_1_gt, comparator_1_lt, controlled_buffer_1_out,
       counter_1_carry, not_1_out, not_2_out, or_1_out, or_2_out, pull_resistor_1_node, Reset_out, t_ff_1_qn,
       transistor_2_out;
  wire [6:0] demultiplexer_1_out0, demultiplexer_1_out1, demultiplexer_2_out0, demultiplexer_2_out1,
       rom_1_data;
  wire [15:0] counter_2_q;

  Clock clock_1 (.out(clock_1_out));
  not not_1 (not_1_out, clock_1_out);
  Pull_Resistor pull_resistor_1 (.node(pull_resistor_1_node));
  Transistor #(.gate("br")) transistor_1 (.in(clock_1_out), .out(pull_resistor_1_node), .gate(transistor_2_out));
  Transistor transistor_2 (.in(not_1_out), .out(transistor_2_out), .gate(clock_1_out));
  Pull_Resistor pull_resistor_2 (.node(transistor_2_out));
  Happy_PI_Day happy_pi_day_1 ();
  Counter #(.max('h78), .ongoal("load")) counter_1 (
    .D(8'h1), .carry(counter_1_carry), .clk(or_1_out), .clr(Reset_out));  // open: load, count, Q
  or or_1 (or_1_out, pull_resistor_1_node, transistor_2_out);
  T_Flip_Flop t_ff_1 (
    .clk(counter_1_carry), .T(counter_1_carry), .Qn(t_ff_1_qn), .reset(Reset_out));  // open: Q, preset, en
  Counter #(.width(16), .max('h5a00), .ongoal("stay")) counter_2 (
    .Q(counter_2_q), .clk(or_1_out), .clr(Reset_out));  // open: load, D, count, carry
  assign controlled_buffer_1_out = Reset_out ? Reset_out : 1'bz;  // Controlled_Buffer controlled_buffer_1
  Button Reset (.out(Reset_out));
  Comparator #(.width(16), .mode("unsigned")) comparator_1 (
    .a(counter_2_q), .b(16'h2d00), .gt(comparator_1_gt), .eq(comparator_1_eq), .lt(comparator_1_lt));
  Demultiplexer #(.width(7), .disabled(0)) demultiplexer_1 (
    .out0(demultiplexer_1_out0), .out1(demultiplexer_1_out1), .in(rom_1_data), .sel(t_ff_1_qn),
    .en(comparator_1_lt));
  or or_2 (or_2_out, comparator_1_gt, comparator_1_eq);
  ROM #(.addrWidth(16), .dataWidth(7)) rom_1 (.addr(counter_2_q), .data(rom_1_data));  // open: sel
  TTY #(.rows(48), .cols(120)) tty_1 (
    .data(demultiplexer_1_out1), .clk(or_1_out), .we(controlled_buffer_1_out), .clr(controlled_buffer_1_out));
  not not_2 (not_2_out, t_ff_1_qn);
  Demultiplexer #(.width(7), .disabled(0)) demultiplexer_2 (
    .out0(demultiplexer_2_out0), .out1(demultiplexer_2_out1), .in(rom_1_data), .sel(not_2_out), .en(or_2_out));
  TTY #(.rows(48), .cols(120)) tty_2 (
    .data(demultiplexer_2_out0), .clk(or_1_out), .we(controlled_buffer_1_out), .clr(controlled_buffer_1_out));
  TTY #(.rows(48), .cols(120)) tty_3 (
    .data(demultiplexer_1_out0), .clk(or_1_out), .we(controlled_buffer_1_out), .clr(controlled_buffer_1_out));
  TTY #(.rows(48), .cols(120)) tty_4 (
    .data(demultiplexer_2_out1), .clk(or_1_out), .we(controlled_buffer_1_out), .clr(controlled_buffer_1_out));

  // Notes on the sheet:
  //   Happy Pi Day :)
  //   Created by SrBrahma - Reddit
  //   Will correctly display 23039 digits of Pi
  //   The reading is made like those 4 TTY's are just one page.
  //   Pi ASCII
  //   contents of rom_1 (hex, n*v repeats v):
  //   33 2e 31 34 31 35 39 32 36 35 33 35 38 39 37 39 33 32 33 38 34 36 32 36 34 33 33 38 33 32 37 39 35
  //   30 32 38 38 34 31 39 37 31 36 39 33 39 39 33 37 35 31 30 35 38 32 30 39 37 34 39 34 34 35 39 32 33
  //   30 37 38 31 36 34 30 36 32 38 36 32 30 38 39 39 38 36 32 38 30 33 34 38 32 35 33 34 32 31 31 37 30
  //   36 37 39 38 32 31 34 38 30 38 36 35 31 33 32 38 32 33 30 36 36 34 37 30 39 33 38 34 34 36 30 39 35
  //   35 30 35 38 32 32 33 31 37 32 35 33 35 39 34 30 38 31 32 38 34 38 31 31 31 37 34 35 30 32 38 34 31
  //   30 32 37 30 31 39 33 38 35 32 31 31 30 35 35 35 39 36 34 34 36 32 32 39 34 38 39 35 34 39 33 30 33
  //   38 31 39 36 34 34 32 38 38 31 30 39 37 35 36 36 35 39 33 33 34 34 36 31 32 38 34 37 35 36 34 38 32
  //   33 33 37 38 36 37 38 33 31 36 35 32 37 31 32 30 31 39 30 39 31 34 35 36 34 38 35 36 36 39 32 33 34
  //   36 30 33 34 38 36 31 30 34 35 34 33 32 36 36 34 38 32 31 33 33 39 33 36 30 37 32 36 30 32 34 39 31
  //   34 31 32 37 33 37 32 34 35 38 37 30 30 36 36 30 36 33 31 35 35 38 38 31 37 34 38 38 31 35 32 30 39
  //   32 30 39 36 32 38 32 39 32 35 34 30 39 31 37 31 35 33 36 34 33 36 37 38 39 32 35 39 30 33 36 30 30
  //   31 31 33 33 30 35 33 30 35 34 38 38 32 30 34 36 36 35 32 31 33 38 34 31 34 36 39 35 31 39 34 31 35
  //   31 31 36 30 39 34 33 33 30 35 37 32 37 30 33 36 35 37 35 39 35 39 31 39 35 33 30 39 32 31 38 36 31
  //   31 37 33 38 31 39 33 32 36 31 31 37 39 33 31 30 35 31 31 38 35 34 38 30 37 34 34 36 32 33 37 39 39
  //   36 32 37 34 39 35 36 37 33 35 31 38 38 35 37 35 32 37 32 34 38 39 31 32 32 37 39 33 38 31 38 33 30
  //   31 31 39 34 39 31 32 39 38 33 33 36 37 33 33 36 32 34 34 30 36 35 36 36 34 33 30 38 36 30 32 31 33
  //   39 34 39 34 36 33 39 35 32 32 34 37 33 37 31 39 30 37 30 32 31 37 39 38 36 30 39 34 33 37 30 32 37
  //   37 30 35 33 39 32 31 37 31 37 36 32 39 33 31 37 36 37 35 32 33 38 34 36 37 34 38 31 38 34 36 37 36
  //   36 39 34 30 35 31 33 32 30 30 30 35 36 38 31 32 37 31 34 35 32 36 33 35 36 30 38 32 37 37 38 35 37
  //   37 31 33 34 32 37 35 37 37 38 39 36 30 39 31 37 33 36 33 37 31 37 38 37 32 31 34 36 38 34 34 30 39
  //   30 31 32 32 34 39 35 33 34 33 30 31 34 36 35 34 39 35 38 35 33 37 31 30 35 30 37 39 32 32 37 39 36
  //   38 39 32 35 38 39 32 33 35 34 32 30 31 39 39 35 36 31 31 32 31 32 39 30 32 31 39 36 30 38 36 34 30
  //   33 34 34 31 38 31 35 39 38 31 33 36 32 39 37 37 34 37 37 31 33 30 39 39 36 30 35 31 38 37 30 37 32
  //   31 31 33 34 6*39 38 33 37 32 39 37 38 30 34 39 39 35 31 30 35 39 37 33 31 37 33 32 38 31 36 30 39 36
  //   33 31 38 35 39 35 30 32 34 34 35 39 34 35 35 33 34 36 39 30 38 33 30 32 36 34 32 35 32 32 33 30 38
  //   32 35 33 33 34 34 36 38 35 30 33 35 32 36 31 39 33 31 31 38 38 31 37 31 30 31 30 30 30 33 31 33 37
  //   38 33 38 37 35 32 38 38 36 35 38 37 35 33 33 32 30 38 33 38 31 34 32 30 36 31 37 31 37 37 36 36 39
  //   31 34 37 33 30 33 35 39 38 32 35 33 34 39 30 34 32 38 37 35 35 34 36 38 37 33 31 31 35 39 35 36 32
  //   38 36 33 38 38 32 33 35 33 37 38 37 35 39 33 37 35 31 39 35 37 37 38 31 38 35 37 37 38 30 35 33 32
  //   31 37 31 32 32 36 38 30 36 36 31 33 30 30 31 39 32 37 38 37 36 36 31 31 31 39 35 39 30 39 32 31 36
  //   34 32 30 31 39 38 39 33 38 30 39 35 32 35 37 32 30 31 30 36 35 34 38 35 38 36 33 32 37 38 38 36 35
  //   39 33 36 31 35 33 33 38 31 38 32 37 39 36 38 32 33 30 33 30 31 39 35 32 30 33 35 33 30 31 38 35 32
  //   39 36 38 39 39 35 37 37 33 36 32 32 35 39 39 34 31 33 38 39 31 32 34 39 37 32 31 37 37 35 32 38 33
  //   34 37 39 31 33 31 35 31 35 35 37 34 38 35 37 32 34 32 34 35 34 31 35 30 36 39 35 39 35 30 38 32 39
  //   35 33 33 31 31 36 38 36 31 37 32 37 38 35 35 38 38 39 30 37 35 30 39 38 33 38 31 37 35 34 36 33 37
  //   34 36 34 39 33 39 33 31 39 32 35 35 30 36 30 34 30 30 39 32 37 37 30 31 36 37 31 31 33 39 30 30 39
  //   38 34 38 38 32 34 30 31 32 38 35 38 33 36 31 36 30 33 35 36 33 37 30 37 36 36 30 31 30 34 37 31 30
  //   31 38 31 39 34 32 39 35 35 35 39 36 31 39 38 39 34 36 37 36 37 38 33 37 34 34 39 34 34 38 32 35 35
  //   33 37 39 37 37 34 37 32 36 38 34 37 31 30 34 30 34 37 35 33 34 36 34 36 32 30 38 30 34 36 36 38 34
  //   32 35 39 30 36 39 34 39 31 32 39 33 33 31 33 36 37 37 30 32 38 39 38 39 31 35 32 31 30 34 37 35 32
  //   31 36 32 30 35 36 39 36 36 30 32 34 30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
endmodule
