// Logisim project Logiwin Open Project.circ as structural Verilog
module Logiwin (
);

  wire C, console_back_1__4clock_2on_2off, console_back_1_clear, keyboard_1_avail, keyboard_back_1_clock,
       ON_OFF_out, P;
  wire [4:0] joystick_1_x, joystick_1_y;
  wire [6:0] console_back_1_data, keyboard_1_data, keyboard_back_1_out_4;
  wire [7:0] cpu_external_connections_1_external_controller_selector;
  wire [7:7] external_devices_controler_1__1fb;
  wire [9:0] joystick_back_1_output;
  wire [31:0] cpu_external_connections_1_acc, cpu_external_connections_1_external,
       external_devices_controler_1_cpu_out_in, external_devices_controler_1_output_device_1,
       external_devices_controler_1_output_device_2;

  // DotMatrix2 dotmatrix2_1: pin names not known
  Keyboard #(.buflen(256)) keyboard_1 (
    .clk(keyboard_back_1_clock), .avail(keyboard_1_avail), .data(keyboard_1_data));  // open: re, clr
  // RAM ram_1: pin names not known
  Keyboard_Back keyboard_back_1 (
    .Keyboard_Data(keyboard_1_data), .Clock__Feedback(external_devices_controler_1__1fb[7]),
    .out_4(keyboard_back_1_out_4), .Clock(keyboard_back_1_clock), .There_is_char(keyboard_1_avail));
  GPU_____External_Connections gpu_external_connections_1 (
    .Clock(C), .Power(P), .Data_Out_In(external_devices_controler_1_output_device_2));  // open: Update_Screen, out_7, out_8, out_9, out_10, out_11, out_12, out_13, out_14, out_15, out_16, out_17, out_18, out_19, out_20, out_21, out_22, out_23, out_24, out_25, out_26, out_27, out_28, out_29, out_30, out_31, out_32, out_33, out_34, out_35, out_36, out_37, out_38, out_39, out_40, out_41, out_42, Row_Selector, in_1
  Joystick_Back joystick_back_1 (.X(joystick_1_x), .Y(joystick_1_y), .Output(joystick_back_1_output));
  Joystick #(.bits(5)) joystick_1 (.x(joystick_1_x), .y(joystick_1_y));
  CPU____External_Connections cpu_external_connections_1 (
    .External(cpu_external_connections_1_external), .Acc(cpu_external_connections_1_acc), .Power(P),
    .Turn_it_on(ON_OFF_out), .Clock(C),
    .External_Controller_Selector(cpu_external_connections_1_external_controller_selector),
    .External_Input(external_devices_controler_1_cpu_out_in));  // open: SSD_Data_In____Out, SSD_Data_Out____In, RAM_Reset, RAM_Data_In____Out, RAM_Data_Out____In, SSD_Address, RAM_Address, SSD_Clock, RAM_Clock
  // RAM ram_2: pin names not known; wires that end beside it: P
  External_Devices_Controler external_devices_controler_1 (
    .Input_Device_1(keyboard_back_1_out_4), .CPU_In_Out(cpu_external_connections_1_external),
    .CPU_Out_In(external_devices_controler_1_cpu_out_in), .Input_Device_3(joystick_back_1_output),
    .External_Controller_Selector(cpu_external_connections_1_external_controller_selector),
    .Output_Device_2(external_devices_controler_1_output_device_2),
    .Output_Device_1(external_devices_controler_1_output_device_1),
    ._1FB(external_devices_controler_1__1fb[7]));  // open: Input_Device_4, Output_Device_4, Input_Device_2, Output_Device_3, _2FB, _3FB, _4FB, GPU_Additional_bit
  Button ON_OFF (.out(ON_OFF_out));
  TTY #(.rows(20), .cols(44)) tty_1 (
    .data(console_back_1_data), .clk(console_back_1__4clock_2on_2off), .clr(console_back_1_clear));  // open: we
  // Probe on cpu_external_connections_1_acc
  // Probe on cpu_external_connections_1_acc
  // Probe on cpu_external_connections_1_acc
  Console_Back console_back_1 (
    .Data(console_back_1_data), .Console_Data_Clear(external_devices_controler_1_output_device_1), .Power(P),
    .Clear(console_back_1_clear), ._4Clock_2On_2Off(console_back_1__4clock_2on_2off), .Clock_1_1(C));

  // Notes on the sheet:
  //   Never store data on Address 0x000000.
  //   It will get buggy. Readme.
  //   Logiwin
  //   Working like a charm!
  //    Read Readme!
endmodule

module CPU____External_Connections (
  input  [31:0] External_Input,
  input  [31:0] SSD_Data_Out____In,
  input  [31:0] RAM_Data_Out____In,
  input  Turn_it_on,
  output [7:0] External_Controller_Selector,
  output [31:0] External,
  output [31:0] Acc,
  output [31:0] SSD_Data_In____Out,
  output [31:0] RAM_Data_In____Out,
  output [21:0] SSD_Address,
  output [21:0] RAM_Address,
  output SSD_Clock,
  output RAM_Clock,
  output Clock,
  output Power,
  output RAM_Reset
);

  wire controlled_buffer_4_out, cpu_core_1_store_current_address, demultiplexer_1_out0, demultiplexer_1_out1,
       not_1_out, or_1_out, Second_Clock_out, transistor_1_out;
  wire [1:0] cpu_core_1_address_out_2, cpu_core_1_adress_commands, cpu_core_1_jump,
       cpu_core_1_sra__set_relative_address_2, multiplexer_3_out, Program_Counter_q_2, register_1_q;
  wire [2:2] cpu_core_1_jump_2;
  wire [21:0] adder_1_out, adder_2_out, cpu_core_1_address_out, cpu_core_1_sra__set_relative_address,
       demultiplexer_4_out0, demultiplexer_4_out1, demultiplexer_5_out0, demultiplexer_5_out1,
       multiplexer_5_out, Program_Counter_q, Relative_Address_2_q, Relative_Address_q;
  wire [23:0] bit_extender_1_out, controlled_buffer_3_out, multiplexer_6_out;
  wire [24:24] cpu_core_1_sra__set_relative_address_3;
  wire [31:0] cpu_core_1_data_cpu____memory, multiplexer_4_out, pull_resistor_1_node;

  T_Flip_Flop t_ff_1 (.clk(Turn_it_on), .T(Turn_it_on), .Q(Power), .Qn(RAM_Reset));  // open: preset, reset, en
  Demultiplexer #(.select(2), .enable("false")) demultiplexer_1 (
    .out0(demultiplexer_1_out0), .out1(demultiplexer_1_out1),
    .in(cpu_core_1_sra__set_relative_address_3[24]), .sel(cpu_core_1_sra__set_relative_address_2));  // open: out2, out3
  Adder #(.width(22)) adder_1 (.a(demultiplexer_4_out0), .b(Relative_Address_q), .out(adder_1_out));  // open: cin, cout
  Register #(.width(22)) Relative_Address (
    .D(cpu_core_1_sra__set_relative_address), .en(demultiplexer_1_out0), .Q(Relative_Address_q),
    .clk(transistor_1_out), .clr(RAM_Reset));
  Adder #(.width(22)) adder_2 (
    .a(demultiplexer_4_out1), .b(Relative_Address_2_q), .out(adder_2_out));  // open: cin, cout
  Register #(.width(22)) Relative_Address_2 (
    .D(cpu_core_1_sra__set_relative_address), .en(demultiplexer_1_out1), .Q(Relative_Address_2_q),
    .clk(transistor_1_out), .clr(RAM_Reset));
  Multiplexer #(.width(22), .enable("false")) multiplexer_1 (
    .in0(demultiplexer_5_out0), .in1(adder_1_out), .out(SSD_Address), .sel(or_1_out));
  Multiplexer #(.width(22), .enable("false")) multiplexer_2 (
    .in0(demultiplexer_5_out1), .in1(adder_2_out), .out(RAM_Address), .sel(or_1_out));
  Demultiplexer #(.select(2), .disabled(0), .enable("false")) demultiplexer_2 (
    .out0(SSD_Clock), .out1(RAM_Clock), .in(controlled_buffer_4_out), .sel(register_1_q));  // open: out2, out3
  Multiplexer #(.width(2), .enable("false")) multiplexer_3 (
    .in0(Program_Counter_q_2), .in1(cpu_core_1_address_out_2), .out(multiplexer_3_out), .sel(or_1_out));
  Multiplexer #(.select(2), .width(32), .enable("false")) multiplexer_4 (
    .in0(SSD_Data_Out____In), .in1(RAM_Data_Out____In), .out(multiplexer_4_out), .sel(multiplexer_3_out));  // open: in2, in3
  Multiplexer #(.select(2), .width(22), .enable("false")) multiplexer_5 (
    .in0(adder_1_out), .in1(adder_2_out), .out(multiplexer_5_out), .sel(cpu_core_1_address_out_2));  // open: in2, in3
  Register #(.width(2)) register_1 (
    .D(cpu_core_1_address_out_2), .Q(register_1_q), .clk(controlled_buffer_4_out));  // open: en, clr
  Demultiplexer #(.select(2), .width(32), .enable("false")) demultiplexer_3 (
    .out0(SSD_Data_In____Out), .out1(RAM_Data_In____Out), .in(cpu_core_1_data_cpu____memory),
    .sel(cpu_core_1_address_out_2));  // open: out2, out3
  Pull_Resistor pull_resistor_1 (.node(pull_resistor_1_node));
  assign pull_resistor_1_node = cpu_core_1_jump[0] ? multiplexer_4_out : 32'bz;  // Controlled_Buffer controlled_buffer_1
  Demultiplexer #(.select(2), .width(22), .disabled(0), .enable("false")) demultiplexer_4 (
    .out0(demultiplexer_4_out0), .out1(demultiplexer_4_out1), .in(cpu_core_1_address_out),
    .sel(cpu_core_1_address_out_2));  // open: out2, out3
  Demultiplexer #(.select(2), .width(22), .disabled(0), .enable("false")) demultiplexer_5 (
    .out0(demultiplexer_5_out0), .out1(demultiplexer_5_out1), .in(Program_Counter_q),
    .sel(Program_Counter_q_2));  // open: out2, out3
  Bit_Extender #(.in_width(32), .out_width(24)) bit_extender_1 (.in(pull_resistor_1_node), .out(bit_extender_1_out));
  or or_1 (or_1_out, cpu_core_1_adress_commands[0], cpu_core_1_adress_commands[1]);
  Multiplexer #(.select(2), .width(24), .disabled(0), .enable("false")) multiplexer_6 (
    .in0({cpu_core_1_address_out_2, multiplexer_5_out}), .in1(bit_extender_1_out),
    .in2({cpu_core_1_address_out_2, cpu_core_1_address_out}), .out(multiplexer_6_out), .sel(cpu_core_1_jump));  // open: in3
  not not_1 (not_1_out, cpu_core_1_jump_2[2]);
  Pull_Resistor pull_resistor_2 (.node(Clock));
  Clock Second_Clock (.out(Second_Clock_out));
  assign Clock = Power ? Second_Clock_out : 1'bz;  // Controlled_Buffer controlled_buffer_2
  assign controlled_buffer_3_out = cpu_core_1_store_current_address ? {Program_Counter_q_2, Program_Counter_q} : 24'bz;  // Controlled_Buffer controlled_buffer_3
  Pull_Resistor pull_resistor_3 (.node(controlled_buffer_3_out));
  assign controlled_buffer_4_out = transistor_1_out ? cpu_core_1_adress_commands[0] : 1'bz;  // Controlled_Buffer controlled_buffer_4
  Pull_Resistor pull_resistor_4 (.node(controlled_buffer_4_out));
  Counter #(.width(24), .max('hffffff)) Program_Counter (
    .load(cpu_core_1_jump_2[2]), .D(multiplexer_6_out), .count(not_1_out),
    .Q({Program_Counter_q_2, Program_Counter_q}), .clk(Second_Clock_out), .clr(RAM_Reset));  // open: carry
  Transistor #(.\type ("n"), .gate("br")) transistor_1 (.in(Second_Clock_out), .out(transistor_1_out), .gate(Power));
  Pull_Resistor pull_resistor_5 (.node(transistor_1_out));
  CPU____Core cpu_core_1 (
    .Output____External_Input(External), .Data_CPU____Memory(cpu_core_1_data_cpu____memory),
    .Address_Out({cpu_core_1_address_out_2, cpu_core_1_address_out}), .Data_Memory____CPU(multiplexer_4_out),
    .Jump({cpu_core_1_jump_2[2], cpu_core_1_jump}), .Reset(RAM_Reset), .Accumulator_content(Acc),
    .Adress_Commands(cpu_core_1_adress_commands), .Clock(transistor_1_out),
    .External_Controller_Selector(External_Controller_Selector), .External_Output____Input(External_Input),
    .Current_Address__SCA___CAL(controlled_buffer_3_out),
    .Store_Current_Address(cpu_core_1_store_current_address),
    .SRA__Set_Relative_Address({cpu_core_1_sra__set_relative_address_3[24], cpu_core_1_sra__set_relative_address_2, cpu_core_1_sra__set_relative_address}));

  // Notes on the sheet:
  //   RAM_Data_Out____In: pull=down
  //   SSD_Data_Out____In: pull=down
  //   SRA
  //   PC OR ADRS
  //   PC or ADRS OUT
  //   JUMP ADRS
  //   ADRS OUT
  //   MEM SEL
  //   PC OUT
  //   MEM SEL
  //   These DMX are to the future. Like adding other memories; external devices.
  //   I used to use the splitter 32>24bits, but my guess is that the Bit Extender 
  //   is more simulation-friendly.
  //   Jump:
  //   1 = Store
  //   3 = Swap
  //   Bit 2 to enable the Jump
  //   Bits 0 ~ 1 to choose the Jump MUX
  //   _________
  //   Address Commands
  //   2 = Addres Read from value
  //   0 = Jump from direct value (use relative Address)
  //   1 = Jump from memory value (don't use relative Address)
  //   2 = Jump from direct value (don't use relative Address)
  //   Address to Jump, is the Return instruction.)
  //   (note on 2: For now the only instruction that don't use the relative
endmodule

module CPU____Core (
  input  [31:0] Data_Memory____CPU,
  input  Clock,
  input  [31:0] External_Output____Input,
  input  Reset,
  input  [23:0] Current_Address__SCA___CAL,
  output [2:0] Jump,
  output [31:0] Accumulator_content,
  output [1:0] Adress_Commands,
  output [7:0] External_Controller_Selector,
  output [31:0] Data_CPU____Memory,
  output [31:0] Output____External_Input,
  output Store_Current_Address,
  output [24:0] SRA__Set_Relative_Address,
  output [23:0] Address_Out
);

  wire bitfinder_1_found, buffer_3_out, buffer_4_out, buffer_5_out, controlled_buffer_2_out,
       cpu_instructions_1_accumulator_clock, or_5_out, pull_resistor_3_node;
  wire [1:0] cpu_instructions_1_exi_dmx, cpu_instructions_1_lifo_psh_pop__rtn___2b_dmx,
       cpu_instructions_1_rnd_clk_dmx, cpu_instructions_1_sca__store_current_address_dmx;
  wire [2:0] cpu_instructions_1_accumulator_out__dmx, cpu_instructions_1_data_memory_out____in__dmx,
       cpu_instructions_1_inc_dec_dmx, cpu_instructions_1_instructions_out__data__dmx;
  wire [3:2] cpu_instructions_1_lifo_psh_pop__rtn___2b_dmx_2;
  wire [4:0] cpu_instructions_1_alu_selector;
  wire [5:0] cpu_alu_1_alu_flag;
  wire [15:0] counter_1_q, subtractor_1_out;
  wire [23:0] bit_extender_2_out, bit_extender_4_out, cpu_instructions_1_address_out;
  wire [31:0] adder_1_out, adder_2_out, bit_extender_1_out, buffer_1_out, buffer_2_out,
       controlled_buffer_1_out, cpu_alu_1_out, cpu_instructions_1_data_instructions_out,
       demultiplexer_1_out0, demultiplexer_1_out1, demultiplexer_1_out2, demultiplexer_1_out4,
       demultiplexer_1_out5, demultiplexer_1_out6, demultiplexer_1_out7, demultiplexer_2_out0,
       demultiplexer_2_out1, demultiplexer_2_out2, demultiplexer_3_out0, demultiplexer_3_out1,
       demultiplexer_4_out1, demultiplexer_4_out2, demultiplexer_5_out0, demultiplexer_5_out1,
       demultiplexer_6_out1, demultiplexer_6_out2, demultiplexer_6_out3, demultiplexer_6_out4,
       demultiplexer_6_out5, demultiplexer_6_out6, demultiplexer_6_out7, demultiplexer_7_out0,
       demultiplexer_7_out1, demultiplexer_7_out2, demultiplexer_8_out1, demultiplexer_8_out2,
       demultiplexer_8_out3, demultiplexer_8_out4, demultiplexer_8_out5, demultiplexer_8_out7,
       Instruction_Register_q, or_2_out, or_3_out, or_4_out, or_6_out, or_8_out, pull_resistor_2_node,
       Random_Generator_out;

  Demultiplexer #(.select(3), .width(32), .enable("false")) demultiplexer_1 (
    .out0(demultiplexer_1_out0), .out1(demultiplexer_1_out1), .out2(demultiplexer_1_out2),
    .out4(demultiplexer_1_out4), .out5(demultiplexer_1_out5), .out6(demultiplexer_1_out6),
    .out7(demultiplexer_1_out7), .in(Data_Memory____CPU), .sel(cpu_instructions_1_data_memory_out____in__dmx));  // open: out3
  assign Data_CPU____Memory = demultiplexer_8_out3 | demultiplexer_4_out2 | demultiplexer_2_out1 | demultiplexer_3_out1 | demultiplexer_6_out1 | demultiplexer_7_out1 | demultiplexer_5_out1;  // OR_Gate or_1, 32 bits wide
  assign bit_extender_1_out = {{8{1'b0}}, Current_Address__SCA___CAL};  // Bit_Extender bit_extender_1
  Demultiplexer #(.select(2), .width(32), .disabled(0), .enable("false")) demultiplexer_2 (
    .out0(demultiplexer_2_out0), .out1(demultiplexer_2_out1), .out2(demultiplexer_2_out2),
    .in(bit_extender_1_out), .sel(cpu_instructions_1_sca__store_current_address_dmx));  // open: out3
  assign controlled_buffer_1_out = cpu_instructions_1_inc_dec_dmx[2] ? {32{1'b1}} : 32'bz;  // Controlled_Buffer controlled_buffer_1
  Pull_Resistor pull_resistor_1 (.node(controlled_buffer_1_out));
  Adder #(.width(32)) adder_1 (
    .a(controlled_buffer_1_out), .b(or_2_out), .out(adder_1_out), .cin(cpu_instructions_1_inc_dec_dmx[1]));  // open: cout
  assign or_2_out = demultiplexer_1_out6 | demultiplexer_6_out6;  // OR_Gate or_2, 32 bits wide
  Demultiplexer #(.width(32), .enable("false")) demultiplexer_3 (
    .out0(demultiplexer_3_out0), .out1(demultiplexer_3_out1), .in(adder_1_out),
    .sel(cpu_instructions_1_inc_dec_dmx[0]));
  Pull_Resistor pull_resistor_2 (.node(pull_resistor_2_node));
  Demultiplexer #(.select(2), .width(32), .enable("false")) demultiplexer_4 (
    .out1(demultiplexer_4_out1), .out2(demultiplexer_4_out2), .in(External_Output____Input),
    .sel(cpu_instructions_1_exi_dmx));  // open: out0, out3
  Adder #(.width(32)) adder_2 (
    .a(demultiplexer_2_out2), .b(pull_resistor_2_node), .out(adder_2_out),
    .cin(cpu_instructions_1_sca__store_current_address_dmx[1]));  // open: cout
  Demultiplexer #(.width(32), .disabled(0)) demultiplexer_5 (
    .out0(demultiplexer_5_out0), .out1(demultiplexer_5_out1), .in(Random_Generator_out),
    .sel(cpu_instructions_1_rnd_clk_dmx[0]), .en(cpu_instructions_1_rnd_clk_dmx[1]));
  Random #(.width(32)) Random_Generator (
    .clk(cpu_instructions_1_rnd_clk_dmx[1]), .out(Random_Generator_out));  // open: next, clr
  Register #(.width(32), .trigger("low")) Instruction_Register (
    .D(demultiplexer_1_out0), .Q(Instruction_Register_q), .clk(pull_resistor_3_node), .clr(Clock));  // open: en
  BitFinder #(.width(32)) bitfinder_1 (.in(Instruction_Register_q), .found(bitfinder_1_found));  // open: index
  Pull_Resistor pull_resistor_3 (.node(pull_resistor_3_node));
  Transistor #(.gate("br")) transistor_1 (.in(bitfinder_1_found), .out(pull_resistor_3_node), .gate(Reset));
  Demultiplexer #(.select(3), .width(32), .enable("false")) demultiplexer_6 (
    .out1(demultiplexer_6_out1), .out2(demultiplexer_6_out2), .out3(demultiplexer_6_out3),
    .out4(demultiplexer_6_out4), .out5(demultiplexer_6_out5), .out6(demultiplexer_6_out6),
    .out7(demultiplexer_6_out7), .in(Accumulator_content), .sel(cpu_instructions_1_accumulator_out__dmx));  // open: out0
  CPU____ALU cpu_alu_1 (
    .A(Accumulator_content), .B(or_3_out), .Selector(cpu_instructions_1_alu_selector), .Out(cpu_alu_1_out),
    .ALU_Flag(cpu_alu_1_alu_flag));
  assign or_3_out = demultiplexer_8_out2 | demultiplexer_6_out2 | demultiplexer_1_out2;  // OR_Gate or_3, 32 bits wide
  Subtractor #(.width(16)) subtractor_1 (.a(counter_1_q), .b(16'h1), .out(subtractor_1_out));  // open: bin, bout
  assign or_4_out = demultiplexer_8_out1 | demultiplexer_3_out0 | demultiplexer_1_out1 | demultiplexer_4_out1 | demultiplexer_2_out0 | demultiplexer_5_out0 | demultiplexer_7_out0 | cpu_alu_1_out;  // OR_Gate or_4, 32 bits wide
  assign buffer_1_out = buffer_2_out;  // Buffer buffer_1, 32 bits wide
  assign buffer_2_out = or_4_out;  // Buffer buffer_2, 32 bits wide
  Register #(.width(32), .trigger("falling")) Accumulator (
    .D(buffer_1_out), .en(Clock), .Q(Accumulator_content), .clk(cpu_instructions_1_accumulator_clock),
    .clr(Reset));
  buf buffer_3 (buffer_3_out, cpu_instructions_1_lifo_psh_pop__rtn___2b_dmx_2[3]);
  buf buffer_4 (buffer_4_out, buffer_3_out);
  Counter #(.width(16), .max('hffff), .ongoal("stay"), .trigger("falling")) counter_1 (
    .load(buffer_4_out), .count(buffer_5_out), .Q(counter_1_q), .clk(or_5_out), .clr(Reset));  // open: D, carry
  buf buffer_5 (buffer_5_out, or_5_out);
  or or_5 (or_5_out, cpu_instructions_1_lifo_psh_pop__rtn___2b_dmx_2[3], cpu_instructions_1_lifo_psh_pop__rtn___2b_dmx_2[2]);
  assign or_6_out = demultiplexer_1_out5 | adder_2_out | demultiplexer_6_out5 | demultiplexer_8_out5;  // OR_Gate or_6, 32 bits wide
  assign controlled_buffer_2_out = Clock ? cpu_instructions_1_lifo_psh_pop__rtn___2b_dmx_2[2] : 1'bz;  // Controlled_Buffer controlled_buffer_2
  assign Output____External_Input = demultiplexer_8_out4 | demultiplexer_6_out4 | demultiplexer_1_out4;  // OR_Gate or_7, 32 bits wide
  // RAM ram_1: pin names not known; wires that end beside it: subtractor_1_out, counter_1_q, or_6_out, controlled_buffer_2_out, Reset
  Demultiplexer #(.select(2), .width(32), .disabled(0)) demultiplexer_7 (
    .out0(demultiplexer_7_out0), .out1(demultiplexer_7_out1), .out2(demultiplexer_7_out2),
    .sel(cpu_instructions_1_lifo_psh_pop__rtn___2b_dmx),
    .en(cpu_instructions_1_lifo_psh_pop__rtn___2b_dmx_2[3]));  // open: out3, in
  Pull_Resistor pull_resistor_4 (.node(controlled_buffer_2_out));
  Demultiplexer #(.select(3), .width(32), .enable("false")) demultiplexer_8 (
    .out1(demultiplexer_8_out1), .out2(demultiplexer_8_out2), .out3(demultiplexer_8_out3),
    .out4(demultiplexer_8_out4), .out5(demultiplexer_8_out5), .out7(demultiplexer_8_out7),
    .in(cpu_instructions_1_data_instructions_out), .sel(cpu_instructions_1_instructions_out__data__dmx));  // open: out0, out6
  assign or_8_out = demultiplexer_8_out7 | demultiplexer_6_out7 | demultiplexer_1_out7;  // OR_Gate or_8, 32 bits wide
  Bit_Extender #(.in_width(32), .out_width(24)) bit_extender_2 (.in(demultiplexer_7_out2), .out(bit_extender_2_out));
  Bit_Extender #(.in_width(32), .out_width(24)) bit_extender_3 (.in(or_8_out), .out(SRA__Set_Relative_Address[23:0]));
  Bit_Extender #(.in_width(32), .out_width(24)) bit_extender_4 (.in(demultiplexer_6_out3), .out(bit_extender_4_out));
  CPU____Instructions cpu_instructions_1 (
    .Data_In(Instruction_Register_q), .Data_Instructions_Out(cpu_instructions_1_data_instructions_out),
    .Address_Out(cpu_instructions_1_address_out),
    .Instructions_Out__Data__DMX(cpu_instructions_1_instructions_out__data__dmx),
    .ALU_Selector(cpu_instructions_1_alu_selector), .ALU_Flags(cpu_alu_1_alu_flag), .JUMP(Jump),
    .Data_Memory_Out____In__DMX(cpu_instructions_1_data_memory_out____in__dmx),
    .Accumulator_Clock(cpu_instructions_1_accumulator_clock), .Address_Commands(Adress_Commands),
    .Acc(Accumulator_content), .Set_Relative_Address(SRA__Set_Relative_Address[24]),
    .External_Controller_Selector(External_Controller_Selector), .EXI_DMX(cpu_instructions_1_exi_dmx),
    .Inc_Dec_DMX(cpu_instructions_1_inc_dec_dmx),
    .Accumulator_Out__DMX(cpu_instructions_1_accumulator_out__dmx),
    .SCA__Store_Current_Address_DMX({Store_Current_Address, cpu_instructions_1_sca__store_current_address_dmx}),
    .LIFO_PSH_POP__RTN___2b_DMX({cpu_instructions_1_lifo_psh_pop__rtn___2b_dmx_2, cpu_instructions_1_lifo_psh_pop__rtn___2b_dmx}),
    .RND_CLK_DMX(cpu_instructions_1_rnd_clk_dmx));
  assign Address_Out = cpu_instructions_1_address_out | bit_extender_4_out | bit_extender_2_out;  // OR_Gate or_9, 24 bits wide

  // Notes on the sheet:
  //   ACC DMX
  //   LIFO
  //   Instruction Data Out DMX
  //   *
endmodule

module CPU____Instructions (
  input  [31:0] Data_In,
  input  [31:0] Acc,
  input  [5:0] ALU_Flags,
  output [2:0] Data_Memory_Out____In__DMX,
  output Accumulator_Clock,
  output [2:0] Accumulator_Out__DMX,
  output Set_Relative_Address,
  output [4:0] ALU_Selector,
  output [2:0] Instructions_Out__Data__DMX,
  output [31:0] Data_Instructions_Out,
  output [23:0] Address_Out,
  output [1:0] Address_Commands,
  output [1:0] EXI_DMX,
  output [3:0] LIFO_PSH_POP__RTN___2b_DMX,
  output [2:0] Inc_Dec_DMX,
  output [7:0] External_Controller_Selector,
  output [1:0] RND_CLK_DMX,
  output [2:0] SCA__Store_Current_Address_DMX,
  output [2:0] JUMP
);

  wire ACC_0, ACC_1_nACC, ACC_1_nMEM, ACC_1_tilde, ACC_X, ALU_0, ALU_1_nACC, ALU_1_nMEM, ALU_1_tilde, ALU_X,
       bitfinder_1_found, comparator_1_eq, controlled_inverter_1_out, decoder_1_out2, ERS, EXI_tilde, EXO_0,
       EXO_1_nACC, EXO_1_nMEM, EXO_1_tilde, EXO_X, INC_DEC, INC_DEC_nACC, JA_out, JAE_out, JBE_out, JE_out,
       JG_out, JMP_0, JMP_1_nACC, JMP_1_tilde, JMP_X, or_1_out, or_2_out, or_3_out, or_4_out, or_5_out,
       or_6_out, POP_nACC, POP_tilde, PSH_0, PSH_1_nACC, PSH_1_nMEM, PSH_1_tilde, PSH_X,
       pull_resistor_5_node, pull_resistor_7_node, pull_resistor_9_node, pull_resistor_12_node,
       pull_resistor_14_node, pull_resistor_15_node, RND_nACC, SCA_nACC, SCA_tilde, SRA_0, SRA_1_nACC,
       SRA_1_nMEM, SRA_1_tilde, STO, SWP, transistor_2_out, transistor_3_out;
  wire [1:0] DATA_OUT_out;
  wire [4:0] demultiplexer_12_out0, demultiplexer_12_out2;
  wire [18:0] JUMPCodes;
  wire [23:0] demultiplexer_13_out1, register_1_q;
  wire [31:0] controlled_buffer_1_out;

  assign JA_out = ALU_Flags[1] ? JUMPCodes[5] : 1'bz;  // Controlled_Buffer JA
  Pull_Resistor pull_resistor_1 (.node(JA_out));
  or or_1 (or_1_out, JUMPCodes[1], JUMPCodes[2]);
  assign controlled_buffer_1_out = or_1_out ? Acc : 32'bz;  // Controlled_Buffer controlled_buffer_1
  Comparator #(.width(32), .mode("unsigned")) comparator_1 (
    .a(controlled_buffer_1_out), .b({32{1'b0}}), .eq(comparator_1_eq));  // open: gt, lt
  assign JAE_out = or_2_out ? JUMPCodes[6] : 1'bz;  // Controlled_Buffer JAE
  Pull_Resistor pull_resistor_2 (.node(JAE_out));
  assign JG_out = ALU_Flags[2] ? JUMPCodes[7] : 1'bz;  // Controlled_Buffer JG
  Pull_Resistor pull_resistor_3 (.node(JG_out));
  or or_2 (or_2_out, ALU_Flags[1], ALU_Flags[3]);
  or or_3 (or_3_out, ALU_Flags[3], ALU_Flags[2]);
  or or_4 (or_4_out, ALU_Flags[3], ALU_Flags[4]);
  or or_5 (or_5_out, ALU_Flags[3], ALU_Flags[5]);
  Pull_Resistor pull_resistor_4 (.node(comparator_1_eq));
  Pull_Resistor pull_resistor_5 (.node(pull_resistor_5_node));
  assign pull_resistor_5_node = JUMPCodes[1] ? comparator_1_eq : 1'bz;  // Controlled_Buffer controlled_buffer_2
  assign controlled_inverter_1_out = JUMPCodes[2] ? ~comparator_1_eq : 1'bz;  // Controlled_Inverter controlled_inverter_1
  Pull_Resistor pull_resistor_6 (.node(controlled_inverter_1_out));
  Pull_Resistor pull_resistor_7 (.node(pull_resistor_7_node));
  assign pull_resistor_7_node = or_3_out ? JUMPCodes[8] : 1'bz;  // Controlled_Buffer JGE
  assign JE_out = ALU_Flags[3] ? JUMPCodes[9] : 1'bz;  // Controlled_Buffer JE
  Pull_Resistor pull_resistor_8 (.node(JE_out));
  Pull_Resistor pull_resistor_9 (.node(pull_resistor_9_node));
  Transistor #(.gate("br")) transistor_1 (.in(JUMPCodes[4]), .out(pull_resistor_9_node), .gate(ALU_Flags[0]));
  Transistor #(.\type ("n")) transistor_2 (.in(ALU_Flags[0]), .out(transistor_2_out), .gate(JUMPCodes[3]));
  Pull_Resistor pull_resistor_10 (.node(transistor_2_out));
  Transistor #(.gate("br")) transistor_3 (.in(JUMPCodes[10]), .out(transistor_3_out), .gate(ALU_Flags[3]));
  Pull_Resistor pull_resistor_11 (.node(transistor_3_out));
  Pull_Resistor pull_resistor_12 (.node(pull_resistor_12_node));
  assign pull_resistor_12_node = ALU_Flags[4] ? JUMPCodes[11] : 1'bz;  // Controlled_Buffer JB
  Register #(.width(24)) register_1 (.D(Data_In[23:0]), .Q(register_1_q), .clk(or_6_out));  // open: en, clr
  or or_6 (or_6_out, SCA_tilde, SRA_1_tilde, ALU_1_tilde, INC_DEC, JMP_1_tilde, EXO_1_tilde, ACC_1_tilde, RND_CLK_DMX[1], PSH_1_tilde, POP_tilde, EXI_tilde);
  Demultiplexer #(.disabled(0), .enable("false")) demultiplexer_1 (
    .out0(EXI_DMX[0]), .out1(EXI_DMX[1]), .in(EXI_tilde), .sel(bitfinder_1_found));
  Demultiplexer #(.enable("false")) demultiplexer_2 (
    .out0(POP_nACC), .out1(LIFO_PSH_POP__RTN___2b_DMX[0]), .in(POP_tilde), .sel(bitfinder_1_found));
  Demultiplexer #(.enable("false")) demultiplexer_3 (
    .out0(PSH_1_nACC), .out1(PSH_1_nMEM), .in(PSH_1_tilde), .sel(bitfinder_1_found));
  Demultiplexer #(.enable("false")) demultiplexer_4 (
    .out0(RND_nACC), .out1(RND_CLK_DMX[0]), .in(RND_CLK_DMX[1]), .sel(bitfinder_1_found));
  Demultiplexer #(.enable("false")) demultiplexer_5 (
    .out0(ACC_1_nACC), .out1(ACC_1_nMEM), .in(ACC_1_tilde), .sel(bitfinder_1_found));
  Demultiplexer #(.enable("false")) demultiplexer_6 (
    .out0(EXO_1_nACC), .out1(EXO_1_nMEM), .in(EXO_1_tilde), .sel(bitfinder_1_found));
  Demultiplexer #(.enable("false")) demultiplexer_7 (
    .out0(JMP_1_nACC), .out1(JUMP[0]), .in(JMP_1_tilde), .sel(bitfinder_1_found));
  Demultiplexer #(.enable("false")) demultiplexer_8 (
    .out0(INC_DEC_nACC), .out1(Inc_Dec_DMX[0]), .in(INC_DEC), .sel(bitfinder_1_found));
  Demultiplexer #(.enable("false")) demultiplexer_9 (
    .out0(ALU_1_nACC), .out1(ALU_1_nMEM), .in(ALU_1_tilde), .sel(bitfinder_1_found));
  Demultiplexer #(.enable("false")) demultiplexer_10 (
    .out0(SRA_1_nACC), .out1(SRA_1_nMEM), .in(SRA_1_tilde), .sel(bitfinder_1_found));
  Demultiplexer #(.enable("false")) demultiplexer_11 (
    .out0(SCA_nACC), .out1(SCA__Store_Current_Address_DMX[0]), .in(SCA_tilde), .sel(bitfinder_1_found));
  or or_7 (SCA__Store_Current_Address_DMX[2], SCA_tilde, SCA__Store_Current_Address_DMX[1]);
  assign JBE_out = or_4_out ? JUMPCodes[12] : 1'bz;  // Controlled_Buffer JBE
  Pull_Resistor pull_resistor_13 (.node(JBE_out));
  Pull_Resistor pull_resistor_14 (.node(pull_resistor_14_node));
  assign pull_resistor_14_node = ALU_Flags[5] ? JUMPCodes[13] : 1'bz;  // Controlled_Buffer JL
  Demultiplexer #(.select(2), .width(5), .enable("false")) demultiplexer_12 (
    .out0(demultiplexer_12_out0), .out1(ALU_Selector), .out2(demultiplexer_12_out2), .in(Data_In[28:24]),
    .sel(Data_In[30:29]));  // open: out3
  Decoder #(.select(2), .enable("false")) decoder_1 (
    .out2(decoder_1_out2), .sel(Data_In[30:29]));  // open: out0, out1, out3
  BitFinder #(.width(24)) bitfinder_1 (.in(register_1_q), .found(bitfinder_1_found));  // open: index
  Pull_Resistor pull_resistor_15 (.node(pull_resistor_15_node));
  assign pull_resistor_15_node = or_5_out ? JUMPCodes[14] : 1'bz;  // Controlled_Buffer JLE
  Decoder #(.select(5), .enable("false")) decoder_2 (
    .out1(ACC_X), .out2(STO), .out3(ERS), .out4(SWP), .out7(SCA__Store_Current_Address_DMX[1]),
    .out8(JUMPCodes[0]), .out9(JUMPCodes[1]), .out10(JUMPCodes[2]), .out11(JUMPCodes[3]),
    .out12(JUMPCodes[4]), .out13(JUMPCodes[5]), .out14(JUMPCodes[6]), .out15(JUMPCodes[7]),
    .out16(JUMPCodes[8]), .out17(JUMPCodes[9]), .out18(JUMPCodes[10]), .out19(JUMPCodes[11]),
    .out20(JUMPCodes[12]), .out21(JUMPCodes[13]), .out22(JUMPCodes[14]), .out23(JUMPCodes[15]),
    .out24(JUMPCodes[16]), .out25(JUMPCodes[17]), .out26(JUMPCodes[18]),
    .out27(LIFO_PSH_POP__RTN___2b_DMX[1]), .out28(Inc_Dec_DMX[1]), .out29(Inc_Dec_DMX[2]), .out30(SCA_tilde),
    .out31(Set_Relative_Address), .sel(demultiplexer_12_out0));  // open: out0, out5, out6
  Decoder #(.select(5), .disabled(0)) decoder_3 (
    .out0(RND_CLK_DMX[1]), .out1(PSH_X), .out2(POP_tilde), .out3(External_Controller_Selector[0]),
    .out4(External_Controller_Selector[1]), .out5(External_Controller_Selector[2]),
    .out6(External_Controller_Selector[3]), .out7(External_Controller_Selector[4]),
    .out8(External_Controller_Selector[5]), .out9(External_Controller_Selector[6]),
    .out10(External_Controller_Selector[7]), .sel(demultiplexer_12_out2), .en(decoder_1_out2));  // open: out11, out12, out13, out14, out15, out16, out17, out18, out19, out20, out21, out22, out23, out24, out25, out26, out27, out28, out29, out30, out31
  or or_8 (JUMP[2], LIFO_PSH_POP__RTN___2b_DMX[1], JMP_X);
  or or_9 (JMP_X, JUMPCodes[0], SCA__Store_Current_Address_DMX[1], pull_resistor_9_node, transistor_2_out, pull_resistor_5_node, controlled_inverter_1_out, JA_out, JAE_out, JG_out, pull_resistor_7_node, JE_out, transistor_3_out, pull_resistor_12_node, JBE_out, pull_resistor_14_node, pull_resistor_15_node);
  buf or_10 (JUMP[1], LIFO_PSH_POP__RTN___2b_DMX[1]);  // OR_Gate
  BitFinder #(.width(4)) bitfinder_2 (.in(External_Controller_Selector[3:0]), .found(EXO_X));  // open: index
  BitFinder #(.width(4)) bitfinder_3 (.in(External_Controller_Selector[7:4]), .found(EXI_tilde));  // open: index
  Demultiplexer #(.select(2), .width(24), .enable("false")) demultiplexer_13 (
    .out1(demultiplexer_13_out1), .out2(Address_Out), .in(Data_In[23:0]), .sel(DATA_OUT_out));  // open: out0, out3
  or ADRS_OUT (DATA_OUT_out[1], ACC_1_nMEM, JMP_X, EXO_1_nMEM, STO, ALU_1_nMEM, LIFO_PSH_POP__RTN___2b_DMX[0], SCA__Store_Current_Address_DMX[0], SRA_1_nMEM, RND_CLK_DMX[0], Inc_Dec_DMX[0], ERS, PSH_1_nMEM);
  ROM #(.addrWidth(14), .dataWidth(18)) rom_1 ();  // open: addr, data, sel
  assign Data_Instructions_Out = {{8{1'b0}}, demultiplexer_13_out1};  // Bit_Extender bit_extender_1
  or DATA_OUT (DATA_OUT_out[0], EXO_0, ACC_0, SRA_0, ALU_0, PSH_0);
  or or_11 (Accumulator_Clock, EXI_DMX[0], SCA_nACC, ALU_X, POP_nACC, ACC_X, INC_DEC_nACC, RND_nACC, SWP);
  BitFinder #(.width(5)) bitfinder_4 (.in(ALU_Selector), .found(ALU_X));  // open: index
  or or_12 (Address_Commands[1], SWP, ACC_1_nMEM, ALU_1_nMEM, JUMP[0], SRA_1_nMEM, PSH_1_nMEM, EXO_1_nMEM, Inc_Dec_DMX[0]);
  Decoder #(.disabled(0)) decoder_4 (.out0(ALU_0), .out1(ALU_1_tilde), .sel(Data_In[31]), .en(ALU_X));
  Decoder #(.disabled(0)) decoder_5 (.out0(ACC_0), .out1(ACC_1_tilde), .sel(Data_In[31]), .en(ACC_X));
  Decoder #(.disabled(0)) decoder_6 (.out0(JMP_0), .out1(JMP_1_tilde), .sel(Data_In[31]), .en(JMP_X));
  Decoder #(.disabled(0)) decoder_7 (.out0(EXO_0), .out1(EXO_1_tilde), .sel(Data_In[31]), .en(EXO_X));
  Decoder #(.disabled(0)) decoder_8 (.out0(SRA_0), .out1(SRA_1_tilde), .sel(Data_In[31]), .en(Set_Relative_Address));
  Decoder #(.disabled(0)) decoder_9 (.out0(PSH_0), .out1(PSH_1_tilde), .sel(Data_In[31]), .en(PSH_X));
  or or_13 (LIFO_PSH_POP__RTN___2b_DMX[2], POP_tilde, LIFO_PSH_POP__RTN___2b_DMX[1]);
  or or_14 (LIFO_PSH_POP__RTN___2b_DMX[3], PSH_X, SCA__Store_Current_Address_DMX[1]);
  or or_15 (Data_Memory_Out____In__DMX[0], SRA_1_nMEM, PSH_1_nMEM, ACC_1_tilde);
  or or_16 (Data_Memory_Out____In__DMX[1], SRA_1_nMEM, ALU_1_tilde, Inc_Dec_DMX[0], Inc_Dec_DMX[0]);
  or or_17 (Data_Memory_Out____In__DMX[2], SRA_1_nMEM, PSH_1_nMEM, Inc_Dec_DMX[0], EXO_1_nMEM);
  or or_18 (Accumulator_Out__DMX[0], ACC_1_nACC, JMP_1_nACC, PSH_1_nACC, INC_DEC_nACC, SRA_1_nACC, STO);
  or or_19 (Accumulator_Out__DMX[1], ACC_1_nACC, JMP_1_nACC, SRA_1_nACC, ALU_1_nACC);
  or or_20 (Accumulator_Out__DMX[2], SRA_1_nACC, PSH_1_nACC, EXO_1_nACC, INC_DEC_nACC);
  or or_21 (Instructions_Out__Data__DMX[0], SRA_0, PSH_0, ACC_0);
  or or_22 (Instructions_Out__Data__DMX[1], ALU_0, SRA_0);
  or or_23 (Instructions_Out__Data__DMX[2], SRA_0, PSH_0, EXO_0);
  or Store (Address_Commands[0], SCA__Store_Current_Address_DMX[0], SWP, RND_CLK_DMX[0], ERS, Inc_Dec_DMX[0], EXI_DMX[1], STO, LIFO_PSH_POP__RTN___2b_DMX[0]);
  or or_24 (INC_DEC, Inc_Dec_DMX[1], Inc_Dec_DMX[2]);

  // Other names for the same wires on the sheet: Read_Address_Content = Address_Commands[1]; LSB_31 = Data_In[31];
  //   EXI_nACC = EXI_DMX[0]; EXI_nMEM = EXI_DMX[1]; EXO[3:0] = External_Controller_Selector[3:0];
  //   EXI[3:0] = External_Controller_Selector[7:4]; INC_DEC_nMEM = Inc_Dec_DMX[0];
  //   INC_DEC_tilde[1:0] = Inc_Dec_DMX[2:1]; JMP_1_nMEM = JUMP[0]; POP_nMEM = LIFO_PSH_POP__RTN___2b_DMX[0];
  //   RTN = LIFO_PSH_POP__RTN___2b_DMX[1]; RND_nMEM = RND_CLK_DMX[0]; RND_tilde = RND_CLK_DMX[1];
  //   SCA_nMEM = SCA__Store_Current_Address_DMX[0]; CAL = SCA__Store_Current_Address_DMX[1];
  //   SRA_X = Set_Relative_Address

  // Notes on the sheet:
  //   Data_In: pull=down
  //   LSB 2 = Greater
  //   LSB 3 = Equal
  //   If no additional information is given,
  //   JC/JNC
  //   LSB 0 = CMP Flag
  //   LSB 1 = Above
  //   LSB 4 = Below
  //   LSB 5 = Lesser
  //   Tunnel labeling:
  //   ACC X = The raw form of the instruction. Still will be treated.
  //   ACC 0 = ACC instruction and the LSB 31 is 0
  //   ACC 1~ = LSB 31 is 1. Have a complexiest name.
  //   ACC 1~ACC = ... LSB 31 is 1 and uses the Accumulator
  //   (instruction argument (LSB 0 ~ 23) is 0
  //   (instruction argument (LSB 0 ~ 23) is NOT 0
  //   POP~ = Another raw form of the instruction.
  //   - Will be treated, but the LSB 31 = don't care.
  //   POP~ACC = ... LSB 31 is 1 and uses the Accumulator
  //   (instruction argument (LSB 0 ~ 23) is 0
  //   POP~MEM = ... LSB 31 is 1 and uses a Memory Address
  //   (instruction argument (LSB 0 ~ 23) is NOT 0
  //   If has a ~, means that it have a ACC and/or MEM variant
  //    means there is no variants or is a unusual tunnel
  //   it will be specified what means.
  //   REMEMBER:
  //   A lot of stuff look really ugly, but is in your benefit :)
  //   JA
  //   ERS = A raw instruction that will not be treated and have a complexiest name.
  //   ACC 1~MEM = ... LSB 31 is 1 and uses a Memory Address
  //   So, if is XYZ 1 or 0, specifies that it has 2 variants using the LSB 31
  //   The $ will usually means Selector (like in EXO/EXI). In other cases,
  //   The smaller the number of nodes in the wires, the higher is a simulation frequency
  //   Possible Optimization: Does other instructions are executed due delay?
  //   JAE
  //   JG
  //   ---Jump Codes Instruction---
  //   JGE
  //   JE
  //   JZ/JNZ
  //   JNE
  //   JNE
  //   JB
  //   0x00/0x80 -> 0x1F/0x9F
  //   0x20/0xA0 -> 0x3F/0xBF
  //   0x40/0xC0 -> 0x5F/0xDF
  //   0x60/0xE0 -> 0x8F/0xFF
  //   2 = Store on LIFO
  //   LSB 2 to enable
  //   JBE
  //   JL
  //   0 = Store on Accumulator
  //   1 = Store on given Address
  //   JLE
  //   All this project was made by
  //   Henrique Bruno Fantauzzi de Almeida
  //   (SrBrahma)
  //   (just to say I made this if someday
  //   I need to prove it)
  //   ACC
  //   STO
  //   ERS
  //   SWP
  //   CAL
  //   JMP
  //   JZ
  //   JNZ
  //   JC
  //   JNC
  //   JA
  //   JAE
  //   JG
  //   JGE
  //   JE
  //   JNE
  //   JB
  //   JBE
  //   JL
  //   JLE
  //   RESERVED
  //   RTN
  //   INC
  //   DEC
  //   SCA
  //   SRA
  //   RND
  //   PSH
  //   POP
  //   TXT
  //   KEY
  //   1 = Accumulator
  //   2 = Memory
  //   JLE
  //   JL
  //   JBE
  //   JB
  //   JNE
  //   JE
  //   JGE
  //   JG
  //   JAE
  //   JA
  //   JNC
  //   JC
  //   JNZ
  //   JZ
  //   JMP
  //   Jump:
  //   LSB 2 to enable the Jump
  //   LSB 0 ~ 1 to choose the Jump MUX
  //   24bit "Data In" DMX
  //   0 = Nothing
  //   1 = Data Out
  //   2 = Address
  //   contents of rom_1 (hex, n*v repeats v):
  //   0 1 2 3 4 5 6 7 8 9 10 11 12 13 14 15 16 17 18 19 20 21 22 23 24 25 26 27 28 29 30 31 32 33 34 35 36
  //   37 38 39 40 41 42 43 44 45 46 47 48 49 50 51 52 53 54 55 56 57 58 59 60 61 62 63 64 65 66 67 68 69
  //   70 71 72 73 74 75 76 77 78 79 80 81 82 83 84 85 86 87 88 89 90 91 92 93 94 95 96 97 98 99 100 101
  //   102 103 104 105 106 107 108 109 110 111 112 113 114 115 116 117 118 119 120 121 122 123 124 125 126
  //   127 128 129 130 131 132 133 134 135 136 137 138 139 140 141 142 143 144 145 146 147 148 149 150 151
  //   152 153 154 155 156 157 158 159 160 161 162 163 164 165 166 167 168 169 170 171 172 173 174 175 176
  //   177 178 179 180 181 182 183 184 185 186 187 188 189 190 191 192 193 194 195 196 197 198 199 200 201
  //   202 203 204 205 206 207 208 209 210 211 212 213 214 215 216 217 218 219 220 221 222 223 224 225 226
  //   227 228 229 230 231 232 233 234 235 236 237 238 239 240 241 242 243 244 245 246 247 248 249 250 251
  //   252 253 254 255 256 257 258 259 260 261 262 263 264 265 266 267 268 269 270 271 272 273 274 275 276
  //   277 278 279 280 281 282 283 284 285 286 287 288 289 290 291 292 293 294 295 296 297 298 299 300 301
  //   302 303 304 305 306 307 308 309 310 311 312 313 314 315 316 317 318 319 320 321 322 323 324 325 326
  //   327 328 329 330 331 332 333 334 335 336 337 338 339 340 341 342 343 344 345 346 347 348 349 350 351
  //   352 353 354 355 356 357 358 359 360 361 362 363 364 365 366 367 368 369 370 371 372 373 374 375 376
  //   377 378 379 380 381 382 383 384 385 386 387 388 389 390 391 392 393 394 395 396 397 398 399 400 401
  //   402 403 404 405 406 407 408 409 410 411 412 413 414 415 416 417 418 419 420 421 422 423 424 425 426
  //   427 428 429 430 431 432 433 434 435 436 437 438 439 440 441 442 443 444 445 446 447 448 449 450 451
  //   452 453 454 455 456 457 458 459 460 461 462 463 464 465 466 467 468 469 470 471 472 473 474 475 476
  //   477 478 479 480 481 482 483 484 485 486 487 488 489 490 491 492 493 494 495 496 497 498 499 500 501
  //   502 503 504 505 506 507 508 509 510 511 512 513 514 515 516 517 518 519 520 521 522 523 524 525 526
  //   527 528 529 530 531 532 533 534 535 536 537 538 539 540 541 542 543 544 545 546 547 548 549 550 551
  //   552 553 554 555 556 557 558 559 560 561 562 563 564 565 566 567 568 569 570 571 572 573 574 575 576
  //   577 578 579 580 581 582 583 584 585 586 587 588 589 590 591 592 593 594 595 596 597 598 599 600 601
  //   602 603 604 605 606 607 608 609 610 611 612 613 614 615 616 617 618 619 620 621 622 623 624 625 626
  //   627 628 629 630 631 632 633 634 635 636 637 638 639 640 641 642 643 644 645 646 647 648 649 650 651
  //   652 653 654 655 656 657 658 659 660 661 662 663 664 665 666 667 668 669 670 671 672 673 674 675 676
  //   677 678 679 680 681 682 683 684 685 686 687 688 689 690 691 692 693 694 695 696 697 698 699 700 701
  //   702 703 704 705 706 707 708 709 710 711 712 713 714 715 716 717 718 719 720 721 722 723 724 725 726
  //   727 728 729 730 731 732 733 734 735 736 737 738 739 740 741 742 743 744 745 746 747 748 749 750 751
  //   752 753 754 755 756 757 758 759 760 761 762 763 764 765 766 767 768 769 770 771 772 773 774 775 776
  //   777 778 779 780 781 782 783 784 785 786 787 788 789 790 791 792 793 794 795 796 797 798 799 800 801
  //   802 803 804 805 806 807 808 809 810 811 812 813 814 815 816 817 818 819 820 821 822 823 824 825 826
  //   827 828 829 830 831 832 833 834 835 836 837 838 839 840 841 842 843 844 845 846 847 848 849 850 851
  //   852 853 854 855 856 857 858 859 860 861 862 863 864 865 866 867 868 869 870 871 872 873 874 875 876
  //   877 878 879 880 881 882 883 884 885 886 887 888 889 890 891 892 893 894 895 896 897 898 899 900 901
  //   902 903 904 905 906 907 908 909 910 911 912 913 914 915 916 917 918 919 920 921 922 923 924 925 926
  //   927 928 929 930 931 932 933 934 935 936 937 938 939 940 941 942 943 944 945 946 947 948 949 950 951
  //   952 953 954 955 956 957 958 959 960 961 962 963 964 965 966 967 968 969 970 971 972 973 974 975 976
  //   977 978 979 980 981 982 983 984 985 986 987 988 989 990 991 992 993 994 995 996 997 998 999 1000
  //   1001 1002 1003 1004 1005 1006 1007 1008 1009 1010 1011 1012 1013 1014 1015 1016 1017 1018 1019 1020
  //   1021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
  //   BCD decoder (WIP)
  //   The jump instructions are order inverted here.
  //   0 = Jump from direct value (use relative Address)
  //   1 = Jump from memory value (don't use relative Address)
  //   2 = Jump from direct value (don't use relative Address)
  //   (note on 2: For now the only instruction that don't use the relative
  //   Address to Jump, is the Return instruction.)
  //   5 = LIFO
  //   5 = LIFO
  //   0 = Nothing
  //   2 = ALU B
  //   3 = nothing
  //   5 = LIFO
  //   6 = nothing
  //   3 = Swap
  //   LSB 2 = POP
  //   LSB 3 = PSH
  //   0 = Instructions (default)
  //   1 = Accumulator
  //   2 = ALU B
  //   3 = nothing
  //   4 = External Output
  //   6 = Inc/Dec
  //   7 = SRA; Set Relative Address
  //   0 = nothing
  //   1 = Data In -> Out
  //   2 = ALU B
  //   3 = Address Out
  //   4 = Extenal Output
  //   6 = Inc/Dec
  //   7 = SRA; Set Relative Address
  //   1 = Accumulator
  //   4 = Extenal Output
  //   7 = SRA; Set Relative Address
  //   1 = Store data at given Address
  //   2 = Read Address Content
  //   LSB 0~1 = POP DMX
  //   0 = Accumulator
  //   1 = Data In > Out
  //   2 = Address Out
endmodule

module CPU____ALU (
  input  [31:0] A,
  input  [4:0] Selector,
  input  [31:0] B,
  output [5:0] ALU_Flag,
  output [31:0] Out
);

  wire adder_1_cout, bitfinder_1_found, bitfinder_2_found, bitfinder_3_found, bitfinder_4_found,
       bitfinder_5_found, comparator_2_eq, decoder_1_out1, decoder_1_out2, decoder_1_out3, decoder_1_out4,
       decoder_1_out5, decoder_1_out6, or_1_out, or_2_out, or_3_out, or_4_out, subtractor_1_bout;
  wire [2:0] bit_extender_1_out;
  wire [4:0] bit_extender_2_out, bit_extender_3_out, bit_extender_4_out, bit_extender_5_out,
       bitfinder_1_index, bitfinder_2_index, bitfinder_3_index, bitfinder_4_index, comparator_1_gt;
  wire [31:0] adder_1_out, adder_2_out, adder_3_out, adder_4_out, adder_5_out, and_1_out, bit_extender_6_out,
       bit_extender_7_out, bit_extender_8_out, bit_extender_9_out, demultiplexer_1_out1,
       demultiplexer_1_out2, demultiplexer_1_out3, demultiplexer_1_out4, demultiplexer_1_out5,
       demultiplexer_1_out6, demultiplexer_1_out7, demultiplexer_1_out8, demultiplexer_1_out9,
       demultiplexer_1_out10, demultiplexer_1_out11, demultiplexer_1_out12, demultiplexer_1_out13,
       demultiplexer_1_out14, demultiplexer_1_out15, demultiplexer_1_out16, demultiplexer_1_out26,
       demultiplexer_1_out27, demultiplexer_1_out28, demultiplexer_1_out29, demultiplexer_1_out30,
       demultiplexer_1_out31, demultiplexer_2_out1, demultiplexer_2_out2, demultiplexer_2_out3,
       demultiplexer_2_out4, demultiplexer_2_out5, demultiplexer_2_out6, demultiplexer_2_out7,
       demultiplexer_2_out8, demultiplexer_2_out9, demultiplexer_2_out10, demultiplexer_2_out11,
       demultiplexer_2_out12, demultiplexer_2_out13, demultiplexer_2_out14, demultiplexer_2_out15,
       demultiplexer_2_out16, divider_1_out, multiplier_1_cout, multiplier_1_out, nand_1_out, negator_1_out,
       nor_1_out, not_1_out, or_5_out, pull_resistor_2_node, pull_resistor_3_node, pull_resistor_4_node,
       pull_resistor_5_node, pull_resistor_6_node, pull_resistor_7_node, pull_resistor_8_node, register_1_q,
       shifter_1_out, shifter_2_out, shifter_3_out, subtractor_1_out, xnor_1_out, xor_1_out;

  Demultiplexer #(.select(5), .width(32), .disabled(0), .enable("false")) demultiplexer_1 (
    .out1(demultiplexer_1_out1), .out2(demultiplexer_1_out2), .out3(demultiplexer_1_out3),
    .out4(demultiplexer_1_out4), .out5(demultiplexer_1_out5), .out6(demultiplexer_1_out6),
    .out7(demultiplexer_1_out7), .out8(demultiplexer_1_out8), .out9(demultiplexer_1_out9),
    .out10(demultiplexer_1_out10), .out11(demultiplexer_1_out11), .out12(demultiplexer_1_out12),
    .out13(demultiplexer_1_out13), .out14(demultiplexer_1_out14), .out15(demultiplexer_1_out15),
    .out16(demultiplexer_1_out16), .out26(demultiplexer_1_out26), .out27(demultiplexer_1_out27),
    .out28(demultiplexer_1_out28), .out29(demultiplexer_1_out29), .out30(demultiplexer_1_out30),
    .out31(demultiplexer_1_out31), .in(A), .sel(Selector));  // open: out0, out17, out18, out19, out20, out21, out22, out23, out24, out25
  Bit_Extender #(.in_width(5), .out_width(3)) bit_extender_1 (.in(Selector), .out(bit_extender_1_out));
  Decoder #(.select(3), .disabled(0), .enable("false")) decoder_1 (
    .out1(decoder_1_out1), .out2(decoder_1_out2), .out3(decoder_1_out3), .out4(decoder_1_out4),
    .out5(decoder_1_out5), .out6(decoder_1_out6), .sel(bit_extender_1_out));  // open: out0, out7
  or or_1 (or_1_out, decoder_1_out3, decoder_1_out4);
  or or_2 (or_2_out, decoder_1_out5, decoder_1_out6);
  or or_3 (or_3_out, decoder_1_out1, decoder_1_out2, or_1_out);
  Demultiplexer #(.select(5), .width(32), .disabled(0), .enable("false")) demultiplexer_2 (
    .out1(demultiplexer_2_out1), .out2(demultiplexer_2_out2), .out3(demultiplexer_2_out3),
    .out4(demultiplexer_2_out4), .out5(demultiplexer_2_out5), .out6(demultiplexer_2_out6),
    .out7(demultiplexer_2_out7), .out8(demultiplexer_2_out8), .out9(demultiplexer_2_out9),
    .out10(demultiplexer_2_out10), .out11(demultiplexer_2_out11), .out12(demultiplexer_2_out12),
    .out13(demultiplexer_2_out13), .out14(demultiplexer_2_out14), .out15(demultiplexer_2_out15),
    .out16(demultiplexer_2_out16), .in(B), .sel(Selector));  // open: out0, out17, out18, out19, out20, out21, out22, out23, out24, out25, out26, out27, out28, out29, out30, out31
  or or_4 (or_4_out, subtractor_1_bout, adder_1_cout, bitfinder_5_found);
  Bit_Extender #(.in_width(32), .out_width(5)) bit_extender_2 (.in(demultiplexer_2_out13), .out(bit_extender_2_out));
  Bit_Extender #(.in_width(32), .out_width(5)) bit_extender_3 (.in(demultiplexer_2_out14), .out(bit_extender_3_out));
  Bit_Extender #(.in_width(32), .out_width(5)) bit_extender_4 (.in(demultiplexer_2_out15), .out(bit_extender_4_out));
  Bit_Extender #(.in_width(32), .out_width(5)) bit_extender_5 (.in(demultiplexer_2_out16), .out(bit_extender_5_out));
  BitFinder #(.width(32), .\type ("low0")) bitfinder_1 (
    .in(demultiplexer_1_out26), .index(bitfinder_1_index), .found(bitfinder_1_found));
  BitFinder #(.width(32), .\type ("high0")) bitfinder_2 (
    .in(demultiplexer_1_out27), .index(bitfinder_2_index), .found(bitfinder_2_found));
  BitFinder #(.width(32)) bitfinder_3 (
    .in(demultiplexer_1_out28), .index(bitfinder_3_index), .found(bitfinder_3_found));
  BitFinder #(.width(32), .\type ("high1")) bitfinder_4 (
    .in(demultiplexer_1_out29), .index(bitfinder_4_index), .found(bitfinder_4_found));
  Register #(.width(1), .trigger("high")) Carry_Flag (.D(or_4_out), .Q(ALU_Flag[5]), .clk(or_3_out));  // open: en, clr
  Register #(.width(32)) register_1 (.D(multiplier_1_cout), .Q(register_1_q), .clk(or_1_out));  // open: en, clr
  BitFinder #(.width(32)) bitfinder_5 (.in(multiplier_1_cout), .found(bitfinder_5_found));  // open: index
  Adder #(.width(32)) adder_1 (
    .a(demultiplexer_1_out1), .b(demultiplexer_2_out1), .out(adder_1_out), .cout(adder_1_cout));  // open: cin
  Subtractor #(.width(32)) subtractor_1 (
    .a(demultiplexer_1_out2), .b(demultiplexer_2_out2), .out(subtractor_1_out), .bout(subtractor_1_bout));  // open: bin
  Multiplier #(.width(32)) multiplier_1 (
    .a(demultiplexer_1_out3), .b(demultiplexer_2_out3), .out(multiplier_1_out), .cout(multiplier_1_cout));  // open: cin
  Divider #(.width(32)) divider_1 (
    .a(demultiplexer_1_out4), .b(demultiplexer_2_out4), .out(divider_1_out), .rem(multiplier_1_cout));  // open: upper
  Comparator #(.width(32), .mode("unsigned")) comparator_1 (
    .a(demultiplexer_1_out5), .b(demultiplexer_2_out5), .gt(comparator_1_gt[0]), .eq(comparator_1_gt[2]),
    .lt(comparator_1_gt[3]));
  Comparator #(.width(32)) comparator_2 (
    .a(demultiplexer_1_out5), .b(demultiplexer_2_out5), .gt(comparator_1_gt[1]), .eq(comparator_2_eq),
    .lt(comparator_1_gt[4]));
  assign and_1_out = demultiplexer_1_out7 & demultiplexer_2_out7;  // AND_Gate and_1, 32 bits wide
  assign or_5_out = demultiplexer_1_out8 | demultiplexer_2_out8;  // OR_Gate or_5, 32 bits wide
  assign xor_1_out = demultiplexer_1_out9 ^ demultiplexer_2_out9;  // XOR_Gate xor_1, 32 bits wide
  assign nand_1_out = ~(demultiplexer_1_out10 & demultiplexer_2_out10);  // NAND_Gate nand_1, 32 bits wide
  assign nor_1_out = ~(demultiplexer_1_out11 | demultiplexer_2_out11);  // NOR_Gate nor_1, 32 bits wide
  assign xnor_1_out = ~(demultiplexer_1_out12 ^ demultiplexer_2_out12);  // XNOR_Gate xnor_1, 32 bits wide
  Shifter #(.width(32)) shifter_1 (.in(demultiplexer_1_out13), .\dist (bit_extender_2_out), .out(shifter_1_out));
  Shifter #(.width(32), .shift("lr")) shifter_2 (
    .in(demultiplexer_1_out14), .\dist (bit_extender_3_out), .out(shifter_2_out));
  Shifter #(.width(32), .shift("rl")) shifter_3 (
    .in(demultiplexer_1_out15), .\dist (bit_extender_4_out), .out(shifter_3_out));
  Pull_Resistor pull_resistor_1 (.node(shifter_3_out));
  Pull_Resistor pull_resistor_2 (.node(pull_resistor_2_node));
  Shifter #(.width(32), .shift("rr")) shifter_4 (
    .in(demultiplexer_1_out16), .\dist (bit_extender_5_out), .out(pull_resistor_2_node));
  assign bit_extender_6_out = {{27{1'b0}}, bitfinder_1_index};  // Bit_Extender bit_extender_6
  Adder #(.width(32)) adder_2 (
    .a(bit_extender_6_out), .b(pull_resistor_3_node), .out(adder_2_out), .cin(bitfinder_1_found));  // open: cout
  Pull_Resistor pull_resistor_3 (.node(pull_resistor_3_node));
  assign bit_extender_7_out = {{27{1'b0}}, bitfinder_2_index};  // Bit_Extender bit_extender_7
  Adder #(.width(32)) adder_3 (
    .a(bit_extender_7_out), .b(pull_resistor_4_node), .out(adder_3_out), .cin(bitfinder_2_found));  // open: cout
  Pull_Resistor pull_resistor_4 (.node(pull_resistor_4_node));
  assign bit_extender_8_out = {{27{1'b0}}, bitfinder_3_index};  // Bit_Extender bit_extender_8
  Adder #(.width(32)) adder_4 (
    .a(bit_extender_8_out), .b(pull_resistor_5_node), .out(adder_4_out), .cin(bitfinder_3_found));  // open: cout
  Pull_Resistor pull_resistor_5 (.node(pull_resistor_5_node));
  assign bit_extender_9_out = {{27{1'b0}}, bitfinder_4_index};  // Bit_Extender bit_extender_9
  Adder #(.width(32)) adder_5 (
    .a(bit_extender_9_out), .b(pull_resistor_6_node), .out(adder_5_out), .cin(bitfinder_4_found));  // open: cout
  Pull_Resistor pull_resistor_6 (.node(pull_resistor_6_node));
  assign not_1_out = ~demultiplexer_1_out30;  // NOT_Gate not_1, 32 bits wide
  Negator #(.width(32)) negator_1 (.in(demultiplexer_1_out31), .out(negator_1_out));
  Register #(.width(5), .trigger("high")) CMP_Flag (
    .D(comparator_1_gt), .Q(ALU_Flag[4:0]), .clk(or_2_out));  // open: en, clr
  Pull_Resistor pull_resistor_7 (.node(pull_resistor_7_node));
  Pull_Resistor pull_resistor_8 (.node(pull_resistor_8_node));
  Multiplexer #(.select(5), .width(32), .disabled(0), .enable("false")) multiplexer_1 (
    .in0(pull_resistor_7_node), .in1(adder_1_out), .in2(subtractor_1_out), .in3(multiplier_1_out),
    .in4(divider_1_out), .in5(demultiplexer_1_out5), .in6(demultiplexer_1_out6), .in7(and_1_out),
    .in8(or_5_out), .in9(xor_1_out), .in10(nand_1_out), .in11(nor_1_out), .in12(xnor_1_out),
    .in13(shifter_1_out), .in14(shifter_2_out), .in15(shifter_3_out), .in16(pull_resistor_2_node),
    .in17(pull_resistor_8_node), .in18(pull_resistor_8_node), .in19(pull_resistor_8_node),
    .in20(pull_resistor_8_node), .in21(pull_resistor_8_node), .in22(pull_resistor_8_node),
    .in23(pull_resistor_8_node), .in24(pull_resistor_8_node), .in25(register_1_q), .in26(adder_2_out),
    .in27(adder_3_out), .in28(adder_4_out), .in29(adder_5_out), .in30(not_1_out), .in31(negator_1_out),
    .out(Out), .sel(Selector));

  // Other names for the same wires on the sheet: SEL[4:0] = Selector

  // Notes on the sheet:
  //   7 = AND
  //   8 = OR
  //   9 = XOR
  //   10 = NAND
  //   11 = NOR
  //   12 = XNOR
  //   13 = SHL
  //   14 = SHR
  //   15 = ROL
  //   16 = ROR
  //   17 = CMS
  //   18~29 = Unused
  //   30 = NOT
  //   29 = FLH
  //   30 = NOT
  //   31 = NEG
  //   ALU Selector:
  //   0 = Nothing
  //   1 = ADD, Sum
  //   2 = SUB, Substract
  //   3 = MUL, Multiplication
  //   4 = DIV, Divide
  //   5 = CMP, Compare
  //   6 = Unused
  //   NOT
  //   NEG
  //   UNS
  //   SIG
  //   CMP Flag
  //   Bit 0 = Above
  //   Bit 1 = Greater
  //   Bit 2 = Equal
  //   Bit 3 = Below
  //   Bit 4 = Lesser
  //   _________
  //   The Carry Flag can mean:
  //   Carry out from ADD
  //   Burrow out from SUB
  //   There is Carry out from MUL
  //   There is Remain from DIV
  //   _________
endmodule

module Console_Back (
  input  [31:0] Console_Data_Clear,
  input  Power,
  input  Clock_1_1,
  output [6:0] Data,
  output Clear,
  output _4Clock_2On_2Off
);

  wire bitfinder_1_found, bitfinder_2_found, bitfinder_3_found, buffer_1_out, buffer_2_out, buffer_3_out,
       buffer_4_out, buffer_5_out, counter_1_carry, n2signals_turn_off_1_out_2, n2signals_turn_off_2_out_2,
       not_1_out, not_2_out, not_3_out, or_1_out, pull_resistor_4_node, transistor_1_out, transistor_3_out;
  wire [1:0] counter_1_q;
  wire [31:0] register_1_q, register_2_q;

  Transistor #(.\type ("n")) transistor_1 (.in(Clock_1_1), .out(transistor_1_out), .gate(bitfinder_3_found));
  Pull_Resistor pull_resistor_1 (.node(transistor_1_out));
  Register #(.width(32)) register_1 (
    .D(Console_Data_Clear), .en(not_1_out), .Q(register_1_q), .clk(buffer_1_out));  // open: clr
  Register #(.width(32)) register_2 (
    .D(Console_Data_Clear), .Q(register_2_q), .clk(buffer_1_out), .clr(or_1_out));  // open: en
  BitFinder #(.width(32)) bitfinder_1 (.in(Console_Data_Clear), .found(bitfinder_1_found));  // open: index
  buf buffer_1 (buffer_1_out, bitfinder_1_found);
  or or_1 (or_1_out, not_3_out, counter_1_carry);
  buf buffer_2 (buffer_2_out, transistor_1_out);
  BitFinder #(.width(32)) bitfinder_2 (.in(register_1_q), .found(bitfinder_2_found));  // open: index
  not not_1 (not_1_out, bitfinder_2_found);
  BitFinder #(.width(32)) bitfinder_3 (.in(register_2_q), .found(bitfinder_3_found));  // open: index
  Pull_Resistor pull_resistor_2 (.node(Clear));
  Transistor #(.gate("br")) transistor_2 (.in(not_3_out), .out(Clear), .gate(buffer_3_out));
  buf buffer_3 (buffer_3_out, not_3_out);
  buf buffer_4 (buffer_4_out, buffer_5_out);
  buf buffer_5 (buffer_5_out, buffer_2_out);
  Transistor transistor_3 (.in(not_2_out), .out(transistor_3_out), .gate(buffer_4_out));
  not not_2 (not_2_out, buffer_4_out);
  Pull_Resistor pull_resistor_3 (.node(transistor_3_out));
  Counter #(.width(2), .max('h3)) counter_1 (
    .Q(counter_1_q), .carry(counter_1_carry), .clk(_4Clock_2On_2Off), .clr(not_3_out));  // open: load, D, count
  not not_3 (not_3_out, Power);
  Pull_Resistor pull_resistor_4 (.node(pull_resistor_4_node));
  _2Signals_Turn_OFF u_2signals_turn_off_1 (.in_1(pull_resistor_4_node), .out_2(n2signals_turn_off_1_out_2));
  Transistor #(.gate("br")) transistor_4 (.in(buffer_4_out), .out(pull_resistor_4_node), .gate(transistor_3_out));
  or or_2 (_4Clock_2On_2Off, n2signals_turn_off_1_out_2, n2signals_turn_off_2_out_2);
  _2Signals_Turn_OFF u_2signals_turn_off_2 (.in_1(transistor_3_out), .out_2(n2signals_turn_off_2_out_2));
  Multiplexer #(.select(2), .width(7), .disabled(0), .enable("false")) multiplexer_1 (
    .in0(register_2_q[30:24]), .in1(register_2_q[22:16]), .in2(register_2_q[14:8]), .in3(register_2_q[6:0]),
    .out(Data), .sel(counter_1_q));
  Counter #(.width(32), .max('hffffffff)) counter_2 (
    .clk(_4Clock_2On_2Off), .clr(not_3_out));  // open: load, D, count, Q, carry

  // Notes on the sheet:
  //   [1.1.0]Yeah, it made me change the clock system, you can read README for the change explanation.
  //   32th, 24th, 16th, 8th bits aren't used.
  //   But all bits in these intervals (7-bit sized) means a character.
  //   The writing on the console is made from left to right, first the 31~25 bit and so on.
  //   I am a genius.
endmodule

module Keyboard_Back (
  input  There_is_char,
  input  [6:0] Keyboard_Data,
  input  Clock__Feedback,
  output [6:0] out_4,
  output Clock
);

  wire counter_1_q;

  Counter #(.width(1), .max('h1), .ongoal("stay")) counter_1 (
    .count(There_is_char), .Q(counter_1_q), .clk(Clock__Feedback), .clr(Clock));  // open: load, D, carry
  Register #(.width(1), .trigger("falling")) register_1 (
    .D(1'b1), .en(counter_1_q), .Q(Clock), .clk(Clock__Feedback), .clr(Clock));
  Pull_Resistor pull_resistor_1 (.node(out_4));
  Transistor #(.\type ("n"), .width(7)) transistor_1 (.in(Keyboard_Data), .out(out_4), .gate(counter_1_q));

  // Notes on the sheet:
  //   out_4: pull=down
  //   This reg fixes clock ignoring the first character.
  //   A lot time after getting some letters eating bugs, I got this working system. I surely don't know why it works, but it does.
endmodule

module External_Devices_Controler (
  input  [6:0] Input_Device_1,
  input  [31:0] Input_Device_2,
  input  [9:0] Input_Device_3,
  input  [31:0] Input_Device_4,
  input  [31:0] CPU_In_Out,
  input  [7:0] External_Controller_Selector,
  output [31:0] Output_Device_1,
  output [31:0] Output_Device_2,
  output [31:0] Output_Device_3,
  output [31:0] CPU_Out_In,
  output [31:0] Output_Device_4,
  output _1FB,
  output _2FB,
  output _3FB,
  output _4FB,
  output GPU_Additional_bit
);

  wire [31:0] bit_extender_1_out, bit_extender_2_out, pull_resistor_1_node;

  assign bit_extender_1_out = {{25{1'b0}}, Input_Device_1};  // Bit_Extender bit_extender_1
  assign bit_extender_2_out = {{22{1'b0}}, Input_Device_3};  // Bit_Extender bit_extender_2
  Pull_Resistor pull_resistor_1 (.node(pull_resistor_1_node));
  Multiplexer #(.select(4), .width(32), .disabled(0), .enable("false")) multiplexer_1 (
    .in0(pull_resistor_1_node), .in1(bit_extender_1_out), .in2(Input_Device_2), .in4(bit_extender_2_out),
    .in8(Input_Device_4), .out(CPU_Out_In), .sel(External_Controller_Selector[7:4]));  // open: in3, in5, in6, in7, in9, in10, in11, in12, in13, in14, in15
  Decoder #(.select(4), .enable("false")) decoder_1 (
    .out1(_1FB), .out2(_2FB), .out4(_3FB), .out8(_4FB), .sel(External_Controller_Selector[7:4]));  // open: out0, out3, out5, out6, out7, out9, out10, out11, out12, out13, out14, out15
  Demultiplexer #(.select(4), .width(32), .enable("false")) demultiplexer_1 (
    .out1(Output_Device_1), .out2(Output_Device_2), .out4(Output_Device_3), .out8(Output_Device_4),
    .in(CPU_In_Out), .sel(External_Controller_Selector[3:0]));  // open: out0, out3, out5, out6, out7, out9, out10, out11, out12, out13, out14, out15
  Decoder #(.select(4), .enable("false")) decoder_2 (
    .out14(GPU_Additional_bit), .sel(External_Controller_Selector[3:0]));  // open: out0, out1, out2, out3, out4, out5, out6, out7, out8, out9, out10, out11, out12, out13, out15

  // Notes on the sheet:
  //   Input_Device_1: pull=down
  //   By default, Keyboard
  //   Yeah, this subcircuit is ugly.
  //   Joystick
  //   FB = Feedback
  //   The feedback will send the external device a signal when it is acessed.
  //   For now it will use this immediate value to DMX as I think it's faster than putting OR gates on the CPU instruction
  //   to generate the specific DMX selector. But on the future that should change to be possible to hold more devices.
  //   This device connects the CPU to external devices, Inputs or Outputs.
  //   Prob will be sound.
  //   But is functional!
  //   Will probably be the GPU.
  //   (or should I treat it as an Address?)
  //   By default, Console
endmodule

module _2Signals_Turn_OFF (
  input  in_1,
  output out_2
);

  wire buffer_1_out, counter_1_q, or_1_out, transistor_2_out;

  Transistor #(.gate("br")) transistor_1 (.in(or_1_out), .out(out_2), .gate(buffer_1_out));
  Pull_Resistor pull_resistor_1 (.node(out_2));
  buf buffer_1 (buffer_1_out, or_1_out);
  or or_1 (or_1_out, transistor_2_out, counter_1_q);
  Transistor #(.gate("br")) transistor_2 (.in(in_1), .out(transistor_2_out), .gate(counter_1_q));
  Pull_Resistor pull_resistor_2 (.node(transistor_2_out));
  Counter #(.width(1), .max('h1), .ongoal("stay")) counter_1 (
    .Q(counter_1_q), .clk(in_1), .clr(buffer_1_out));  // open: load, D, count, carry
endmodule

module Joystick_Back (
  input  [4:0] X,
  input  [4:0] Y,
  output [9:0] Output
);


  assign Output = {Y, X};
endmodule

module GPU_____External_Connections (
  input  [7:0] in_1,
  input  Clock,
  input  [31:0] Data_Out_In,
  input  Power,
  output [7:0] Row_Selector,
  output Update_Screen,
  output [7:0] out_7,
  output [7:0] out_8,
  output [7:0] out_9,
  output [7:0] out_10,
  output [7:0] out_11,
  output [7:0] out_12,
  output [7:0] out_13,
  output [7:0] out_14,
  output [7:0] out_15,
  output [7:0] out_16,
  output [7:0] out_17,
  output [7:0] out_18,
  output [7:0] out_19,
  output [7:0] out_20,
  output [7:0] out_21,
  output [7:0] out_22,
  output [7:0] out_23,
  output [7:0] out_24,
  output [7:0] out_25,
  output [7:0] out_26,
  output [7:0] out_27,
  output [7:0] out_28,
  output [7:0] out_29,
  output [7:0] out_30,
  output [7:0] out_31,
  output [7:0] out_32,
  output [7:0] out_33,
  output [7:0] out_34,
  output [7:0] out_35,
  output [7:0] out_36,
  output [7:0] out_37,
  output [7:0] out_38,
  output [7:0] out_39,
  output [7:0] out_40,
  output [7:0] out_41,
  output [7:0] out_42
);

  wire button_1_out, button_2_out, button_3_out, comparator_1_gt, comparator_2_gt, comparator_3_lt,
       comparator_4_lt, comparator_5_lt, decoder_1_out1, decoder_1_out2, decoder_1_out3, decoder_1_out4,
       decoder_1_out6, decoder_2_out4, decoder_2_out5, decoder_2_out6, decoder_2_out7, decoder_2_out8,
       decoder_2_out9, decoder_2_out10, decoder_2_out11, decoder_2_out12, decoder_2_out13, decoder_2_out14,
       decoder_2_out15, FUPS, Load_next_Object, not_1_out, not_2_out, or_1_out, or_2_out, or_3_out, or_4_out,
       or_5_out, or_6_out, or_7_out, ram_1_p2, ram_1_p5, ram_2_p1, ram_3_p2, ram_4_p1, ram_4_p3,
       Ready_to_receive_instruction_q, RST, UPS;
  wire [3:0] controlled_buffer_1_out, counter_6_q;
  wire [6:0] undriven;
  wire [7:0] _X_Pos, _Y_Pos, A, A3, A4, adder_1_out, counter_1_q, H__Y, Height, negator_1_out,
       transistor_1_out, Widht;
  wire [11:0] pull_resistor_3_node;
  wire [15:0] A2, adder_3_out, bit_extender_1_out, bit_extender_2_out, counter_2_q;
  wire [31:0] demultiplexer_1_out0, demultiplexer_2_out0, demultiplexer_2_out1, demultiplexer_2_out2,
       demultiplexer_2_out3, demultiplexer_2_out4, demultiplexer_2_out5, demultiplexer_2_out6,
       demultiplexer_2_out7, demultiplexer_2_out8, demultiplexer_2_out9, demultiplexer_2_out10,
       demultiplexer_2_out11, demultiplexer_2_out12, gpu_color_replacer_2_1_out_52,
       gpu_color_replacer_2_1_out_53, gpu_color_replacer_2_1_out_54, gpu_color_replacer_2_1_out_55,
       gpu_color_replacer_2_1_out_56, gpu_color_replacer_2_1_out_57, gpu_color_replacer_2_1_out_58,
       gpu_color_replacer_2_1_out_59, gpu_color_replacer_2_1_out_60, ram_5_p1, ram_7_data, ram_10_data,
       ram_12_data, ram_15_data, ram_18_data, ram_20_data, ram_21_data, ram_22_data, ram_23_data,
       ram_24_data, ram_25_data, ram_26_data;

  Counter #(.ongoal("stay")) counter_1 (.Q(counter_1_q), .clk(Load_next_Object));  // open: load, D, count, carry, clr
  Pull_Resistor pull_resistor_1 ();  // open: node
  Decoder #(.select(3), .enable("false")) decoder_1 (
    .out1(decoder_1_out1), .out2(decoder_1_out2), .out3(decoder_1_out3), .out4(decoder_1_out4),
    .out6(decoder_1_out6), .out7(RST), .sel(demultiplexer_1_out0[31:29]));  // open: out0, out5
  Demultiplexer #(.width(32), .enable("false")) demultiplexer_1 (
    .out0(demultiplexer_1_out0), .in(Data_Out_In), .sel(Ready_to_receive_instruction_q));  // open: out1
  D_Flip_Flop Ready_to_receive_instruction (
    .Q(Ready_to_receive_instruction_q), .preset(or_4_out), .reset(or_1_out));  // open: clk, D, Qn, en
  buf or_1 (or_1_out, FUPS);  // OR_Gate
  Adder adder_1 (.a(Widht), .b(_X_Pos), .out(adder_1_out));  // open: cin, cout
  Comparator comparator_1 (.a(_X_Pos), .b(8'h23), .gt(comparator_1_gt));  // open: eq, lt
  Adder adder_2 (.a(Height), .b(_Y_Pos), .out(H__Y));  // open: cin, cout
  Comparator comparator_2 (.a(_Y_Pos), .b(8'h17), .gt(comparator_2_gt));  // open: eq, lt
  // Probe on nothing
  // RAM ram_1: pin names not known; wires that end beside it: counter_1_q, ram_1_p2, A4, A4, ram_1_p5
  Register Address_for_saving_Infos (.Q(A3), .clr(ram_1_p2));  // open: D, en, clk
  Comparator comparator_3 (.a(adder_1_out), .b(8'h1), .lt(comparator_3_lt));  // open: gt, eq
  Comparator comparator_4 (.a(H__Y), .b(8'h1), .lt(comparator_4_lt));  // open: gt, eq
  D_Flip_Flop d_ff_1 (.Q(UPS), .preset(decoder_1_out6), .reset(or_2_out));  // open: clk, D, Qn, en
  or or_2 (or_2_out, FUPS, ram_1_p2);
  or or_3 (or_3_out, comparator_3_lt, comparator_1_gt, comparator_4_lt, comparator_2_gt);
  // RAM ram_2: pin names not known; wires that end beside it: ram_2_p1, ram_1_p2, A4, A3
  assign controlled_buffer_1_out = decoder_1_out1 ? 4'b0001 : 4'bz;  // Controlled_Buffer controlled_buffer_1
  assign controlled_buffer_1_out = decoder_1_out2 ? 4'b0010 : 4'bz;  // Controlled_Buffer controlled_buffer_2
  or or_4 (or_4_out, decoder_1_out1, decoder_1_out2, decoder_1_out3, decoder_1_out4);
  assign controlled_buffer_1_out = decoder_1_out3 ? 4'b0011 : 4'bz;  // Controlled_Buffer controlled_buffer_3
  Transistor #(.gate("br"), .width(8)) transistor_1 (.in(_Y_Pos), .out(transistor_1_out), .gate(comparator_5_lt));
  // Probe on in_1
  // Probe on in_1
  // RAM ram_3: pin names not known; wires that end beside it: or_3_out, ram_3_p2, ram_1_p2, A4, A3, ram_1_p5
  Comparator comparator_5 (.a({8{1'b0}}), .b(_Y_Pos), .lt(comparator_5_lt));  // open: gt, eq
  Negator negator_1 (.in(transistor_1_out), .out(negator_1_out));
  assign bit_extender_1_out = {{8{1'b0}}, negator_1_out};  // Bit_Extender bit_extender_1
  assign bit_extender_2_out = {{8{1'b0}}, A4};  // Bit_Extender bit_extender_2
  Multiplier #(.width(16)) multiplier_1 (.a(bit_extender_2_out), .b(16'h18), .out(A2));  // open: cin, cout
  or or_5 (or_5_out, button_1_out, button_2_out);
  Adder #(.width(16)) adder_3 (.a(bit_extender_1_out), .b(A2), .out(adder_3_out));  // open: cin, cout
  Button button_1 (.out(button_1_out));
  or or_6 (or_6_out, button_1_out, button_2_out);
  or or_7 (or_7_out, button_2_out, button_1_out);
  Button button_2 (.out(button_2_out));
  Counter #(.width(16), .max('hffff), .ongoal("stay")) counter_2 (
    .load(button_1_out), .D(adder_3_out), .count(button_2_out), .Q(counter_2_q), .clk(or_5_out),
    .clr(button_3_out));  // open: carry
  Counter #(.ongoal("stay")) counter_3 (
    .load(or_6_out), .D(H__Y), .count(button_2_out), .carry(Load_next_Object), .clk(or_7_out),
    .clr(button_3_out));  // open: Q
  or or_8 (ram_1_p2, RST, not_1_out);
  not not_1 (not_1_out, Power);
  // RAM ram_4: pin names not known; wires that end beside it: ram_4_p1, ram_1_p2, ram_4_p3, Update_Screen
  Counter #(.ongoal("stay")) counter_4 ();  // open: load, D, count, Q, carry, clk, clr
  Button button_3 (.out(button_3_out));
  // RAM ram_5: pin names not known; wires that end beside it: ram_5_p1, _X_Pos, ram_4_p3
  // Probe on counter_2_q
  Counter #(.max('h17)) counter_5 (
    .count(UPS), .Q(Row_Selector), .carry(FUPS), .clk(Clock), .clr(ram_1_p2));  // open: load, D
  Pull_Resistor pull_resistor_2 ();  // open: node
  not not_2 (not_2_out, Clock);
  // Probe on undriven[1:0]
  Counter #(.width(4), .max('hf), .ongoal("stay")) counter_6 (
    .D(controlled_buffer_1_out), .Q(counter_6_q), .clk(or_4_out), .clr(ram_1_p2));  // open: load, count, carry
  Decoder #(.select(4), .disabled(0), .enable("false")) decoder_2 (
    .out1(ram_2_p1), .out2(ram_3_p2), .out3(ram_4_p1), .out4(decoder_2_out4), .out5(decoder_2_out5),
    .out6(decoder_2_out6), .out7(decoder_2_out7), .out8(decoder_2_out8), .out9(decoder_2_out9),
    .out10(decoder_2_out10), .out11(decoder_2_out11), .out12(decoder_2_out12), .out13(decoder_2_out13),
    .out14(decoder_2_out14), .out15(decoder_2_out15), .sel(counter_6_q));  // open: out0
  RAM #(.dataWidth(32), .bus("separate")) ram_6 (
    .addr(A), .din(gpu_color_replacer_2_1_out_60), .data({out_7, out_8, out_9, out_10}), .clk(not_2_out),
    .clr(ram_1_p2));  // open: str, sel, ld
  GPU_____Color_replacer_2 gpu_color_replacer_2_1 (
    .in_10(demultiplexer_2_out11), .in_5(demultiplexer_2_out10), .in_2(demultiplexer_2_out9),
    .in_11(demultiplexer_2_out8), .in_6(demultiplexer_2_out7), .in_3(demultiplexer_2_out6),
    .in_12(demultiplexer_2_out5), .in_4(demultiplexer_2_out3), .in_13(demultiplexer_2_out2),
    ._1(demultiplexer_2_out0), .Amount(undriven[1:0]), .in_7(demultiplexer_2_out4), .in_16(out_42),
    .in_17(out_41), .in_18(out_40), .in_19(out_39), .in_20(out_38), .in_21(out_37), .in_22(out_36),
    .in_23(out_35), .in_24(out_34), .in_25(out_33), .in_26(out_32), .in_27(out_31), .in_28(out_30),
    .in_29(out_29), .in_30(out_28), .in_31(out_27), .in_32(out_26), .in_33(out_25), .in_34(out_24),
    .in_35(out_23), .in_36(out_22), .in_37(out_21), .in_38(out_20), .in_39(out_19), .in_40(out_18),
    .in_41(out_17), .in_42(out_16), .in_43(out_15), .in_44(out_14), .in_45(out_13), .in_46(out_12),
    .in_47(out_11), .in_48(out_10), .in_49(out_9), .in_50(out_8), .in_51(out_7),
    .out_60(gpu_color_replacer_2_1_out_60), .out_59(gpu_color_replacer_2_1_out_59),
    .out_57(gpu_color_replacer_2_1_out_57), .out_58(gpu_color_replacer_2_1_out_58),
    .out_54(gpu_color_replacer_2_1_out_54), .out_55(gpu_color_replacer_2_1_out_55),
    .out_56(gpu_color_replacer_2_1_out_56), .out_52(gpu_color_replacer_2_1_out_52),
    .out_53(gpu_color_replacer_2_1_out_53), .Push(Clock), .in_14(demultiplexer_2_out1),
    ._13(demultiplexer_2_out12));
  Demultiplexer #(.select(5), .width(32), .tristate("true"), .disabled(0), .enable("false")) demultiplexer_2 (
    .out0(demultiplexer_2_out0), .out1(demultiplexer_2_out1), .out2(demultiplexer_2_out2),
    .out3(demultiplexer_2_out3), .out4(demultiplexer_2_out4), .out5(demultiplexer_2_out5),
    .out6(demultiplexer_2_out6), .out7(demultiplexer_2_out7), .out8(demultiplexer_2_out8),
    .out9(demultiplexer_2_out9), .out10(demultiplexer_2_out10), .out11(demultiplexer_2_out11),
    .out12(demultiplexer_2_out12), .in(ram_7_data), .sel(undriven[6:2]));  // open: out13, out14, out15, out16, out17, out18, out19, out20, out21, out22, out23, out24, out25, out26, out27, out28, out29, out30, out31
  RAM #(.addrWidth(16), .dataWidth(32), .bus("separate")) ram_7 (
    .addr(A2), .din(ram_5_p1), .data(ram_7_data), .sel(pull_resistor_3_node[11]), .clk(decoder_2_out4),
    .clr(ram_1_p2));  // open: str, ld
  RAM #(.dataWidth(32), .bus("separate")) ram_8 (
    .addr(A), .din(gpu_color_replacer_2_1_out_59), .data({out_11, out_12, out_13, out_14}), .clk(not_2_out),
    .clr(ram_1_p2));  // open: str, sel, ld
  RAM #(.dataWidth(32), .bus("separate")) ram_9 (
    .addr(A), .din(gpu_color_replacer_2_1_out_58), .data({out_15, out_16, out_17, out_18}), .clk(not_2_out),
    .clr(ram_1_p2));  // open: str, sel, ld
  Demultiplexer #(.select(5), .width(32), .tristate("true"), .disabled(0), .enable("false")) demultiplexer_3 (
    .out0(demultiplexer_2_out1), .out1(demultiplexer_2_out2), .out2(demultiplexer_2_out3),
    .out3(demultiplexer_2_out4), .out4(demultiplexer_2_out5), .out5(demultiplexer_2_out6),
    .out6(demultiplexer_2_out7), .out7(demultiplexer_2_out8), .out8(demultiplexer_2_out9),
    .out9(demultiplexer_2_out10), .out10(demultiplexer_2_out11), .out11(demultiplexer_2_out12),
    .out31(demultiplexer_2_out0), .in(ram_10_data), .sel(undriven[6:2]));  // open: out12, out13, out14, out15, out16, out17, out18, out19, out20, out21, out22, out23, out24, out25, out26, out27, out28, out29, out30
  RAM #(.addrWidth(16), .dataWidth(32), .bus("separate")) ram_10 (
    .addr(A2), .din(ram_5_p1), .data(ram_10_data), .sel(pull_resistor_3_node[10]), .clk(decoder_2_out5),
    .clr(ram_1_p2));  // open: str, ld
  Pull_Resistor pull_resistor_3 (.node(pull_resistor_3_node));
  Shifter #(.width(12), .shift("ar")) shifter_1 ();  // open: in, dist, out
  RAM #(.dataWidth(32), .bus("separate")) ram_11 (
    .addr(A), .din(gpu_color_replacer_2_1_out_57), .data({out_19, out_20, out_21, out_22}), .clk(not_2_out),
    .clr(ram_1_p2));  // open: str, sel, ld
  Demultiplexer #(.select(5), .width(32), .tristate("true"), .disabled(0), .enable("false")) demultiplexer_4 (
    .out0(demultiplexer_2_out2), .out1(demultiplexer_2_out3), .out2(demultiplexer_2_out4),
    .out3(demultiplexer_2_out5), .out4(demultiplexer_2_out6), .out5(demultiplexer_2_out7),
    .out6(demultiplexer_2_out8), .out7(demultiplexer_2_out9), .out8(demultiplexer_2_out10),
    .out9(demultiplexer_2_out11), .out30(demultiplexer_2_out0), .out31(demultiplexer_2_out1),
    .in(ram_12_data), .sel(undriven[6:2]));  // open: out10, out11, out12, out13, out14, out15, out16, out17, out18, out19, out20, out21, out22, out23, out24, out25, out26, out27, out28, out29
  RAM #(.addrWidth(16), .dataWidth(32), .bus("separate")) ram_12 (
    .addr(A2), .din(ram_5_p1), .data(ram_12_data), .sel(pull_resistor_3_node[9]), .clk(decoder_2_out6),
    .clr(ram_1_p2));  // open: str, ld
  RAM #(.dataWidth(32), .bus("separate")) ram_13 (
    .addr(A), .din(gpu_color_replacer_2_1_out_56), .data({out_23, out_24, out_25, out_26}), .clk(not_2_out),
    .clr(ram_1_p2));  // open: str, sel, ld
  RAM #(.dataWidth(32), .bus("separate")) ram_14 (
    .addr(A), .din(gpu_color_replacer_2_1_out_55), .data({out_27, out_28, out_29, out_30}), .clk(not_2_out),
    .clr(ram_1_p2));  // open: str, sel, ld
  Demultiplexer #(.select(5), .width(32), .tristate("true"), .disabled(0), .enable("false")) demultiplexer_5 (
    .out0(demultiplexer_2_out3), .out1(demultiplexer_2_out4), .out2(demultiplexer_2_out5),
    .out3(demultiplexer_2_out6), .out4(demultiplexer_2_out7), .out5(demultiplexer_2_out8),
    .out6(demultiplexer_2_out9), .out7(demultiplexer_2_out10), .out8(demultiplexer_2_out11),
    .out29(demultiplexer_2_out0), .out30(demultiplexer_2_out1), .out31(demultiplexer_2_out2),
    .in(ram_15_data), .sel(undriven[6:2]));  // open: out9, out10, out11, out12, out13, out14, out15, out16, out17, out18, out19, out20, out21, out22, out23, out24, out25, out26, out27, out28
  RAM #(.addrWidth(16), .dataWidth(32), .bus("separate")) ram_15 (
    .addr(A2), .din(ram_5_p1), .data(ram_15_data), .sel(pull_resistor_3_node[8]), .clk(decoder_2_out7),
    .clr(ram_1_p2));  // open: str, ld
  RAM #(.dataWidth(32), .bus("separate")) ram_16 (
    .addr(A), .din(gpu_color_replacer_2_1_out_54), .data({out_31, out_32, out_33, out_34}), .clk(not_2_out),
    .clr(ram_1_p2));  // open: str, sel, ld
  RAM #(.dataWidth(32), .bus("separate")) ram_17 (
    .addr(A), .din(gpu_color_replacer_2_1_out_53), .data({out_35, out_36, out_37, out_38}), .clk(not_2_out),
    .clr(ram_1_p2));  // open: str, sel, ld
  Demultiplexer #(.select(5), .width(32), .tristate("true"), .disabled(0), .enable("false")) demultiplexer_6 (
    .out0(demultiplexer_2_out4), .out1(demultiplexer_2_out5), .out2(demultiplexer_2_out6),
    .out3(demultiplexer_2_out7), .out4(demultiplexer_2_out8), .out5(demultiplexer_2_out9),
    .out6(demultiplexer_2_out10), .out7(demultiplexer_2_out11), .out28(demultiplexer_2_out0),
    .out29(demultiplexer_2_out1), .out30(demultiplexer_2_out2), .out31(demultiplexer_2_out3),
    .in(ram_18_data), .sel(undriven[6:2]));  // open: out8, out9, out10, out11, out12, out13, out14, out15, out16, out17, out18, out19, out20, out21, out22, out23, out24, out25, out26, out27
  RAM #(.addrWidth(16), .dataWidth(32), .bus("separate")) ram_18 (
    .addr(A2), .din(ram_5_p1), .data(ram_18_data), .sel(pull_resistor_3_node[7]), .clk(decoder_2_out8),
    .clr(ram_1_p2));  // open: str, ld
  RAM #(.dataWidth(32), .bus("separate")) ram_19 (
    .addr(A), .din(gpu_color_replacer_2_1_out_52), .data({out_39, out_40, out_41, out_42}), .clk(not_2_out),
    .clr(ram_1_p2));  // open: str, sel, ld
  Demultiplexer #(.select(5), .width(32), .tristate("true"), .disabled(0), .enable("false")) demultiplexer_7 (
    .out0(demultiplexer_2_out5), .out1(demultiplexer_2_out6), .out2(demultiplexer_2_out7),
    .out3(demultiplexer_2_out8), .out4(demultiplexer_2_out9), .out5(demultiplexer_2_out10),
    .out6(demultiplexer_2_out11), .out27(demultiplexer_2_out0), .out28(demultiplexer_2_out1),
    .out29(demultiplexer_2_out2), .out30(demultiplexer_2_out3), .out31(demultiplexer_2_out4),
    .in(ram_20_data), .sel(undriven[6:2]));  // open: out7, out8, out9, out10, out11, out12, out13, out14, out15, out16, out17, out18, out19, out20, out21, out22, out23, out24, out25, out26
  RAM #(.addrWidth(16), .dataWidth(32), .bus("separate")) ram_20 (
    .addr(A2), .din(ram_5_p1), .data(ram_20_data), .sel(pull_resistor_3_node[6]), .clk(decoder_2_out9),
    .clr(ram_1_p2));  // open: str, ld
  Demultiplexer #(.select(5), .width(32), .tristate("true"), .disabled(0), .enable("false")) demultiplexer_8 (
    .out0(demultiplexer_2_out6), .out1(demultiplexer_2_out7), .out2(demultiplexer_2_out8),
    .out3(demultiplexer_2_out9), .out4(demultiplexer_2_out10), .out5(demultiplexer_2_out11),
    .out26(demultiplexer_2_out0), .out27(demultiplexer_2_out1), .out28(demultiplexer_2_out2),
    .out29(demultiplexer_2_out3), .out30(demultiplexer_2_out4), .out31(demultiplexer_2_out5),
    .in(ram_21_data), .sel(undriven[6:2]));  // open: out6, out7, out8, out9, out10, out11, out12, out13, out14, out15, out16, out17, out18, out19, out20, out21, out22, out23, out24, out25
  RAM #(.addrWidth(16), .dataWidth(32), .bus("separate")) ram_21 (
    .addr(A2), .din(ram_5_p1), .data(ram_21_data), .sel(pull_resistor_3_node[5]), .clk(decoder_2_out10),
    .clr(ram_1_p2));  // open: str, ld
  Demultiplexer #(.select(5), .width(32), .tristate("true"), .disabled(0), .enable("false")) demultiplexer_9 (
    .out0(demultiplexer_2_out7), .out1(demultiplexer_2_out8), .out2(demultiplexer_2_out9),
    .out3(demultiplexer_2_out10), .out4(demultiplexer_2_out11), .out25(demultiplexer_2_out0),
    .out26(demultiplexer_2_out1), .out27(demultiplexer_2_out2), .out28(demultiplexer_2_out3),
    .out29(demultiplexer_2_out4), .out30(demultiplexer_2_out5), .out31(demultiplexer_2_out6),
    .in(ram_22_data), .sel(undriven[6:2]));  // open: out5, out6, out7, out8, out9, out10, out11, out12, out13, out14, out15, out16, out17, out18, out19, out20, out21, out22, out23, out24
  RAM #(.addrWidth(16), .dataWidth(32), .bus("separate")) ram_22 (
    .addr(A2), .din(ram_5_p1), .data(ram_22_data), .sel(pull_resistor_3_node[4]), .clk(decoder_2_out11),
    .clr(ram_1_p2));  // open: str, ld
  Demultiplexer #(.select(5), .width(32), .tristate("true"), .disabled(0), .enable("false")) demultiplexer_10 (
    .out0(demultiplexer_2_out8), .out1(demultiplexer_2_out9), .out2(demultiplexer_2_out10),
    .out3(demultiplexer_2_out11), .out24(demultiplexer_2_out0), .out25(demultiplexer_2_out1),
    .out26(demultiplexer_2_out2), .out27(demultiplexer_2_out3), .out28(demultiplexer_2_out4),
    .out29(demultiplexer_2_out5), .out30(demultiplexer_2_out6), .out31(demultiplexer_2_out7),
    .in(ram_23_data), .sel(undriven[6:2]));  // open: out4, out5, out6, out7, out8, out9, out10, out11, out12, out13, out14, out15, out16, out17, out18, out19, out20, out21, out22, out23
  RAM #(.addrWidth(16), .dataWidth(32), .bus("separate")) ram_23 (
    .addr(A2), .din(ram_5_p1), .data(ram_23_data), .sel(pull_resistor_3_node[3]), .clk(decoder_2_out12),
    .clr(ram_1_p2));  // open: str, ld
  Demultiplexer #(.select(5), .width(32), .tristate("true"), .disabled(0), .enable("false")) demultiplexer_11 (
    .out0(demultiplexer_2_out9), .out1(demultiplexer_2_out10), .out2(demultiplexer_2_out11),
    .out23(demultiplexer_2_out0), .out24(demultiplexer_2_out1), .out25(demultiplexer_2_out2),
    .out26(demultiplexer_2_out3), .out27(demultiplexer_2_out4), .out28(demultiplexer_2_out5),
    .out29(demultiplexer_2_out6), .out30(demultiplexer_2_out7), .out31(demultiplexer_2_out8),
    .in(ram_24_data), .sel(undriven[6:2]));  // open: out3, out4, out5, out6, out7, out8, out9, out10, out11, out12, out13, out14, out15, out16, out17, out18, out19, out20, out21, out22
  RAM #(.addrWidth(16), .dataWidth(32), .bus("separate")) ram_24 (
    .addr(A2), .din(ram_5_p1), .data(ram_24_data), .sel(pull_resistor_3_node[2]), .clk(decoder_2_out13),
    .clr(ram_1_p2));  // open: str, ld
  Demultiplexer #(.select(5), .width(32), .tristate("true"), .disabled(0), .enable("false")) demultiplexer_12 (
    .out0(demultiplexer_2_out10), .out1(demultiplexer_2_out11), .out22(demultiplexer_2_out0),
    .out23(demultiplexer_2_out1), .out24(demultiplexer_2_out2), .out25(demultiplexer_2_out3),
    .out26(demultiplexer_2_out4), .out27(demultiplexer_2_out5), .out28(demultiplexer_2_out6),
    .out29(demultiplexer_2_out7), .out30(demultiplexer_2_out8), .out31(demultiplexer_2_out9),
    .in(ram_25_data), .sel(undriven[6:2]));  // open: out2, out3, out4, out5, out6, out7, out8, out9, out10, out11, out12, out13, out14, out15, out16, out17, out18, out19, out20, out21
  RAM #(.addrWidth(16), .dataWidth(32), .bus("separate")) ram_25 (
    .addr(A2), .din(ram_5_p1), .data(ram_25_data), .sel(pull_resistor_3_node[1]), .clk(decoder_2_out14),
    .clr(ram_1_p2));  // open: str, ld
  Demultiplexer #(.select(5), .width(32), .tristate("true"), .disabled(0), .enable("false")) demultiplexer_13 (
    .out0(demultiplexer_2_out11), .out1(demultiplexer_2_out12), .out21(demultiplexer_2_out0),
    .out22(demultiplexer_2_out1), .out23(demultiplexer_2_out2), .out24(demultiplexer_2_out3),
    .out25(demultiplexer_2_out4), .out26(demultiplexer_2_out5), .out27(demultiplexer_2_out6),
    .out28(demultiplexer_2_out7), .out29(demultiplexer_2_out8), .out30(demultiplexer_2_out9),
    .out31(demultiplexer_2_out10), .in(ram_26_data), .sel(undriven[6:2]));  // open: out2, out3, out4, out5, out6, out7, out8, out9, out10, out11, out12, out13, out14, out15, out16, out17, out18, out19, out20
  RAM #(.addrWidth(16), .dataWidth(32), .bus("separate")) ram_26 (
    .addr(A2), .din(ram_5_p1), .data(ram_26_data), .sel(pull_resistor_3_node[0]), .clk(decoder_2_out15),
    .clr(ram_1_p2));  // open: str, ld

  // Notes on the sheet:
  //   (screenWidht) -1
  //   (screenHeight) -1
  //   Load order (Layer)
  //   Instruction Dec
  //   IN1
  //   IN2
  //   IN3
  //   NEW
  //   UPL
  //   UPS
  //   RST
  //   This sub-circuit gave me a LOOOOOOT of work.
  //   Looks really simple right now. Indeed, but it was a real mess:
  //   here on Logisim... and on my head :P
  //   Took like 4 months to be done (most was thinking before sleeping :O)
  //   Draw next object
  //   Instructions 1
  //   Widht + _x must be >0
  //   _x must be < 36
  //   8bit _x, 8bit _y
  //   Instructions 2
  //   Height + _y must be >0
  //   _y must be < 24
  //   8bit Widht, 8bit Height
  //   Instructions 3
  //   _X decoder ROM
  //   The screen size is 36x24.
  //   Draw on screen
  //   For now, objects max size is 36x24.
  //   DATA RAM (12)
endmodule

module GPU_____Color_replacer_2 (
  input  [31:0] _13,
  input  [31:0] in_2,
  input  [31:0] in_3,
  input  [31:0] in_4,
  input  [31:0] in_5,
  input  [31:0] in_6,
  input  [31:0] in_7,
  input  [31:0] _1,
  input  Push,
  input  [31:0] in_10,
  input  [31:0] in_11,
  input  [31:0] in_12,
  input  [31:0] in_13,
  input  [31:0] in_14,
  input  [1:0] Amount,
  input  [7:0] in_16,
  input  [7:0] in_17,
  input  [7:0] in_18,
  input  [7:0] in_19,
  input  [7:0] in_20,
  input  [7:0] in_21,
  input  [7:0] in_22,
  input  [7:0] in_23,
  input  [7:0] in_24,
  input  [7:0] in_25,
  input  [7:0] in_26,
  input  [7:0] in_27,
  input  [7:0] in_28,
  input  [7:0] in_29,
  input  [7:0] in_30,
  input  [7:0] in_31,
  input  [7:0] in_32,
  input  [7:0] in_33,
  input  [7:0] in_34,
  input  [7:0] in_35,
  input  [7:0] in_36,
  input  [7:0] in_37,
  input  [7:0] in_38,
  input  [7:0] in_39,
  input  [7:0] in_40,
  input  [7:0] in_41,
  input  [7:0] in_42,
  input  [7:0] in_43,
  input  [7:0] in_44,
  input  [7:0] in_45,
  input  [7:0] in_46,
  input  [7:0] in_47,
  input  [7:0] in_48,
  input  [7:0] in_49,
  input  [7:0] in_50,
  input  [7:0] in_51,
  output [31:0] out_52,
  output [31:0] out_53,
  output [31:0] out_54,
  output [31:0] out_55,
  output [31:0] out_56,
  output [31:0] out_57,
  output [31:0] out_58,
  output [31:0] out_59,
  output [31:0] out_60
);

  wire buffer_1_out, buffer_2_out, buffer_3_out, buffer_4_out, n2signals_turn_off_1_out_2, or_1_out,
       pull_resistor_2_node, transistor_3_out;
  wire [1:0] transistor_1_out;
  wire [7:0] shift_register_1_q3, shift_register_1_q4, shift_register_1_q5, shift_register_1_q6,
       shift_register_1_q7, shift_register_1_q8, shift_register_1_q9, shift_register_1_q10,
       shift_register_1_q11, shift_register_1_q12, shift_register_1_q13, shift_register_1_q14,
       shift_register_1_q15, shift_register_1_q16, shift_register_1_q17, shift_register_1_q18,
       shift_register_1_q19, shift_register_1_q20, shift_register_1_q21, shift_register_1_q22,
       shift_register_1_q23, shift_register_1_q24, shift_register_1_q25, shift_register_1_q26,
       shift_register_1_q27, shift_register_1_q28, shift_register_1_q29, shift_register_1_q30,
       shift_register_2_q0, shift_register_2_q3, shift_register_2_q4, shift_register_2_q5,
       shift_register_2_q6;
  wire [9:0] pull_resistor_4_node, shift_register_1_out, shift_register_1_q31, shift_register_2_q1,
       shift_register_2_q2;
  wire [9:8] shift_register_1_q3_2, shift_register_1_q4_2, shift_register_1_q5_2, shift_register_1_q6_2,
       shift_register_1_q7_2, shift_register_1_q8_2, shift_register_1_q9_2, shift_register_1_q10_2,
       shift_register_1_q11_2, shift_register_1_q12_2, shift_register_1_q13_2, shift_register_1_q14_2,
       shift_register_1_q15_2, shift_register_1_q16_2, shift_register_1_q17_2, shift_register_1_q18_2,
       shift_register_1_q19_2, shift_register_1_q20_2, shift_register_1_q21_2, shift_register_1_q22_2,
       shift_register_1_q23_2, shift_register_1_q24_2, shift_register_1_q25_2, shift_register_1_q26_2,
       shift_register_1_q27_2, shift_register_1_q28_2, shift_register_1_q29_2, shift_register_1_q30_2,
       shift_register_2_q0_2, shift_register_2_q3_2, shift_register_2_q4_2, shift_register_2_q5_2,
       shift_register_2_q6_2;

  buf buffer_1 (buffer_1_out, Push);
  buf buffer_2 (buffer_2_out, transistor_1_out[0]);
  Transistor #(.\type ("n"), .width(2)) transistor_1 (.in(Amount), .out(transistor_1_out), .gate(buffer_1_out));
  Pull_Resistor pull_resistor_1 (.node(transistor_1_out));
  buf buffer_3 (buffer_3_out, Push);
  Pull_Resistor pull_resistor_2 (.node(pull_resistor_2_node));
  Transistor transistor_2 (.in(Push), .out(pull_resistor_2_node), .gate(buffer_3_out));
  Transistor transistor_3 (.in(transistor_1_out[0]), .out(transistor_3_out), .gate(buffer_2_out));
  Pull_Resistor pull_resistor_3 (.node(transistor_3_out));
  _2Signals_Turn_OFF u_2signals_turn_off_1 (.in_1(transistor_1_out[1]), .out_2(n2signals_turn_off_1_out_2));
  buf buffer_4 (buffer_4_out, pull_resistor_2_node);
  Pull_Resistor pull_resistor_4 (.node(pull_resistor_4_node));
  Shift_Register #(.width(10), .length(32)) shift_register_1 (
    .in(pull_resistor_4_node), .clk(or_1_out), .out(shift_register_1_out), .load(buffer_4_out),
    .d0(_13[9:0]), .d1(_13[19:10]), .d2(_13[29:20]), .d3(in_10[9:0]),
    .q3({shift_register_1_q3_2, shift_register_1_q3}), .d4(in_10[19:10]),
    .q4({shift_register_1_q4_2, shift_register_1_q4}), .d5(in_10[29:20]),
    .q5({shift_register_1_q5_2, shift_register_1_q5}), .d6(in_5[9:0]),
    .q6({shift_register_1_q6_2, shift_register_1_q6}), .d7(in_5[19:10]),
    .q7({shift_register_1_q7_2, shift_register_1_q7}), .d8(in_5[29:20]),
    .q8({shift_register_1_q8_2, shift_register_1_q8}), .d9(in_2[9:0]),
    .q9({shift_register_1_q9_2, shift_register_1_q9}), .d10(in_2[19:10]),
    .q10({shift_register_1_q10_2, shift_register_1_q10}), .d11(in_2[29:20]),
    .q11({shift_register_1_q11_2, shift_register_1_q11}), .d12(in_11[9:0]),
    .q12({shift_register_1_q12_2, shift_register_1_q12}), .d13(in_11[19:10]),
    .q13({shift_register_1_q13_2, shift_register_1_q13}), .d14(in_11[29:20]),
    .q14({shift_register_1_q14_2, shift_register_1_q14}), .d15(in_6[9:0]),
    .q15({shift_register_1_q15_2, shift_register_1_q15}), .d16(in_6[19:10]),
    .q16({shift_register_1_q16_2, shift_register_1_q16}), .d17(in_6[29:20]),
    .q17({shift_register_1_q17_2, shift_register_1_q17}), .d18(in_3[9:0]),
    .q18({shift_register_1_q18_2, shift_register_1_q18}), .d19(in_3[19:10]),
    .q19({shift_register_1_q19_2, shift_register_1_q19}), .d20(in_3[29:20]),
    .q20({shift_register_1_q20_2, shift_register_1_q20}), .d21(in_12[9:0]),
    .q21({shift_register_1_q21_2, shift_register_1_q21}), .d22(in_12[19:10]),
    .q22({shift_register_1_q22_2, shift_register_1_q22}), .d23(in_12[29:20]),
    .q23({shift_register_1_q23_2, shift_register_1_q23}), .d24(in_7[9:0]),
    .q24({shift_register_1_q24_2, shift_register_1_q24}), .d25(in_7[19:10]),
    .q25({shift_register_1_q25_2, shift_register_1_q25}), .d26(in_7[29:20]),
    .q26({shift_register_1_q26_2, shift_register_1_q26}), .d27(in_4[9:0]),
    .q27({shift_register_1_q27_2, shift_register_1_q27}), .d28(in_4[19:10]),
    .q28({shift_register_1_q28_2, shift_register_1_q28}), .d29(in_4[29:20]),
    .q29({shift_register_1_q29_2, shift_register_1_q29}), .d30(in_13[9:0]),
    .q30({shift_register_1_q30_2, shift_register_1_q30}), .d31(in_13[19:10]), .q31(shift_register_1_q31));  // open: shift, clr, q0, q1, q2
  or or_1 (or_1_out, pull_resistor_2_node, transistor_3_out, n2signals_turn_off_1_out_2);
  Multiplexer #(.width(8), .disabled(0), .enable("false")) multiplexer_1 (
    .in0(in_16), .in1(shift_register_1_q3), .out(out_52[7:0]), .sel(shift_register_1_q3_2[8]));
  Multiplexer #(.width(8), .disabled(0), .enable("false")) multiplexer_2 (
    .in0(in_17), .in1(shift_register_1_q4), .out(out_52[15:8]), .sel(shift_register_1_q4_2[8]));
  Multiplexer #(.width(8), .disabled(0), .enable("false")) multiplexer_3 (
    .in0(in_18), .in1(shift_register_1_q5), .out(out_52[23:16]), .sel(shift_register_1_q5_2[8]));
  Multiplexer #(.width(8), .disabled(0), .enable("false")) multiplexer_4 (
    .in0(in_19), .in1(shift_register_1_q6), .out(out_52[31:24]), .sel(shift_register_1_q6_2[8]));
  Multiplexer #(.width(8), .disabled(0), .enable("false")) multiplexer_5 (
    .in0(in_20), .in1(shift_register_1_q7), .out(out_53[7:0]), .sel(shift_register_1_q7_2[8]));
  Multiplexer #(.width(8), .disabled(0), .enable("false")) multiplexer_6 (
    .in0(in_21), .in1(shift_register_1_q8), .out(out_53[15:8]), .sel(shift_register_1_q8_2[8]));
  Multiplexer #(.width(8), .disabled(0), .enable("false")) multiplexer_7 (
    .in0(in_22), .in1(shift_register_1_q9), .out(out_53[23:16]), .sel(shift_register_1_q9_2[8]));
  Multiplexer #(.width(8), .disabled(0), .enable("false")) multiplexer_8 (
    .in0(in_23), .in1(shift_register_1_q10), .out(out_53[31:24]), .sel(shift_register_1_q10_2[8]));
  Multiplexer #(.width(8), .disabled(0), .enable("false")) multiplexer_9 (
    .in0(in_24), .in1(shift_register_1_q11), .out(out_54[7:0]), .sel(shift_register_1_q11_2[8]));
  Multiplexer #(.width(8), .disabled(0), .enable("false")) multiplexer_10 (
    .in0(in_25), .in1(shift_register_1_q12), .out(out_54[15:8]), .sel(shift_register_1_q12_2[8]));
  Multiplexer #(.width(8), .disabled(0), .enable("false")) multiplexer_11 (
    .in0(in_26), .in1(shift_register_1_q13), .out(out_54[23:16]), .sel(shift_register_1_q13_2[8]));
  Multiplexer #(.width(8), .disabled(0), .enable("false")) multiplexer_12 (
    .in0(in_27), .in1(shift_register_1_q14), .out(out_54[31:24]), .sel(shift_register_1_q14_2[8]));
  Multiplexer #(.width(8), .disabled(0), .enable("false")) multiplexer_13 (
    .in0(in_28), .in1(shift_register_1_q15), .out(out_55[7:0]), .sel(shift_register_1_q15_2[8]));
  Multiplexer #(.width(8), .disabled(0), .enable("false")) multiplexer_14 (
    .in0(in_29), .in1(shift_register_1_q16), .out(out_55[15:8]), .sel(shift_register_1_q16_2[8]));
  Multiplexer #(.width(8), .disabled(0), .enable("false")) multiplexer_15 (
    .in0(in_30), .in1(shift_register_1_q17), .out(out_55[23:16]), .sel(shift_register_1_q17_2[8]));
  Multiplexer #(.width(8), .disabled(0), .enable("false")) multiplexer_16 (
    .in0(in_31), .in1(shift_register_1_q18), .out(out_55[31:24]), .sel(shift_register_1_q18_2[8]));
  Multiplexer #(.width(8), .disabled(0), .enable("false")) multiplexer_17 (
    .in0(in_32), .in1(shift_register_1_q19), .out(out_56[7:0]), .sel(shift_register_1_q19_2[8]));
  Multiplexer #(.width(8), .disabled(0), .enable("false")) multiplexer_18 (
    .in0(in_33), .in1(shift_register_1_q20), .out(out_56[15:8]), .sel(shift_register_1_q20_2[8]));
  Multiplexer #(.width(8), .disabled(0), .enable("false")) multiplexer_19 (
    .in0(in_34), .in1(shift_register_1_q21), .out(out_56[23:16]), .sel(shift_register_1_q21_2[8]));
  Multiplexer #(.width(8), .disabled(0), .enable("false")) multiplexer_20 (
    .in0(in_35), .in1(shift_register_1_q22), .out(out_56[31:24]), .sel(shift_register_1_q22_2[8]));
  Multiplexer #(.width(8), .disabled(0), .enable("false")) multiplexer_21 (
    .in0(in_36), .in1(shift_register_1_q23), .out(out_57[7:0]), .sel(shift_register_1_q23_2[8]));
  Multiplexer #(.width(8), .disabled(0), .enable("false")) multiplexer_22 (
    .in0(in_37), .in1(shift_register_1_q24), .out(out_57[15:8]), .sel(shift_register_1_q24_2[8]));
  Multiplexer #(.width(8), .disabled(0), .enable("false")) multiplexer_23 (
    .in0(in_38), .in1(shift_register_1_q25), .out(out_57[23:16]), .sel(shift_register_1_q25_2[8]));
  Multiplexer #(.width(8), .disabled(0), .enable("false")) multiplexer_24 (
    .in0(in_39), .in1(shift_register_1_q26), .out(out_57[31:24]), .sel(shift_register_1_q26_2[8]));
  Multiplexer #(.width(8), .disabled(0), .enable("false")) multiplexer_25 (
    .in0(in_40), .in1(shift_register_1_q27), .out(out_58[7:0]), .sel(shift_register_1_q27_2[8]));
  Multiplexer #(.width(8), .disabled(0), .enable("false")) multiplexer_26 (
    .in0(in_41), .in1(shift_register_1_q28), .out(out_58[15:8]), .sel(shift_register_1_q28_2[8]));
  Multiplexer #(.width(8), .disabled(0), .enable("false")) multiplexer_27 (
    .in0(in_42), .in1(shift_register_1_q29), .out(out_58[23:16]), .sel(shift_register_1_q29_2[8]));
  Multiplexer #(.width(8), .disabled(0), .enable("false")) multiplexer_28 (
    .in0(in_43), .in1(shift_register_1_q30), .out(out_58[31:24]), .sel(shift_register_1_q30_2[8]));
  Multiplexer #(.width(8), .disabled(0), .enable("false")) multiplexer_29 (
    .in0(in_44), .in1(shift_register_1_q31[7:0]), .out(out_59[7:0]), .sel(shift_register_1_q31[8]));
  Multiplexer #(.width(8), .disabled(0), .enable("false")) multiplexer_30 (
    .in0(in_45), .in1(shift_register_2_q0), .out(out_59[15:8]), .sel(shift_register_2_q0_2[8]));
  Multiplexer #(.width(8), .disabled(0), .enable("false")) multiplexer_31 (
    .in0(in_46), .in1(shift_register_2_q1[7:0]), .out(out_59[23:16]), .sel(shift_register_2_q1[8]));
  Shift_Register #(.width(10), .length(7)) shift_register_2 (
    .in(shift_register_1_out), .clk(or_1_out), .load(buffer_4_out), .d0(in_13[29:20]),
    .q0({shift_register_2_q0_2, shift_register_2_q0}), .d1(in_14[9:0]), .q1(shift_register_2_q1),
    .d2(in_14[19:10]), .q2(shift_register_2_q2), .d3(in_14[29:20]),
    .q3({shift_register_2_q3_2, shift_register_2_q3}), .d4(_1[9:0]),
    .q4({shift_register_2_q4_2, shift_register_2_q4}), .d5(_1[19:10]),
    .q5({shift_register_2_q5_2, shift_register_2_q5}), .d6(_1[29:20]),
    .q6({shift_register_2_q6_2, shift_register_2_q6}));  // open: shift, out, clr
  Multiplexer #(.width(8), .disabled(0), .enable("false")) multiplexer_32 (
    .in0(in_47), .in1(shift_register_2_q2[7:0]), .out(out_59[31:24]), .sel(shift_register_2_q2[8]));
  Multiplexer #(.width(8), .disabled(0), .enable("false")) multiplexer_33 (
    .in0(in_48), .in1(shift_register_2_q3), .out(out_60[7:0]), .sel(shift_register_2_q3_2[8]));
  Multiplexer #(.width(8), .disabled(0), .enable("false")) multiplexer_34 (
    .in0(in_49), .in1(shift_register_2_q4), .out(out_60[15:8]), .sel(shift_register_2_q4_2[8]));
  Multiplexer #(.width(8), .disabled(0), .enable("false")) multiplexer_35 (
    .in0(in_50), .in1(shift_register_2_q5), .out(out_60[23:16]), .sel(shift_register_2_q5_2[8]));
  Multiplexer #(.width(8), .disabled(0), .enable("false")) multiplexer_36 (
    .in0(in_51), .in1(shift_register_2_q6), .out(out_60[31:24]), .sel(shift_register_2_q6_2[8]));

  // Notes on the sheet:
  //   (the rightest one)
  //   This will only work with 0 or 1 opacity, until I can find a way to use transparency without a lot of lag.
  //   the inputs are inverted left/right
  //   (the leftist one)
endmodule
module GPU_____Color_replacer (
  input  [7:0] Back_color_1,
  input  [31:0] Object_color,
  input  [7:0] Back_color_2,
  input  [7:0] Back_color_3,
  output [7:0] out_5,
  output [7:0] out_6,
  output [7:0] out_7
);

  wire comparator_1_gt, comparator_2_gt, comparator_3_gt, comparator_4_gt, comparator_5_gt, comparator_6_gt,
       comparator_7_gt, comparator_8_gt, comparator_9_gt;
  wire [2:0] adder_1_out, adder_2_out, adder_3_out, adder_4_out, adder_5_out, adder_6_out, adder_7_out,
       adder_8_out, adder_9_out, bit_extender_2_out, bit_extender_4_out, bit_extender_6_out, divider_1_out,
       divider_1_rem, divider_2_out, divider_2_rem, divider_3_out, divider_3_rem, divider_4_out,
       divider_4_rem, divider_5_out, divider_5_rem, divider_6_out, divider_6_rem, divider_7_out,
       divider_7_rem, divider_8_out, divider_8_rem, divider_9_out, divider_9_rem, divider_10_out,
       divider_10_rem, divider_11_out, divider_11_rem, divider_12_out, divider_12_rem, divider_13_out,
       divider_13_rem, divider_14_out, divider_14_rem, divider_15_out, divider_15_rem, divider_16_out,
       divider_16_rem, divider_17_out, divider_17_rem, divider_18_out, divider_18_rem, multiplier_1_cout,
       multiplier_1_out, multiplier_2_cout, multiplier_2_out, multiplier_3_cout, multiplier_3_out,
       multiplier_4_cout, multiplier_4_out, multiplier_5_cout, multiplier_5_out, multiplier_6_cout,
       multiplier_6_out, multiplier_7_cout, multiplier_7_out, multiplier_8_cout, multiplier_8_out,
       multiplier_9_cout, multiplier_9_out, multiplier_10_cout, multiplier_10_out, multiplier_11_cout,
       multiplier_11_out, multiplier_12_cout, multiplier_12_out, multiplier_13_cout, multiplier_13_out,
       multiplier_14_cout, multiplier_14_out, multiplier_15_cout, multiplier_15_out, multiplier_16_cout,
       multiplier_16_out, multiplier_17_cout, multiplier_17_out, multiplier_18_cout, multiplier_18_out,
       subtractor_1_out, subtractor_2_out, subtractor_3_out;
  wire [2:2] adder_12_out, adder_15_out, adder_18_out;
  wire [11:0] bit_extender_1_out, bit_extender_3_out, bit_extender_5_out;

  assign bit_extender_1_out = {{2{1'b0}}, Object_color[9:0]};  // Bit_Extender bit_extender_1
  assign bit_extender_2_out = {{1{1'b0}}, Back_color_1[1:0]};  // Bit_Extender bit_extender_2
  assign bit_extender_3_out = {{2{1'b0}}, Object_color[19:10]};  // Bit_Extender bit_extender_3
  assign bit_extender_4_out = {{1{1'b0}}, Back_color_2[1:0]};  // Bit_Extender bit_extender_4
  assign bit_extender_5_out = {{2{1'b0}}, Object_color[29:20]};  // Bit_Extender bit_extender_5
  assign bit_extender_6_out = {{1{1'b0}}, Back_color_3[1:0]};  // Bit_Extender bit_extender_6
  Multiplier #(.width(3)) multiplier_1 (
    .a(Back_color_1[7:5]), .b(subtractor_1_out), .out(multiplier_1_out), .cout(multiplier_1_cout));  // open: cin
  Subtractor #(.width(3)) subtractor_1 (
    .a(3'b011), .b(bit_extender_1_out[10:8]), .out(subtractor_1_out));  // open: bin, bout
  Multiplier #(.width(3)) multiplier_2 (
    .a(bit_extender_1_out[10:8]), .b(bit_extender_1_out[7:5]), .out(multiplier_2_out),
    .cout(multiplier_2_cout));  // open: cin
  Divider #(.width(3)) divider_1 (
    .a(multiplier_2_out), .b(3'b011), .out(divider_1_out), .upper(multiplier_2_cout), .rem(divider_1_rem));
  Multiplier #(.width(3)) multiplier_3 (
    .a(Back_color_1[4:2]), .b(subtractor_1_out), .out(multiplier_3_out), .cout(multiplier_3_cout));  // open: cin
  Multiplier #(.width(3)) multiplier_4 (
    .a(bit_extender_1_out[4:2]), .b(bit_extender_1_out[10:8]), .out(multiplier_4_out),
    .cout(multiplier_4_cout));  // open: cin
  Divider #(.width(3)) divider_2 (
    .a(multiplier_4_out), .b(3'b011), .out(divider_2_out), .upper(multiplier_4_cout), .rem(divider_2_rem));
  Multiplier #(.width(3)) multiplier_5 (
    .a(subtractor_1_out), .b(bit_extender_2_out), .out(multiplier_5_out), .cout(multiplier_5_cout));  // open: cin
  Multiplier #(.width(3)) multiplier_6 (
    .a(bit_extender_1_out[10:8]), .b({bit_extender_1_out[11], bit_extender_1_out[1:0]}),
    .out(multiplier_6_out), .cout(multiplier_6_cout));  // open: cin
  Divider #(.width(3)) divider_3 (
    .a(multiplier_6_out), .b(3'b011), .out(divider_3_out), .upper(multiplier_6_cout), .rem(divider_3_rem));
  Multiplier #(.width(3)) multiplier_7 (
    .a(Back_color_2[7:5]), .b(subtractor_2_out), .out(multiplier_7_out), .cout(multiplier_7_cout));  // open: cin
  Subtractor #(.width(3)) subtractor_2 (
    .a(3'b011), .b(bit_extender_3_out[10:8]), .out(subtractor_2_out));  // open: bin, bout
  Multiplier #(.width(3)) multiplier_8 (
    .a(bit_extender_3_out[10:8]), .b(bit_extender_3_out[7:5]), .out(multiplier_8_out),
    .cout(multiplier_8_cout));  // open: cin
  Divider #(.width(3)) divider_4 (
    .a(multiplier_8_out), .b(3'b011), .out(divider_4_out), .upper(multiplier_8_cout), .rem(divider_4_rem));
  Multiplier #(.width(3)) multiplier_9 (
    .a(Back_color_2[4:2]), .b(subtractor_2_out), .out(multiplier_9_out), .cout(multiplier_9_cout));  // open: cin
  Multiplier #(.width(3)) multiplier_10 (
    .a(bit_extender_3_out[4:2]), .b(bit_extender_3_out[10:8]), .out(multiplier_10_out),
    .cout(multiplier_10_cout));  // open: cin
  Divider #(.width(3)) divider_5 (
    .a(multiplier_10_out), .b(3'b011), .out(divider_5_out), .upper(multiplier_10_cout), .rem(divider_5_rem));
  Multiplier #(.width(3)) multiplier_11 (
    .a(subtractor_2_out), .b(bit_extender_4_out), .out(multiplier_11_out), .cout(multiplier_11_cout));  // open: cin
  Multiplier #(.width(3)) multiplier_12 (
    .a(bit_extender_3_out[10:8]), .b({bit_extender_3_out[11], bit_extender_3_out[1:0]}),
    .out(multiplier_12_out), .cout(multiplier_12_cout));  // open: cin
  Divider #(.width(3)) divider_6 (
    .a(multiplier_12_out), .b(3'b011), .out(divider_6_out), .upper(multiplier_12_cout), .rem(divider_6_rem));
  Multiplier #(.width(3)) multiplier_13 (
    .a(Back_color_3[7:5]), .b(subtractor_3_out), .out(multiplier_13_out), .cout(multiplier_13_cout));  // open: cin
  Subtractor #(.width(3)) subtractor_3 (
    .a(3'b011), .b(bit_extender_5_out[10:8]), .out(subtractor_3_out));  // open: bin, bout
  Multiplier #(.width(3)) multiplier_14 (
    .a(bit_extender_5_out[10:8]), .b(bit_extender_5_out[7:5]), .out(multiplier_14_out),
    .cout(multiplier_14_cout));  // open: cin
  Divider #(.width(3)) divider_7 (
    .a(multiplier_14_out), .b(3'b011), .out(divider_7_out), .upper(multiplier_14_cout), .rem(divider_7_rem));
  Multiplier #(.width(3)) multiplier_15 (
    .a(Back_color_3[4:2]), .b(subtractor_3_out), .out(multiplier_15_out), .cout(multiplier_15_cout));  // open: cin
  Multiplier #(.width(3)) multiplier_16 (
    .a(bit_extender_5_out[4:2]), .b(bit_extender_5_out[10:8]), .out(multiplier_16_out),
    .cout(multiplier_16_cout));  // open: cin
  Divider #(.width(3)) divider_8 (
    .a(multiplier_16_out), .b(3'b011), .out(divider_8_out), .upper(multiplier_16_cout), .rem(divider_8_rem));
  Multiplier #(.width(3)) multiplier_17 (
    .a(subtractor_3_out), .b(bit_extender_6_out), .out(multiplier_17_out), .cout(multiplier_17_cout));  // open: cin
  Multiplier #(.width(3)) multiplier_18 (
    .a(bit_extender_5_out[10:8]), .b({bit_extender_5_out[11], bit_extender_5_out[1:0]}),
    .out(multiplier_18_out), .cout(multiplier_18_cout));  // open: cin
  Divider #(.width(3)) divider_9 (
    .a(multiplier_18_out), .b(3'b011), .out(divider_9_out), .upper(multiplier_18_cout), .rem(divider_9_rem));
  Divider #(.width(3)) divider_10 (
    .a(multiplier_1_out), .b(3'b011), .out(divider_10_out), .upper(multiplier_1_cout), .rem(divider_10_rem));
  Adder #(.width(3)) adder_1 (.a(divider_10_rem), .b(divider_1_rem), .out(adder_1_out));  // open: cin, cout
  Comparator #(.width(3), .mode("unsigned")) comparator_1 (
    .a(adder_1_out), .b(3'b001), .gt(comparator_1_gt));  // open: eq, lt
  Divider #(.width(3)) divider_11 (
    .a(multiplier_3_out), .b(3'b011), .out(divider_11_out), .upper(multiplier_3_cout), .rem(divider_11_rem));
  Adder #(.width(3)) adder_2 (.a(divider_11_rem), .b(divider_2_rem), .out(adder_2_out));  // open: cin, cout
  Divider #(.width(3)) divider_12 (
    .a(multiplier_5_out), .b(3'b011), .out(divider_12_out), .upper(multiplier_5_cout), .rem(divider_12_rem));
  Adder #(.width(3)) adder_3 (.a(divider_12_rem), .b(divider_3_rem), .out(adder_3_out));  // open: cin, cout
  Comparator #(.width(3), .mode("unsigned")) comparator_2 (
    .a(adder_3_out), .b(3'b001), .gt(comparator_2_gt));  // open: eq, lt
  Divider #(.width(3)) divider_13 (
    .a(multiplier_7_out), .b(3'b011), .out(divider_13_out), .upper(multiplier_7_cout), .rem(divider_13_rem));
  Adder #(.width(3)) adder_4 (.a(divider_13_rem), .b(divider_4_rem), .out(adder_4_out));  // open: cin, cout
  Comparator #(.width(3), .mode("unsigned")) comparator_3 (
    .a(adder_4_out), .b(3'b001), .gt(comparator_3_gt));  // open: eq, lt
  Divider #(.width(3)) divider_14 (
    .a(multiplier_9_out), .b(3'b011), .out(divider_14_out), .upper(multiplier_9_cout), .rem(divider_14_rem));
  Adder #(.width(3)) adder_5 (.a(divider_14_rem), .b(divider_5_rem), .out(adder_5_out));  // open: cin, cout
  Divider #(.width(3)) divider_15 (
    .a(multiplier_11_out), .b(3'b011), .out(divider_15_out), .upper(multiplier_11_cout), .rem(divider_15_rem));
  Adder #(.width(3)) adder_6 (.a(divider_15_rem), .b(divider_6_rem), .out(adder_6_out));  // open: cin, cout
  Comparator #(.width(3), .mode("unsigned")) comparator_4 (
    .a(adder_6_out), .b(3'b001), .gt(comparator_4_gt));  // open: eq, lt
  Divider #(.width(3)) divider_16 (
    .a(multiplier_13_out), .b(3'b011), .out(divider_16_out), .upper(multiplier_13_cout), .rem(divider_16_rem));
  Adder #(.width(3)) adder_7 (.a(divider_16_rem), .b(divider_7_rem), .out(adder_7_out));  // open: cin, cout
  Comparator #(.width(3), .mode("unsigned")) comparator_5 (
    .a(adder_7_out), .b(3'b001), .gt(comparator_5_gt));  // open: eq, lt
  Divider #(.width(3)) divider_17 (
    .a(multiplier_15_out), .b(3'b011), .out(divider_17_out), .upper(multiplier_15_cout), .rem(divider_17_rem));
  Adder #(.width(3)) adder_8 (.a(divider_17_rem), .b(divider_8_rem), .out(adder_8_out));  // open: cin, cout
  Divider #(.width(3)) divider_18 (
    .a(multiplier_17_out), .b(3'b011), .out(divider_18_out), .upper(multiplier_17_cout), .rem(divider_18_rem));
  Adder #(.width(3)) adder_9 (.a(divider_18_rem), .b(divider_9_rem), .out(adder_9_out));  // open: cin, cout
  Comparator #(.width(3), .mode("unsigned")) comparator_6 (
    .a(adder_9_out), .b(3'b001), .gt(comparator_6_gt));  // open: eq, lt
  Adder #(.width(3)) adder_10 (
    .a(divider_10_out), .b(divider_1_out), .out(out_5[7:5]), .cin(comparator_1_gt));  // open: cout
  Comparator #(.width(3), .mode("unsigned")) comparator_7 (
    .a(adder_2_out), .b(3'b001), .gt(comparator_7_gt));  // open: eq, lt
  Adder #(.width(3)) adder_11 (
    .a(divider_11_out), .b(divider_2_out), .out(out_5[4:2]), .cin(comparator_7_gt));  // open: cout
  Adder #(.width(3)) adder_12 (
    .a(divider_12_out), .b(divider_3_out), .out({adder_12_out[2], out_5[1:0]}), .cin(comparator_2_gt));  // open: cout
  Adder #(.width(3)) adder_13 (
    .a(divider_13_out), .b(divider_4_out), .out(out_6[7:5]), .cin(comparator_3_gt));  // open: cout
  Comparator #(.width(3), .mode("unsigned")) comparator_8 (
    .a(adder_5_out), .b(3'b001), .gt(comparator_8_gt));  // open: eq, lt
  Adder #(.width(3)) adder_14 (
    .a(divider_14_out), .b(divider_5_out), .out(out_6[4:2]), .cin(comparator_8_gt));  // open: cout
  Adder #(.width(3)) adder_15 (
    .a(divider_15_out), .b(divider_6_out), .out({adder_15_out[2], out_6[1:0]}), .cin(comparator_4_gt));  // open: cout
  Adder #(.width(3)) adder_16 (
    .a(divider_16_out), .b(divider_7_out), .out(out_7[7:5]), .cin(comparator_5_gt));  // open: cout
  Comparator #(.width(3), .mode("unsigned")) comparator_9 (
    .a(adder_8_out), .b(3'b001), .gt(comparator_9_gt));  // open: eq, lt
  Adder #(.width(3)) adder_17 (
    .a(divider_17_out), .b(divider_8_out), .out(out_7[4:2]), .cin(comparator_9_gt));  // open: cout
  Adder #(.width(3)) adder_18 (
    .a(divider_18_out), .b(divider_9_out), .out({adder_18_out[2], out_7[1:0]}), .cin(comparator_6_gt));  // open: cout

  // Notes on the sheet:
  //   Not being used right now; it lags a lot when using 12 of this.
  //   This will do a weighted average between the current pixel color and the new pixel color, taking count its transparency
  //   Final Color = Oldcolor(1-New Color Opacity)/3 + New Color*Opacity/3
  //   Opacity is a inputted value between 0 and 3, and due to the math, will stands between 0 and 1.
  //   Again, it's a mess just because it seems that the fewer the wire nodes, faster the simulation will be.
  //   Final color values are rounded to nearest integer.
endmodule

module Tools (
);


  // Notes on the sheet:
  //   just a separator
endmodule

module Text_to_Hex_tool_for_you (
);

  wire Clock_out, counter_1_carry, or_1_out, or_2_out, Reset_out;
  wire [6:0] keyboard_1_data;
  wire [7:0] counter_2_q;
  wire [31:0] adder_1_out, bit_extender_1_out, register_1_q, shifter_1_out;

  Keyboard #(.buflen(255)) keyboard_1 (.clk(Clock_out), .clr(Reset_out), .data(keyboard_1_data));  // open: re, avail
  assign bit_extender_1_out = {{25{1'b0}}, keyboard_1_data};  // Bit_Extender bit_extender_1
  Adder #(.width(32)) adder_1 (.a(bit_extender_1_out), .b(register_1_q), .out(adder_1_out));  // open: cin, cout
  Shifter #(.width(32)) shifter_1 (.in(adder_1_out), .\dist (5'b01000), .out(shifter_1_out));
  Button Clock (.out(Clock_out));
  Counter #(.max('h4), .ongoal("stay")) counter_1 (
    .carry(counter_1_carry), .clk(Clock_out), .clr(or_1_out));  // open: load, D, count, Q
  or or_1 (or_1_out, counter_1_carry, Reset_out);
  Register #(.width(32)) register_1 (.D(shifter_1_out), .Q(register_1_q), .clk(Clock_out), .clr(or_2_out));  // open: en
  or or_2 (or_2_out, counter_1_carry, Reset_out);
  Counter #(.ongoal("stay")) counter_2 (
    .Q(counter_2_q), .clk(counter_1_carry), .clr(Reset_out));  // open: load, D, count, carry
  Button Reset (.out(Reset_out));
  // RAM ram_1: pin names not known; wires that end beside it: counter_2_q, adder_1_out, counter_1_carry, Reset_out

  // Notes on the sheet:
  //   I used this for the "Logiwin Open blablabla" on the main screen
  //   This is temporary.
  //   Type the desired text in the keyboard. For each 4 clocks, 1 grouped (4-characters) ASCII will pop out in this RAM
endmodule

module Unused__wait_for_the_future (
);


  // Notes on the sheet:
  //   just a separator
endmodule

module Soundboard_w__Speakers__not_used_yet (
  input  [31:0] In,
  input  in_2
);

  wire bitfinder_1_found, pull_resistor_1_node, pull_resistor_4_node, pull_resistor_5_node,
       pull_resistor_7_node, pull_resistor_11_node, undriven, undriven_2, undriven_7;
  wire [3:0] undriven_3, undriven_4, undriven_5;
  wire [4:0] transistor_4_out, undriven_6;
  wire [6:0] bit_extender_2_out, bit_extender_4_out, bit_extender_6_out, bit_extender_7_out;
  wire [7:0] counter_1_q;
  wire [13:0] random_1_out, random_2_out, random_3_out;
  wire [15:0] bit_extender_1_out, bit_extender_3_out, bit_extender_5_out, bit_extender_8_out,
       pull_resistor_8_node, transistor_1_out, transistor_2_out, transistor_3_out;
  wire [17:0] rom_1_data;

  Old_____Will_delete_later old_will_delete_later_1 ();
  RAM #(.addrWidth(12), .dataWidth(32)) ram_1 ();  // open: addr, data, sel, clk, ld, clr
  Pull_Resistor pull_resistor_1 (.node(pull_resistor_1_node));
  Random #(.width(14)) random_1 (.clk(undriven), .out(random_1_out));  // open: next, clr
  Random #(.width(14)) random_2 (.clk(undriven_2), .out(random_2_out));  // open: next, clr
  assign bit_extender_1_out = {{2{1'b0}}, random_1_out};  // Bit_Extender bit_extender_1
  // Probe on bit_extender_1_out
  Transistor #(.\type ("n"), .width(16)) transistor_1 (
    .in(bit_extender_1_out), .out(transistor_1_out), .gate(pull_resistor_1_node));
  Pull_Resistor pull_resistor_2 (.node(transistor_1_out));
  assign bit_extender_2_out = {{3{1'b0}}, undriven_3};  // Bit_Extender bit_extender_2
  assign bit_extender_3_out = {{2{1'b0}}, random_2_out};  // Bit_Extender bit_extender_3
  // Probe on bit_extender_3_out
  Transistor #(.\type ("n"), .width(16)) transistor_2 (
    .in(bit_extender_3_out), .out(transistor_2_out), .gate(pull_resistor_1_node));
  Pull_Resistor pull_resistor_3 (.node(transistor_2_out));
  assign bit_extender_4_out = {{3{1'b0}}, undriven_4};  // Bit_Extender bit_extender_4
  Pull_Resistor #(.pull(1)) pull_resistor_4 (.node(pull_resistor_4_node));
  Pull_Resistor #(.pull(1)) pull_resistor_5 (.node(pull_resistor_5_node));
  Random #(.width(14)) random_3 (.out(random_3_out));  // open: clk, next, clr
  assign bit_extender_5_out = {{2{1'b0}}, random_3_out};  // Bit_Extender bit_extender_5
  // Probe on bit_extender_5_out
  Transistor #(.\type ("n"), .width(16)) transistor_3 (
    .in(bit_extender_5_out), .out(transistor_3_out), .gate(pull_resistor_1_node));
  Pull_Resistor pull_resistor_6 (.node(transistor_3_out));
  Pull_Resistor #(.pull(1)) pull_resistor_7 (.node(pull_resistor_7_node));
  assign bit_extender_6_out = {{3{1'b0}}, undriven_5};  // Bit_Extender bit_extender_6
  Counter #(.max('h12), .ongoal("load")) counter_1 (
    .Q(counter_1_q), .clk(undriven_7));  // open: load, D, count, carry, clr
  ROM #(.dataWidth(18)) rom_1 (.addr(counter_1_q), .data(rom_1_data));  // open: sel
  Pull_Resistor pull_resistor_8 (.node(pull_resistor_8_node));
  BitFinder #(.width(16)) bitfinder_1 (.in(pull_resistor_8_node), .found(bitfinder_1_found));  // open: index
  assign bit_extender_7_out = {{2{1'b0}}, transistor_4_out};  // Bit_Extender bit_extender_7
  Transistor #(.\type ("n"), .width(5)) transistor_4 (
    .in(undriven_6), .out(transistor_4_out), .gate(bitfinder_1_found));
  Pull_Resistor pull_resistor_9 (.node(transistor_4_out));
  // Probe on transistor_4_out
  Pull_Resistor pull_resistor_10 ();  // open: node
  assign bit_extender_8_out = {{2{1'b0}}, rom_1_data[13:0]};  // Bit_Extender bit_extender_8
  // Probe on bit_extender_8_out
  Pull_Resistor #(.pull(1)) pull_resistor_11 (.node(pull_resistor_11_node));

  // Notes on the sheet:
  //    It will consist of 4 channels sound system, but i am having some problems with this mod for now.
  //   contents of rom_1 (hex, n*v repeats v):
  //   0 93 dc 126 174 126 dc
  //   Still working on it! I use the only available sound mod that i found, the "buzzer".
  //   (Removed the mod for now from the circ, later I will update it)
  //   Sound format:
  //   First 14 bits for frequency
  //   14~18  for volume
endmodule

module Old_____Will_delete_later (
);


  // Notes on the sheet:
  //   cemitery
endmodule

module Dual_Address_RAM_chip (
  input  [31:0] Data_In____Out,
  input  [31:0] Ext_Data_Out____In,
  input  [2:0] Controls,
  input  [21:0] Ext_Address_2__R,
  input  [21:0] Ext_Address_1__W,
  output [31:0] Ext_Data_In____Out,
  output [31:0] Data_Out____In,
  output Clock,
  output Store,
  output Focus,
  output Reset__Be_careful,
  output [21:0] Address_2__READ,
  output [21:0] Address_1__WRITE
);

  not not_1 (Focus, Controls[1]);

  assign Address_1__WRITE = Ext_Address_1__W;
  assign Address_2__READ = Ext_Address_2__R;
  assign Clock = Controls[0];
  assign Data_Out____In = Ext_Data_Out____In;
  assign Ext_Data_In____Out = Data_In____Out;
  assign Store = Controls[0];

  // Notes on the sheet:
  //   Labels texts are big here so you can read from the subcircuit appearance screen.
  //   See how I do everything for you guys? :) Just Mod mod mod mod mod and share!!
  //   Since 1.1.0, not being used.
  //    [=CPU OUT -> IN]
  //    [=CPU IN -> OUT]
  //   *
  //   First to focus
  //   Sencond to Store
  //   Third to Reset
endmodule

module Old_mario_gpu (
  input  [7:0] RGB__3_3_2,
  input  Update_that_pixel,
  input  ON
);

  wire button_2_out, button_3_out, button_4_out, button_5_out, button_out, clock_1_out, decoder_2_out0,
       decoder_2_out1, decoder_2_out2, decoder_2_out3, decoder_2_out4, decoder_2_out5, decoder_2_out6,
       decoder_2_out7, decoder_2_out8, decoder_2_out9, decoder_2_out10, decoder_2_out11, decoder_2_out12,
       decoder_2_out13, decoder_2_out14, decoder_2_out15, decoder_2_out16, decoder_2_out17, decoder_2_out18,
       decoder_2_out19, decoder_2_out20, decoder_2_out21, decoder_2_out22, decoder_2_out23, decoder_2_out24,
       decoder_2_out25, decoder_2_out26, decoder_2_out27, decoder_2_out28, decoder_2_out29, decoder_2_out30,
       decoder_2_out31, gpu_2_primitive_used_on_mario_1_p8, or_1_out, or_2_out, or_3_out, Reset_out;
  wire [4:0] bit_extender_1_out, Column_q;
  wire [7:0] Row_q;
  wire [23:0] decoder_1_out23;

  Decoder #(.select(5), .enable("false")) decoder_1 (
    .out0(decoder_1_out23[23]), .out1(decoder_1_out23[22]), .out2(decoder_1_out23[21]),
    .out3(decoder_1_out23[20]), .out4(decoder_1_out23[19]), .out5(decoder_1_out23[18]),
    .out6(decoder_1_out23[17]), .out7(decoder_1_out23[16]), .out8(decoder_1_out23[15]),
    .out9(decoder_1_out23[14]), .out10(decoder_1_out23[13]), .out11(decoder_1_out23[12]),
    .out12(decoder_1_out23[11]), .out13(decoder_1_out23[10]), .out14(decoder_1_out23[9]),
    .out15(decoder_1_out23[8]), .out16(decoder_1_out23[7]), .out17(decoder_1_out23[6]),
    .out18(decoder_1_out23[5]), .out19(decoder_1_out23[4]), .out20(decoder_1_out23[3]),
    .out21(decoder_1_out23[2]), .out22(decoder_1_out23[1]), .out23(decoder_1_out23[0]),
    .sel(bit_extender_1_out));  // open: out24, out25, out26, out27, out28, out29, out30, out31
  Button button (.out(button_out));
  Counter #(.width(5), .max('h1f), .ongoal("stay")) Column (
    .load(button_out), .count(or_1_out), .Q(Column_q), .clk(or_1_out));  // open: D, carry, clr
  or or_1 (or_1_out, button_out, button_2_out);
  Button button_2 (.out(button_2_out));
  Button button_3 (.out(button_3_out));
  Button button_4 (.out(button_4_out));
  or or_2 (or_2_out, button_4_out, button_5_out);
  Button button_5 (.out(button_5_out));
  Clock clock_1 (.out(clock_1_out));
  Counter #(.ongoal("stay")) Row (
    .load(button_4_out), .count(or_2_out), .Q(Row_q), .clk(or_2_out));  // open: D, carry, clr
  Bit_Extender #(.out_width(5)) bit_extender_1 (.in(Row_q), .out(bit_extender_1_out));
  // Probe on RGB__3_3_2
  or or_3 (or_3_out, Update_that_pixel, button_3_out);
  Button Reset (.out(Reset_out));
  Decoder #(.select(5), .enable("false")) decoder_2 (
    .out0(decoder_2_out0), .out1(decoder_2_out1), .out2(decoder_2_out2), .out3(decoder_2_out3),
    .out4(decoder_2_out4), .out5(decoder_2_out5), .out6(decoder_2_out6), .out7(decoder_2_out7),
    .out8(decoder_2_out8), .out9(decoder_2_out9), .out10(decoder_2_out10), .out11(decoder_2_out11),
    .out12(decoder_2_out12), .out13(decoder_2_out13), .out14(decoder_2_out14), .out15(decoder_2_out15),
    .out16(decoder_2_out16), .out17(decoder_2_out17), .out18(decoder_2_out18), .out19(decoder_2_out19),
    .out20(decoder_2_out20), .out21(decoder_2_out21), .out22(decoder_2_out22), .out23(decoder_2_out23),
    .out24(decoder_2_out24), .out25(decoder_2_out25), .out26(decoder_2_out26), .out27(decoder_2_out27),
    .out28(decoder_2_out28), .out29(decoder_2_out29), .out30(decoder_2_out30), .out31(decoder_2_out31),
    .sel(Column_q));
  DotMatrix #(.matrixcols(32), .matrixrows(1)) dotmatrix_1 (
    .col0(decoder_2_out0), .col1(decoder_2_out1), .col2(decoder_2_out2), .col3(decoder_2_out3),
    .col4(decoder_2_out4), .col5(decoder_2_out5), .col6(decoder_2_out6), .col7(decoder_2_out7),
    .col8(decoder_2_out8), .col9(decoder_2_out9), .col10(decoder_2_out10), .col11(decoder_2_out11),
    .col12(decoder_2_out12), .col13(decoder_2_out13), .col14(decoder_2_out14), .col15(decoder_2_out15),
    .col16(decoder_2_out16), .col17(decoder_2_out17), .col18(decoder_2_out18), .col19(decoder_2_out19),
    .col20(decoder_2_out20), .col21(decoder_2_out21), .col22(decoder_2_out22), .col23(decoder_2_out23),
    .col24(decoder_2_out24), .col25(decoder_2_out25), .col26(decoder_2_out26), .col27(decoder_2_out27),
    .col28(decoder_2_out28), .col29(decoder_2_out29), .col30(decoder_2_out30), .col31(decoder_2_out31));
  // DotMatrix2 dotmatrix2_1: pin names not known
  DotMatrix #(.matrixcols(1), .matrixrows(24)) dotmatrix_2 (.col0(decoder_1_out23));
  // GPU_2__primitive__used_on_Mario gpu_2_primitive_used_on_mario_1: pin names not known; wires that end beside it: clock_1_out, Row_q, Column_q, RGB__3_3_2, or_3_out, Reset_out, ON, gpu_2_primitive_used_on_mario_1_p8, gpu_2_primitive_used_on_mario_1_p8

  // Notes on the sheet:
  //   Size and colors may not represent the officials ones.  Also, this coin is not from this Mario version. Who cares?
  //   Just a primitive way to draw stuff. Turn main computer On first and make sure Tick Frequency is on the max.
  //   Select Row and Column, select color (RGB 8-bit 3-3-2), and when ready push "Update that Pixel", or just leave it On
  //   There will be easier ways to draw stuff, like a Paint Brush program, but I just wanted to draw a Mario. Deal with it.
  //   Actually, made this to think about how GPU should work, and how to make it the most clock eficienccy way.
  //   Yeah I know this row is bugged. I won't mind it, as will only be a waste of time, as I won't use this "GPU".
endmodule

module GPU_2__primitive__used_on_Mario (
  input  [7:0] Row_Selector,
  input  [7:0] Pixel_Color,
  input  Reset,
  input  Power,
  input  [4:0] Column_Selector,
  input  Clock,
  input  Done_with_this_pixel,
  output [4:0] Column_Screen_Selector,
  output [7:0] out_9,
  output [7:0] out_10,
  output [7:0] out_11,
  output [7:0] out_12,
  output [7:0] out_13,
  output [7:0] out_14,
  output [7:0] out_15,
  output [7:0] out_16,
  output [7:0] out_17,
  output [7:0] out_18,
  output [7:0] out_19,
  output [7:0] out_20,
  output [7:0] out_21,
  output [7:0] out_22,
  output [7:0] out_23,
  output [7:0] out_24,
  output [7:0] out_25,
  output [7:0] out_26,
  output [7:0] out_27,
  output [7:0] out_28,
  output [7:0] out_29,
  output [7:0] out_30,
  output [7:0] out_31,
  output [7:0] out_32,
  output [7:0] out_33,
  output [7:0] out_34,
  output [7:0] out_35,
  output [7:0] out_36,
  output [7:0] out_37,
  output [7:0] out_38,
  output [7:0] out_39,
  output [7:0] out_40,
  output Reset_2,
  output Update_Screen
);

  wire buffer_1_out, buffer_2_out, counter_1_carry, decoder_1_out0, decoder_1_out1, decoder_1_out2,
       decoder_1_out3, decoder_1_out4, decoder_1_out5, decoder_1_out6, decoder_1_out7, decoder_1_out8,
       decoder_1_out9, decoder_1_out10, decoder_1_out11, decoder_1_out12, decoder_1_out13, decoder_1_out14,
       decoder_1_out15, decoder_1_out16, decoder_1_out17, decoder_1_out18, decoder_1_out19, decoder_1_out20,
       decoder_1_out21, decoder_1_out22, decoder_1_out23, decoder_1_out24, decoder_1_out25, decoder_1_out26,
       decoder_1_out27, decoder_1_out28, decoder_1_out29, decoder_1_out30, decoder_1_out31, not_1_out,
       or_3_out, pull_resistor_4_node, register_1_q, transistor_3_out, transistor_5_out;
  wire [7:0] bit_extender_1_out, or_2_out, pull_resistor_1_node, pull_resistor_3_node;

  Counter #(.width(5), .max('h17), .trigger("falling")) counter_1 (
    .count(register_1_q), .Q(Column_Screen_Selector), .carry(counter_1_carry), .clk(Clock), .clr(Reset_2));  // open: load, D
  Pull_Resistor #(.pull(1)) pull_resistor_1 (.node(pull_resistor_1_node));
  buf buffer_1 (buffer_1_out, counter_1_carry);
  Pull_Resistor pull_resistor_2 (.node(Update_Screen));
  Transistor #(.gate("br")) transistor_1 (.in(counter_1_carry), .out(Update_Screen), .gate(buffer_1_out));
  assign bit_extender_1_out = {{3{1'b0}}, Column_Screen_Selector};  // Bit_Extender bit_extender_1
  or or_1 (Reset_2, Reset, not_1_out);
  not not_1 (not_1_out, Power);
  Pull_Resistor pull_resistor_3 (.node(pull_resistor_3_node));
  Transistor #(.width(8)) transistor_2 (.in(pull_resistor_1_node), .out(pull_resistor_3_node), .gate(Power));
  buf buffer_2 (buffer_2_out, Power);
  assign or_2_out = bit_extender_1_out | pull_resistor_3_node;  // OR_Gate or_2, 8 bits wide
  Register #(.width(1), .trigger("high")) register_1 (
    .D(or_3_out), .Q(register_1_q), .clk(or_3_out), .clr(pull_resistor_4_node));  // open: en
  Transistor transistor_3 (.in(Power), .out(transistor_3_out), .gate(buffer_2_out));
  Pull_Resistor pull_resistor_4 (.node(pull_resistor_4_node));
  Transistor #(.gate("br")) transistor_4 (.in(counter_1_carry), .out(pull_resistor_4_node), .gate(or_3_out));
  or or_3 (or_3_out, transistor_3_out, transistor_5_out);
  Pull_Resistor pull_resistor_5 (.node(transistor_3_out));
  Transistor #(.\type ("n"), .gate("br")) transistor_5 (
    .in(Clock), .out(transistor_5_out), .gate(Done_with_this_pixel));
  Pull_Resistor pull_resistor_6 (.node(transistor_5_out));
  Decoder #(.select(5), .disabled(0)) decoder_1 (
    .out0(decoder_1_out0), .out1(decoder_1_out1), .out2(decoder_1_out2), .out3(decoder_1_out3),
    .out4(decoder_1_out4), .out5(decoder_1_out5), .out6(decoder_1_out6), .out7(decoder_1_out7),
    .out8(decoder_1_out8), .out9(decoder_1_out9), .out10(decoder_1_out10), .out11(decoder_1_out11),
    .out12(decoder_1_out12), .out13(decoder_1_out13), .out14(decoder_1_out14), .out15(decoder_1_out15),
    .out16(decoder_1_out16), .out17(decoder_1_out17), .out18(decoder_1_out18), .out19(decoder_1_out19),
    .out20(decoder_1_out20), .out21(decoder_1_out21), .out22(decoder_1_out22), .out23(decoder_1_out23),
    .out24(decoder_1_out24), .out25(decoder_1_out25), .out26(decoder_1_out26), .out27(decoder_1_out27),
    .out28(decoder_1_out28), .out29(decoder_1_out29), .out30(decoder_1_out30), .out31(decoder_1_out31),
    .sel(Column_Selector), .en(transistor_5_out));
  // RAM ram_1: pin names not known; wires that end beside it: Row_Selector, decoder_1_out0, Reset, out_9, Row_Selector
  // RAM ram_2: pin names not known; wires that end beside it: decoder_1_out1, Reset, out_10, Row_Selector
  // RAM ram_3: pin names not known; wires that end beside it: decoder_1_out2, Reset, out_11, Row_Selector
  // RAM ram_4: pin names not known; wires that end beside it: decoder_1_out3, Reset, out_12, Row_Selector
  // RAM ram_5: pin names not known; wires that end beside it: decoder_1_out4, Reset, out_13, Row_Selector
  // RAM ram_6: pin names not known; wires that end beside it: decoder_1_out5, Reset, out_14, Row_Selector
  // RAM ram_7: pin names not known; wires that end beside it: decoder_1_out6, Reset, out_15, Row_Selector
  // RAM ram_8: pin names not known; wires that end beside it: decoder_1_out7, Reset, out_16, Row_Selector
  // RAM ram_9: pin names not known; wires that end beside it: decoder_1_out8, Reset, out_17, Row_Selector
  // RAM ram_10: pin names not known; wires that end beside it: decoder_1_out9, Reset, out_18, Row_Selector
  // RAM ram_11: pin names not known; wires that end beside it: decoder_1_out10, Reset, out_19, Row_Selector
  // RAM ram_12: pin names not known; wires that end beside it: decoder_1_out11, Reset, out_20, Row_Selector
  // RAM ram_13: pin names not known; wires that end beside it: decoder_1_out12, Reset, out_21, Row_Selector
  // RAM ram_14: pin names not known; wires that end beside it: decoder_1_out13, Reset, out_22, Row_Selector
  // RAM ram_15: pin names not known; wires that end beside it: decoder_1_out14, Reset, out_23, Row_Selector
  // RAM ram_16: pin names not known; wires that end beside it: decoder_1_out15, Reset, out_24, Row_Selector
  // RAM ram_17: pin names not known; wires that end beside it: decoder_1_out16, Reset, out_25, Row_Selector
  // RAM ram_18: pin names not known; wires that end beside it: decoder_1_out17, Reset, out_26, Row_Selector
  // RAM ram_19: pin names not known; wires that end beside it: decoder_1_out18, Reset, out_27, Row_Selector
  // RAM ram_20: pin names not known; wires that end beside it: decoder_1_out19, Reset, out_28, Row_Selector
  // RAM ram_21: pin names not known; wires that end beside it: decoder_1_out20, Reset, out_29, Row_Selector
  // RAM ram_22: pin names not known; wires that end beside it: decoder_1_out21, Reset, out_30, Row_Selector
  // RAM ram_23: pin names not known; wires that end beside it: decoder_1_out22, Reset, out_31, Row_Selector
  // RAM ram_24: pin names not known; wires that end beside it: decoder_1_out23, Reset, out_32, Row_Selector
  // RAM ram_25: pin names not known; wires that end beside it: decoder_1_out24, Reset, out_33, Row_Selector
  // RAM ram_26: pin names not known; wires that end beside it: decoder_1_out25, Reset, out_34, Row_Selector
  // RAM ram_27: pin names not known; wires that end beside it: decoder_1_out26, Reset, out_35, Row_Selector
  // RAM ram_28: pin names not known; wires that end beside it: decoder_1_out27, Reset, out_36, Row_Selector
  // RAM ram_29: pin names not known; wires that end beside it: decoder_1_out28, Reset, out_37, Row_Selector
  // RAM ram_30: pin names not known; wires that end beside it: decoder_1_out29, Reset, out_38, Row_Selector
  // RAM ram_31: pin names not known; wires that end beside it: decoder_1_out30, Reset, out_39, Row_Selector, Pixel_Color
  // RAM ram_32: pin names not known; wires that end beside it: decoder_1_out31, Reset, out_40, Row_Selector, or_2_out

  // Notes on the sheet:
  //   That one is to load the Mario on load
  //   But won't have an use on future.
  //   This above is to avoid some visual bugs
endmodule

module Calculator (
  input  [15:0] in_1,
  input  [17:0] in_2,
  output [13:0] out_3
);

  wire _0_out, _1_out, _2_out, _3_out, _4_out, _5_out, _6_out, _7_out, _8_out, _9_out, add3_1_u, add3_1_y,
       add3_1_z, add3_2_u, add3_2_x, add3_2_y, add3_2_z, add3_3_u, add3_3_x, add3_3_y, add3_3_z, add3_4_u,
       add3_4_x, add3_4_y, add3_4_z, add3_5_u, add3_5_y, add3_5_z, add3_6_u, add3_6_x, add3_6_y, add3_6_z,
       add3_7_u, add3_7_x, add3_7_y, add3_7_z, add3_8_u, add3_8_x, add3_8_y, add3_8_z, add3_9_u, add3_9_x,
       add3_9_y, add3_9_z, add3_10_u, add3_10_x, add3_10_y, add3_10_z, add3_11_u, add3_11_x, add3_11_y,
       add3_11_z, add3_12_u, add3_12_x, add3_12_y, add3_12_z, add3_13_u, add3_13_x, add3_13_y, add3_13_z,
       add3_14_u, add3_14_x, add3_14_y, add3_14_z, add3_15_u, add3_15_x, add3_15_y, add3_15_z, add3_16_u,
       add3_16_x, add3_16_y, add3_16_z, add3_17_u, add3_17_x, add3_17_y, add3_17_z, add3_18_u, add3_18_y,
       add3_18_z, add3_19_u, add3_19_x, add3_19_y, add3_19_z, add3_20_u, add3_20_x, add3_20_y, add3_20_z,
       add3_21_u, add3_21_x, add3_21_y, add3_21_z, add3_22_u, add3_22_x, add3_22_y, add3_22_z, add3_23_u,
       add3_23_x, add3_23_y, add3_23_z, add3_24_u, add3_24_x, add3_24_y, add3_24_z, add3_25_u, add3_25_x,
       add3_25_y, add3_25_z, add3_28_u, add3_28_x, add3_28_y, add3_28_z, add3_29_u, add3_29_x, add3_29_y,
       add3_29_z, add3_30_u, add3_30_x, add3_30_y, add3_30_z, add3_31_u, add3_31_x, add3_31_y, add3_31_z,
       add3_32_u, add3_32_x, add3_32_y, add3_32_z, add3_33_u, add3_33_x, add3_33_y, add3_33_z, add3_34_u,
       add3_34_x, add3_34_y, add3_34_z, add3_35_u, add3_35_x, add3_35_y, add3_35_z, add3_36_u, add3_36_x,
       add3_36_y, add3_36_z, add3_37_u, add3_37_x, add3_37_y, add3_37_z, add3_38_u, add3_38_x, add3_38_y,
       add3_38_z, add3_39_u, add3_39_x, add3_39_y, add3_39_z, button_2_out, button_3_out, button_4_out,
       button_out, clock_1_out, comparator_1_gt, comparator_2_lt, comparator_3_gt, new_out, not_1_out,
       Op_out, or_1_out, pull_resistor_3_node, RST_out;
  wire [3:0] add3_27_x, add3_40_x, add3_41_x, add3_42_x;
  wire [3:1] add3_42_u;
  wire [17:0] _1_2_out, adder_1_out, adder_2_out, counter_1_q, Current_number_q, demultiplexer_1_out1,
       multiplier_1_out, negator_1_out, Saved_Number_q, undriven, undriven_2;

  _7_Segment_Display u_7_segment_display_1 (.g(comparator_2_lt));  // open: f, a, b, e, d, c, dp
  Hex_Digit_Display hex_digit_display_1 (.value(add3_27_x));  // open: dp
  // Probe on out_3
  Pull_Resistor #(.pull(1)) pull_resistor_1 (.node(out_3));
  Hex_Digit_Display hex_digit_display_2 (.value(add3_41_x));  // open: dp
  Hex_Digit_Display hex_digit_display_3 (.value(add3_40_x));  // open: dp
  Button _2 (.out(_2_out));
  Button _1 (.out(_1_out));
  Button _3 (.out(_3_out));
  Button _4 (.out(_4_out));
  Button _6 (.out(_6_out));
  Button _5 (.out(_5_out));
  Button _7 (.out(_7_out));
  Button _9 (.out(_9_out));
  Button _8 (.out(_8_out));
  Button _0 (.out(_0_out));
  Button button (.out(button_out));
  Button button_2 (.out(button_2_out));
  Button button_3 (.out(button_3_out));
  Button RST (.out(RST_out));
  // Probe on counter_1_q
  RAM #(.addrWidth(18), .dataWidth(20), .bus("separate")) ram_1 (
    .addr(counter_1_q), .din({add3_27_x, add3_41_x, add3_40_x, add3_42_x, add3_42_u, counter_1_q[0]}),
    .clk(clock_1_out));  // open: data, str, sel, ld, clr
  RAM #(.addrWidth(18), .dataWidth(20), .bus("separate")) ram_2 ();  // open: addr, din, data, str, sel, clk, ld, clr
  Hex_Digit_Display hex_digit_display_4 (.value(add3_42_x));  // open: dp
  Hex_Digit_Display hex_digit_display_5 (.value({add3_42_u, counter_1_q[0]}));  // open: dp
  not not_1 (not_1_out, comparator_1_gt);
  Clock clock_1 (.out(clock_1_out));
  or \new  (new_out, _1_out, _3_out, _2_out, _4_out, _6_out, _5_out, _7_out, _9_out, _8_out, _0_out);
  or Op (Op_out, button_3_out, button_out, button_2_out);
  Counter #(.width(18), .max('h3ffff), .ongoal("stay")) counter_1 (
    .count(not_1_out), .Q(counter_1_q), .clk(clock_1_out), .clr(button_4_out));  // open: load, D, carry
  Button button_4 (.out(button_4_out));
  or _1_2 (_1_2_out[0], _1_out, _3_out, _9_out, _7_out, _5_out);
  or _2_2 (_1_2_out[1], _3_out, _2_out, _6_out, _7_out);
  or _4_2 (_1_2_out[2], _5_out, _6_out, _7_out, _4_out);
  or _8_2 (_1_2_out[3], _9_out, _8_out);
  or or_1 (or_1_out, Op_out, RST_out);
  Pull_Resistor pull_resistor_2 (.node(_1_2_out));
  Pull_Resistor pull_resistor_3 (.node(pull_resistor_3_node));
  Transistor transistor_1 (.in(new_out), .out(pull_resistor_3_node), .gate(comparator_3_gt));
  Comparator #(.width(18), .mode("unsigned")) comparator_1 (
    .a(counter_1_q), .b(in_2), .gt(comparator_1_gt));  // open: eq, lt
  // Probe on in_2
  Register #(.width(18)) Saved_Number (
    .D(Current_number_q), .Q(Saved_Number_q), .clk(Op_out), .clr(RST_out));  // open: en
  Register #(.width(18), .trigger("falling")) Current_number (
    .D(adder_1_out), .Q(Current_number_q), .clk(pull_resistor_3_node), .clr(or_1_out));  // open: en
  Multiplier #(.width(18)) multiplier_1 (.a(Current_number_q), .b(18'ha), .out(multiplier_1_out));  // open: cin, cout
  // Probe on adder_1_out
  Adder #(.width(18)) adder_1 (.a(multiplier_1_out), .b(_1_2_out), .out(adder_1_out));  // open: cin, cout
  // Probe on Current_number_q
  add3 add3_1 (.c(counter_1_q[17]), .d(counter_1_q[16]), .y(add3_1_y), .z(add3_1_z), .u(add3_1_u));  // open: a, b, x
  add3 add3_2 (
    .a(add3_1_y), .b(add3_1_z), .c(add3_1_u), .d(counter_1_q[15]), .x(add3_2_x), .y(add3_2_y), .z(add3_2_z),
    .u(add3_2_u));
  add3 add3_3 (
    .a(add3_2_y), .b(add3_2_z), .c(add3_2_u), .d(counter_1_q[14]), .x(add3_3_x), .y(add3_3_y), .z(add3_3_z),
    .u(add3_3_u));
  add3 add3_4 (
    .a(add3_3_y), .b(add3_3_z), .c(add3_3_u), .d(counter_1_q[13]), .x(add3_4_x), .y(add3_4_y), .z(add3_4_z),
    .u(add3_4_u));
  add3 add3_5 (.b(add3_2_x), .c(add3_3_x), .d(add3_4_x), .y(add3_5_y), .z(add3_5_z), .u(add3_5_u));  // open: a, x
  add3 add3_6 (
    .a(add3_4_y), .b(add3_4_z), .c(add3_4_u), .d(counter_1_q[12]), .x(add3_6_x), .y(add3_6_y), .z(add3_6_z),
    .u(add3_6_u));
  add3 add3_7 (
    .a(add3_5_y), .b(add3_5_z), .c(add3_5_u), .d(add3_6_x), .x(add3_7_x), .y(add3_7_y), .z(add3_7_z),
    .u(add3_7_u));
  add3 add3_8 (
    .a(add3_6_y), .b(add3_6_z), .c(add3_6_u), .d(counter_1_q[11]), .x(add3_8_x), .y(add3_8_y), .z(add3_8_z),
    .u(add3_8_u));
  add3 add3_9 (
    .a(add3_7_y), .b(add3_7_z), .c(add3_7_u), .d(add3_8_x), .x(add3_9_x), .y(add3_9_y), .z(add3_9_z),
    .u(add3_9_u));
  add3 add3_10 (
    .a(add3_8_y), .b(add3_8_z), .c(add3_8_u), .d(counter_1_q[10]), .x(add3_10_x), .y(add3_10_y),
    .z(add3_10_z), .u(add3_10_u));
  add3 add3_11 (
    .a(add3_9_y), .b(add3_9_z), .c(add3_9_u), .d(add3_10_x), .x(add3_11_x), .y(add3_11_y), .z(add3_11_z),
    .u(add3_11_u));
  add3 add3_12 (
    .a(add3_11_y), .b(add3_11_z), .c(add3_11_u), .d(add3_28_x), .x(add3_12_x), .y(add3_12_y), .z(add3_12_z),
    .u(add3_12_u));
  add3 add3_13 (
    .b(add3_7_x), .c(add3_9_x), .d(add3_11_x), .x(add3_13_x), .y(add3_13_y), .z(add3_13_z), .u(add3_13_u));  // open: a
  add3 add3_14 (
    .a(add3_13_y), .b(add3_13_z), .c(add3_13_u), .d(add3_12_x), .x(add3_14_x), .y(add3_14_y), .z(add3_14_z),
    .u(add3_14_u));
  add3 add3_15 (
    .a(add3_12_y), .b(add3_12_z), .c(add3_12_u), .d(add3_29_x), .x(add3_15_x), .y(add3_15_y), .z(add3_15_z),
    .u(add3_15_u));
  add3 add3_16 (
    .a(add3_15_y), .b(add3_15_z), .c(add3_15_u), .d(add3_30_x), .x(add3_16_x), .y(add3_16_y), .z(add3_16_z),
    .u(add3_16_u));
  add3 add3_17 (
    .a(add3_14_y), .b(add3_14_z), .c(add3_14_u), .d(add3_15_x), .x(add3_17_x), .y(add3_17_y), .z(add3_17_z),
    .u(add3_17_u));
  add3 add3_18 (
    .b(add3_13_x), .c(add3_14_x), .d(add3_17_x), .y(add3_18_y), .z(add3_18_z), .u(add3_18_u));  // open: a, x
  add3 add3_19 (
    .a(add3_17_y), .b(add3_17_z), .c(add3_17_u), .d(add3_16_x), .x(add3_19_x), .y(add3_19_y), .z(add3_19_z),
    .u(add3_19_u));
  add3 add3_20 (
    .a(add3_19_y), .b(add3_19_z), .c(add3_19_u), .d(add3_33_x), .x(add3_20_x), .y(add3_20_y), .z(add3_20_z),
    .u(add3_20_u));
  add3 add3_21 (
    .a(add3_18_y), .b(add3_18_z), .c(add3_18_u), .d(add3_19_x), .x(add3_21_x), .y(add3_21_y), .z(add3_21_z),
    .u(add3_21_u));
  add3 add3_22 (
    .a(add3_20_y), .b(add3_20_z), .c(add3_20_u), .d(add3_34_x), .x(add3_22_x), .y(add3_22_y), .z(add3_22_z),
    .u(add3_22_u));
  add3 add3_23 (
    .a(add3_21_y), .b(add3_21_z), .c(add3_21_u), .d(add3_20_x), .x(add3_23_x), .y(add3_23_y), .z(add3_23_z),
    .u(add3_23_u));
  add3 add3_24 (
    .a(add3_23_y), .b(add3_23_z), .c(add3_23_u), .d(add3_22_x), .x(add3_24_x), .y(add3_24_y), .z(add3_24_z),
    .u(add3_24_u));
  add3 add3_25 (
    .a(add3_22_y), .b(add3_22_z), .c(add3_22_u), .d(add3_36_x), .x(add3_25_x), .y(add3_25_y), .z(add3_25_z),
    .u(add3_25_u));
  add3 add3_26 (
    .b(add3_21_x), .c(add3_23_x), .d(add3_24_x), .y(add3_27_x[3]), .z(add3_27_x[2]), .u(add3_27_x[1]));  // open: a, x
  add3 add3_27 (
    .a(add3_24_y), .b(add3_24_z), .c(add3_24_u), .d(add3_25_x), .x(add3_27_x[0]), .y(add3_41_x[3]),
    .z(add3_41_x[2]), .u(add3_41_x[1]));
  Adder #(.width(18)) adder_2 (.a(undriven), .b(undriven_2), .out(adder_2_out));  // open: cin, cout
  Demultiplexer #(.width(18), .enable("false")) demultiplexer_1 (
    .out0(adder_2_out), .out1(demultiplexer_1_out1));  // open: in, sel
  Subtractor #(.width(18)) subtractor_1 (.a(undriven), .b(undriven_2), .out(demultiplexer_1_out1));  // open: bin, bout
  Negator #(.width(18)) negator_1 (.in(Current_number_q), .out(negator_1_out));
  Comparator #(.width(18)) comparator_2 (.a(Current_number_q), .b({18{1'b0}}), .lt(comparator_2_lt));  // open: gt, eq
  Comparator #(.width(18), .mode("unsigned")) comparator_3 (
    .a(Current_number_q), .b(18'h270f), .gt(comparator_3_gt));  // open: eq, lt
  Multiplexer #(.width(18), .disabled(0), .enable("false")) multiplexer_1 (
    .in0(Current_number_q), .in1(negator_1_out), .sel(comparator_2_lt));  // open: out
  add3 add3_28 (
    .a(add3_10_y), .b(add3_10_z), .c(add3_10_u), .d(counter_1_q[9]), .x(add3_28_x), .y(add3_28_y),
    .z(add3_28_z), .u(add3_28_u));
  add3 add3_29 (
    .a(add3_28_y), .b(add3_28_z), .c(add3_28_u), .d(counter_1_q[8]), .x(add3_29_x), .y(add3_29_y),
    .z(add3_29_z), .u(add3_29_u));
  add3 add3_30 (
    .a(add3_29_y), .b(add3_29_z), .c(add3_29_u), .d(counter_1_q[7]), .x(add3_30_x), .y(add3_30_y),
    .z(add3_30_z), .u(add3_30_u));
  add3 add3_31 (
    .a(add3_30_y), .b(add3_30_z), .c(add3_30_u), .d(counter_1_q[6]), .x(add3_31_x), .y(add3_31_y),
    .z(add3_31_z), .u(add3_31_u));
  add3 add3_32 (
    .a(add3_31_y), .b(add3_31_z), .c(add3_31_u), .d(counter_1_q[5]), .x(add3_32_x), .y(add3_32_y),
    .z(add3_32_z), .u(add3_32_u));
  add3 add3_33 (
    .a(add3_16_y), .b(add3_16_z), .c(add3_16_u), .d(add3_31_x), .x(add3_33_x), .y(add3_33_y), .z(add3_33_z),
    .u(add3_33_u));
  add3 add3_34 (
    .a(add3_33_y), .b(add3_33_z), .c(add3_33_u), .d(add3_32_x), .x(add3_34_x), .y(add3_34_y), .z(add3_34_z),
    .u(add3_34_u));
  add3 add3_35 (
    .a(add3_32_y), .b(add3_32_z), .c(add3_32_u), .d(counter_1_q[4]), .x(add3_35_x), .y(add3_35_y),
    .z(add3_35_z), .u(add3_35_u));
  add3 add3_36 (
    .a(add3_34_y), .b(add3_34_z), .c(add3_34_u), .d(add3_35_x), .x(add3_36_x), .y(add3_36_y), .z(add3_36_z),
    .u(add3_36_u));
  add3 add3_37 (
    .a(add3_35_y), .b(add3_35_z), .c(add3_35_u), .d(counter_1_q[3]), .x(add3_37_x), .y(add3_37_y),
    .z(add3_37_z), .u(add3_37_u));
  add3 add3_38 (
    .a(add3_37_y), .b(add3_37_z), .c(add3_37_u), .d(counter_1_q[2]), .x(add3_38_x), .y(add3_38_y),
    .z(add3_38_z), .u(add3_38_u));
  add3 add3_39 (
    .a(add3_36_y), .b(add3_36_z), .c(add3_36_u), .d(add3_37_x), .x(add3_39_x), .y(add3_39_y), .z(add3_39_z),
    .u(add3_39_u));
  add3 add3_40 (
    .a(add3_39_y), .b(add3_39_z), .c(add3_39_u), .d(add3_38_x), .x(add3_40_x[0]), .y(add3_42_x[3]),
    .z(add3_42_x[2]), .u(add3_42_x[1]));
  add3 add3_41 (
    .a(add3_25_y), .b(add3_25_z), .c(add3_25_u), .d(add3_39_x), .x(add3_41_x[0]), .y(add3_40_x[3]),
    .z(add3_40_x[2]), .u(add3_40_x[1]));
  Register #(.width(16)) Current_number_2 ();  // open: D, en, Q, clk, clr
  add3 add3_42 (
    .a(add3_38_y), .b(add3_38_z), .c(add3_38_u), .d(counter_1_q[1]), .x(add3_42_x[0]), .y(add3_42_u[3]),
    .z(add3_42_u[2]), .u(add3_42_u[1]));

  // Notes on the sheet:
  //   (<0)
endmodule

module add3 (
  input  a,
  input  b,
  input  c,
  input  d,
  output x,
  output y,
  output z,
  output u
);

  wire and_1_out, and_2_out, and_3_out, and_4_out, and_5_out, and_6_out, and_7_out, and_8_out, and_9_out,
       and_10_out, not_1_out, not_2_out, not_3_out, not_4_out, not_5_out, not_6_out, not_7_out, not_8_out,
       not_9_out, not_10_out;

  and and_1 (and_1_out, b, d);
  and and_2 (and_2_out, b, c);
  and and_3 (and_3_out, b, not_1_out, not_2_out);
  not not_1 (not_1_out, c);
  not not_2 (not_2_out, d);
  and and_4 (and_4_out, a, d);
  not not_3 (not_3_out, a);
  not not_4 (not_4_out, b);
  and and_5 (and_5_out, not_3_out, not_4_out, c);
  and and_6 (and_6_out, c, d);
  not not_5 (not_5_out, c);
  and and_7 (and_7_out, a, not_5_out, not_6_out);
  not not_6 (not_6_out, d);
  not not_7 (not_7_out, a);
  not not_8 (not_8_out, b);
  and and_8 (and_8_out, not_7_out, not_8_out, d);
  and and_9 (and_9_out, b, c, not_9_out);
  not not_9 (not_9_out, d);
  and and_10 (and_10_out, a, not_10_out);
  not not_10 (not_10_out, d);
  or or_1 (x, and_1_out, and_2_out, a);
  or or_2 (y, and_3_out, and_4_out);
  or or_3 (z, and_5_out, and_6_out, and_7_out);
  or or_4 (u, and_8_out, and_9_out, and_10_out);
endmodule
