// Logisim project LogiwinCore.circ as structural Verilog: 11 circuits, main circuit Logiwin
module Logiwin (
  input  [13:0] in_1,
  input  [31:0] in_2
);

  wire clock_1_out, cpu_external_connections_1_p6, not_1_out, undriven_2, undriven_4, undriven_5;
  wire [1:0] cpu_external_connections_1_p4;
  wire [4:0] gpu_1_rowdebug;
  wire [6:0] cpu_external_connections_1_p5, keyboard_1_data;
  wire [13:0] undriven;
  wire [23:0] cpu_external_connections_1_p3;
  wire [31:0] gpu_1_out_9, gpu_1_out_10, gpu_1_out_11, gpu_1_out_12, gpu_1_out_13, gpu_1_out_14,
       gpu_1_out_15, gpu_1_out_16, gpu_1_out_17, gpu_1_out_18, gpu_1_out_19, gpu_1_out_20, gpu_1_out_22,
       gpu_1_out_23, gpu_1_out_24, gpu_1_out_25, gpu_1_out_26, gpu_1_out_27, gpu_1_out_28, gpu_1_out_29,
       gpu_1_out_30, gpu_1_out_31, gpu_1_out_32, gpu_1_out_33, ram_1_data, transistor_1_out, undriven_3;

  Clock clock_1 (.out(clock_1_out));
  // Probe on in_1
  GPU gpu_1 (
    .DataIn(undriven_3), .Clock(clock_1_out), .Reset(undriven_4), .out_9(gpu_1_out_9), .out_10(gpu_1_out_10),
    .out_11(gpu_1_out_11), .out_12(gpu_1_out_12), .out_13(gpu_1_out_13), .out_14(gpu_1_out_14),
    .out_15(gpu_1_out_15), .out_16(gpu_1_out_16), .out_17(gpu_1_out_17), .out_18(gpu_1_out_18),
    .out_19(gpu_1_out_19), .RowDebug(gpu_1_rowdebug), .out_20(gpu_1_out_20), .out_22(gpu_1_out_22),
    .out_23(gpu_1_out_23), .out_24(gpu_1_out_24), .out_25(gpu_1_out_25), .out_26(gpu_1_out_26),
    .out_27(gpu_1_out_27), .out_28(gpu_1_out_28), .out_29(gpu_1_out_29), .out_30(gpu_1_out_30),
    .out_31(gpu_1_out_31), .out_32(gpu_1_out_32), .out_33(gpu_1_out_33), .RowSpecEnable(undriven_2),
    .Decrementar(undriven_5), .VSync___Actual_Logisim_Clock(in_1), .VSync___Max_FPS(undriven));  // open: RowIn
  Transistor #(.gate("br"), .width(32)) transistor_1 (.in(ram_1_data), .out(transistor_1_out), .gate(not_1_out));
  RAM_part #(.addrWidth(24), .dataWidth(32), .bus("asynch")) ram_1 (
    .addr(cpu_external_connections_1_p3), .data(ram_1_data), .ld(not_1_out),
    .clr(cpu_external_connections_1_p4[1]));  // open: sel
  not not_1 (not_1_out, cpu_external_connections_1_p4[0]);
  DotMatrix #(.inputtype("row"), .matrixcols(32), .matrixrows(24)) dotmatrix_1 (
    .row0(gpu_1_out_9), .row1(gpu_1_out_10), .row2(gpu_1_out_11), .row3(gpu_1_out_12), .row4(gpu_1_out_13),
    .row5(gpu_1_out_14), .row6(gpu_1_out_15), .row7(gpu_1_out_16), .row8(gpu_1_out_17), .row9(gpu_1_out_18),
    .row10(gpu_1_out_19), .row11(gpu_1_out_20), .row12(gpu_1_out_22), .row13(gpu_1_out_23),
    .row14(gpu_1_out_24), .row15(gpu_1_out_25), .row16(gpu_1_out_26), .row17(gpu_1_out_27),
    .row18(gpu_1_out_28), .row19(gpu_1_out_29), .row20(gpu_1_out_30), .row21(gpu_1_out_31),
    .row22(gpu_1_out_32), .row23(gpu_1_out_33));
  TTY #(.rows(5), .cols(44)) tty_1 (
    .data(cpu_external_connections_1_p5), .clk(clock_1_out), .clr(cpu_external_connections_1_p6));  // open: we
  Keyboard #(.buflen(40)) keyboard_1 (.clk(clock_1_out), .data(keyboard_1_data));  // open: re, clr, avail
  // CPU___External_Connections cpu_external_connections_1: pin names not known; wires that end beside it: transistor_1_out, ram_1_data, cpu_external_connections_1_p3, cpu_external_connections_1_p4, cpu_external_connections_1_p5, cpu_external_connections_1_p6, keyboard_1_data
  // Probe on keyboard_1_data
endmodule

module CPU___External_Connections (
  input  [6:0] Keyboard,
  input  [31:0] in_2,
  input  [31:0] MEMRISTOR_Value_Out,
  output [6:0] Console_Screen,
  output Console_Clear,
  output [31:0] MEMRISTOR_Value_In,
  output [21:0] MEMRISTOR_Adress,
  output [21:0] GPU_Adress,
  output [1:0] HDD_Selector__Load__Reset
);

  Pull_Resistor pull_resistor_1 (.node(Console_Screen));
  // CPU___Core_And_Bus cpu_core_and_bus_1: pin names not known; wires that end beside it: in_2, MEMRISTOR_Value_In, MEMRISTOR_Value_Out, GPU_Adress, HDD_Selector__Load__Reset, Console_Screen, Console_Clear, Keyboard
  Pull_Resistor pull_resistor_2 (.node(Console_Clear));
endmodule

module CPU___Core_And_Bus (
  input  [6:0] Keyboard_7_bit,
  input  [31:0] Data_In__DEBUG,
  input  [23:0] MEMRISTOR_Value_Out,
  output Console_Clear,
  output [6:0] Console_7_bit,
  output [31:0] MESMRISTOR_Value_In,
  output [23:0] MEMRISTOR_Adress,
  output [1:0] HDD_Selector
);

  wire bitfinder_1_found, Carry_Flag_q, cpu_alu_1_carry_flag, not_1_out, or_2_out, transistor_2_out,
       transistor_3_out;
  wire [1:0] cpu_instructions_1_accumulator_out_selector, cpu_instructions_1_adress_data_dest_selector,
       cpu_instructions_1_adress_out_1_2, pull_resistor_2_node;
  wire [2:0] Comparation_Flag_q, cpu_alu_1_out_5, cpu_instructions_1_data_out_selector;
  wire [3:0] cpu_instructions_1_alu_selector;
  wire [3:3] cpu_alu_1_out_5_2;
  wire [7:0] cpu_instructions_1_shift__rotator_data;
  wire [21:0] cpu_instructions_1_adress_out_1, demultiplexer_1_out0;
  wire [31:0] Accumulator_q, cpu_alu_1_out, cpu_instructions_1_data_out_1,
       cpu_shifter_rotator_1_accumulator_out, demultiplexer_2_out2, demultiplexer_2_out3,
       demultiplexer_3_out1, demultiplexer_4_out1, demultiplexer_4_out2, demultiplexer_4_out3,
       demultiplexer_4_out4, or_1_out, or_3_out, or_4_out, ram_1_data, transistor_1_out;

  Clock clock_1 ();  // open: out
  // Probe on MEMRISTOR_Value_Out
  // Probe on MEMRISTOR_Value_Out
  Pull_Resistor pull_resistor_1 (.node(MEMRISTOR_Value_Out));
  Pull_Resistor pull_resistor_2 (.node(pull_resistor_2_node));
  RAM_part #(.addrWidth(22), .dataWidth(32), .bus("asynch")) ram_1 (
    .addr(demultiplexer_1_out0), .data(ram_1_data), .ld(not_1_out), .clr(pull_resistor_2_node[1]));  // open: sel
  not not_1 (not_1_out, pull_resistor_2_node[0]);
  // Probe on demultiplexer_4_out2
  Transistor #(.\type ("n"), .width(32)) transistor_1 (.in(ram_1_data), .out(transistor_1_out), .gate(not_1_out));
  Demultiplexer #(.select(2), .width(22), .enable("false")) demultiplexer_1 (
    .out0(demultiplexer_1_out0), .in(cpu_instructions_1_adress_out_1), .sel(cpu_instructions_1_adress_out_1_2));  // open: out1, out2, out3
  assign ram_1_data = or_1_out;  // Buffer buffer_1, 32 bits wide
  assign or_1_out = demultiplexer_4_out1 | demultiplexer_3_out1;  // OR_Gate or_1, 32 bits wide
  Demultiplexer #(.select(2), .width(32), .enable("false")) demultiplexer_2 (
    .out2(demultiplexer_2_out2), .out3(demultiplexer_2_out3), .in(transistor_1_out),
    .sel(cpu_instructions_1_adress_data_dest_selector));  // open: out0, out1
  Pull_Resistor pull_resistor_3 (.node(ram_1_data));
  or or_2 (or_2_out, cpu_instructions_1_shift__rotator_data[7], transistor_2_out);
  Demultiplexer #(.select(2), .width(32), .enable("false")) demultiplexer_3 (
    .out1(demultiplexer_3_out1), .in(Accumulator_q), .sel(cpu_instructions_1_accumulator_out_selector));  // open: out0, out2, out3
  Transistor transistor_2 (
    .in(transistor_3_out), .out(transistor_2_out), .gate(cpu_instructions_1_data_out_selector[2]));
  assign or_3_out = demultiplexer_2_out2 | cpu_shifter_rotator_1_accumulator_out | demultiplexer_4_out2 | cpu_alu_1_out;  // OR_Gate or_3, 32 bits wide
  Transistor transistor_3 (
    .in(cpu_instructions_1_data_out_selector[1]), .out(transistor_3_out),
    .gate(cpu_instructions_1_data_out_selector[0]));
  Pull_Resistor pull_resistor_4 (.node(transistor_3_out));
  Demultiplexer #(.select(3), .width(32), .enable("false")) demultiplexer_4 (
    .out1(demultiplexer_4_out1), .out2(demultiplexer_4_out2), .out3(demultiplexer_4_out3),
    .out4(demultiplexer_4_out4), .in(cpu_instructions_1_data_out_1),
    .sel(cpu_instructions_1_data_out_selector));  // open: out0, out5, out6, out7
  Register #(.width(32), .trigger("high")) Accumulator (
    .D(or_3_out), .Q(Accumulator_q), .clk(or_2_out));  // open: en, clr
  assign or_4_out = demultiplexer_4_out3 | demultiplexer_2_out3;  // OR_Gate or_4, 32 bits wide
  CPU___Shifter__Rotator cpu_shifter_rotator_1 (
    .Accumulator_In(Accumulator_q), .Shift__Rotate_Data_Selector(cpu_instructions_1_shift__rotator_data),
    .Accumulator_Out(cpu_shifter_rotator_1_accumulator_out));
  CPU___ALU cpu_alu_1 (
    .A(Accumulator_q), .B(or_4_out), .Seletor(cpu_instructions_1_alu_selector), .Out(cpu_alu_1_out),
    .out_5({cpu_alu_1_out_5_2[3], cpu_alu_1_out_5}), .Carry_Flag(cpu_alu_1_carry_flag));  // open: Carry_Out
  Register #(.width(3), .trigger("high")) Comparation_Flag (
    .D(cpu_alu_1_out_5), .Q(Comparation_Flag_q), .clk(cpu_alu_1_out_5_2[3]));  // open: en, clr
  Register #(.width(1), .trigger("high")) Carry_Flag (
    .D(cpu_alu_1_carry_flag), .Q(Carry_Flag_q), .clk(cpu_alu_1_carry_flag));  // open: en, clr
  CPU___Instructions cpu_instructions_1 (
    .Data_In(Data_In__DEBUG), .Data_Out_1(cpu_instructions_1_data_out_1),
    .Adress_Out_1({cpu_instructions_1_adress_out_1_2, cpu_instructions_1_adress_out_1}),
    .Data_Out_Selector(cpu_instructions_1_data_out_selector),
    .Accumulator_Out_Selector(cpu_instructions_1_accumulator_out_selector),
    .Shift__Rotator_Data(cpu_instructions_1_shift__rotator_data),
    .ADRESS_DATA_DEST_SELECTOR(cpu_instructions_1_adress_data_dest_selector),
    .ADRESS_LOAD_RESET(pull_resistor_2_node), .ALU_Selector(cpu_instructions_1_alu_selector),
    .Accumulator(Accumulator_q), .COMPFLAG(Comparation_Flag_q), .CARRYFLAG(Carry_Flag_q));  // open: Clock
  BitFinder #(.width(7)) bitfinder_1 (.in(Keyboard_7_bit), .found(bitfinder_1_found));  // open: index
  Register #(.width(7), .trigger("low")) register_1 (.D(Keyboard_7_bit), .clk(bitfinder_1_found));  // open: en, Q, clr
  RAM_part #(.addrWidth(24), .dataWidth(7), .bus("separate")) ram_2 ();  // open: addr, din, data, str, sel, clk, ld, clr
  // Probe on nothing

  // Notes on the sheet:
  //   0000 0001 MOV
  //   0000 0010 STO
  //   HDD Load
  //   HDD Reset
  //   buffer_1 drives only 1 and floats otherwise
  //   MEMRISTOR DATA DMX
  //   ACCUMULATOR DATA DMX
  //   Instruction Data DMX
  //   COMPFLAG
  //   CARRYFLAG
endmodule

module CPU___Shifter__Rotator (
  input  [31:0] Accumulator_In,
  input  [7:0] Shift__Rotate_Data_Selector,
  output [31:0] Accumulator_Out
);

  wire bitfinder_1_found, comparator_1_eq, counter_1_q, not_1_out, pull_resistor_1_node, pull_resistor_4_node;
  wire [31:0] multiplexer_1_out, or_1_out, shifter_1_out, shifter_2_out, shifter_3_out, shifter_4_out;

  assign or_1_out = Accumulator_In;  // OR_Gate or_1, 32 bits wide OR_Gate
  Shifter #(.width(32)) shifter_1 (.in(or_1_out), .\dist (Shift__Rotate_Data_Selector[4:0]), .out(shifter_1_out));
  Shifter #(.width(32), .shift("lr")) shifter_2 (
    .in(or_1_out), .\dist (Shift__Rotate_Data_Selector[4:0]), .out(shifter_2_out));
  Shifter #(.width(32), .shift("rl")) shifter_3 (
    .in(or_1_out), .\dist (Shift__Rotate_Data_Selector[4:0]), .out(shifter_3_out));
  Shifter #(.width(32), .shift("rr")) shifter_4 (
    .in(or_1_out), .\dist (Shift__Rotate_Data_Selector[4:0]), .out(shifter_4_out));
  Multiplexer #(.select(2), .width(32)) multiplexer_1 (
    .in0(shifter_1_out), .in1(shifter_2_out), .in2(shifter_3_out), .in3(shifter_4_out),
    .out(multiplexer_1_out), .sel(Shift__Rotate_Data_Selector[6:5]), .en(pull_resistor_1_node));
  Pull_Resistor pull_resistor_1 (.node(pull_resistor_1_node));
  Transistor #(.gate("br")) transistor_1 (
    .in(Shift__Rotate_Data_Selector[7]), .out(pull_resistor_1_node), .gate(comparator_1_eq));
  BitFinder #(.width(32)) bitfinder_1 (.in(multiplexer_1_out), .found(bitfinder_1_found));  // open: index
  Pull_Resistor pull_resistor_2 (.node(multiplexer_1_out));
  Register #(.width(32), .trigger("low")) register_1 (
    .D(multiplexer_1_out), .Q(Accumulator_Out), .clk(pull_resistor_4_node));  // open: en, clr
  Pull_Resistor pull_resistor_3 (.node(Accumulator_Out));
  Counter #(.width(1), .max('h1), .ongoal("stay")) counter_1 (
    .Q(counter_1_q), .clk(bitfinder_1_found), .clr(not_1_out));  // open: load, D, count, carry
  Pull_Resistor pull_resistor_4 (.node(pull_resistor_4_node));
  not not_1 (not_1_out, Shift__Rotate_Data_Selector[7]);
  Comparator #(.width(1), .mode("unsigned")) comparator_1 (
    .a(counter_1_q), .b(1'b1), .eq(comparator_1_eq));  // open: gt, lt
endmodule

module CPU___ALU (
  input  [31:0] A,
  input  [31:0] B,
  input  [3:0] Seletor,
  output Carry_Flag,
  output [3:0] out_5,
  output [31:0] Out,
  output [31:0] Carry_Out
);

  wire adder_1_cout, bitfinder_1_found, comparator_2_eq;
  wire [2:0] comparator_1_lt;
  wire [3:0] bit_extender_2_out;
  wire [31:0] adder_1_out, and_1_out, bit_extender_1_out, divider_1_out, multiplier_1_cout, multiplier_1_out,
       or_1_out, subtractor_1_out;

  assign or_1_out = B;  // OR_Gate or_1, 32 bits wide OR_Gate
  Pull_Resistor pull_resistor_1 (.node(or_1_out));
  Pull_Resistor pull_resistor_2 (.node(Seletor));
  BitFinder #(.width(32)) bitfinder_1 (.in(multiplier_1_cout), .found(bitfinder_1_found));  // open: index
  Adder #(.width(32)) adder_1 (.a(A), .b(or_1_out), .out(adder_1_out), .cout(adder_1_cout));  // open: cin
  Subtractor #(.width(32)) subtractor_1 (.a(A), .b(or_1_out), .out(subtractor_1_out));  // open: bin, bout
  Multiplier #(.width(32)) multiplier_1 (
    .a(A), .b(or_1_out), .out(multiplier_1_out), .cout(multiplier_1_cout));  // open: cin
  Divider #(.width(32)) divider_1 (.a(A), .b(or_1_out), .out(divider_1_out));  // open: upper, rem
  Comparator #(.width(32), .mode("unsigned")) comparator_1 (
    .a(A), .b(or_1_out), .gt(comparator_1_lt[2]), .eq(comparator_1_lt[1]), .lt(comparator_1_lt[0]));
  assign and_1_out = A & or_1_out;  // AND_Gate and_1, 32 bits wide
  assign bit_extender_1_out = {{29{1'b0}}, comparator_1_lt};  // Bit_Extender bit_extender_1
  Multiplexer #(.select(4), .enable("false")) multiplexer_1 (
    .in1(adder_1_cout), .in4(bitfinder_1_found), .out(Carry_Flag), .sel(Seletor));  // open: in0, in2, in3, in5, in6, in7, in8, in9, in10, in11, in12, in13, in14, in15
  Pull_Resistor pull_resistor_3 (.node(Carry_Flag));
  Pull_Resistor pull_resistor_4 (.node(Out));
  Multiplexer #(.select(4), .width(32), .enable("false")) multiplexer_2 (
    .in1(adder_1_out), .in2(subtractor_1_out), .in3(multiplier_1_out), .in4(divider_1_out),
    .in5(bit_extender_1_out), .in6(and_1_out), .out(Out), .sel(Seletor));  // open: in0, in7, in8, in9, in10, in11, in12, in13, in14, in15
  Comparator #(.width(4), .mode("unsigned")) comparator_2 (
    .a(Seletor), .b(4'b0101), .eq(comparator_2_eq));  // open: gt, lt
  Transistor #(.\type ("n"), .width(4)) transistor_1 (.in(bit_extender_2_out), .out(out_5), .gate(comparator_2_eq));
  assign bit_extender_2_out = {{1{1'b1}}, Out[2:0]};  // Bit_Extender bit_extender_2
  Pull_Resistor pull_resistor_5 (.node(out_5));

  // Notes on the sheet:
  //   ALU Selector:
  //   6 = AND
  //   0 = Nothing
  //   1 = ADD, Sum
  //   2 = SUB, Substract
  //   3 = MUL, Multiplication
  //   4 = DIV, Divide
  //   5 = CMP, Compare
endmodule

module CPU___Instructions (
  input  Clock,
  input  [31:0] Data_In,
  input  [31:0] Accumulator,
  input  CARRYFLAG,
  input  [2:0] COMPFLAG,
  output [7:0] Shift__Rotator_Data,
  output [31:0] Data_Out_1,
  output [2:0] Data_Out_Selector,
  output [1:0] Accumulator_Out_Selector,
  output [1:0] ADRESS_DATA_DEST_SELECTOR,
  output [23:0] Adress_Out_1,
  output [1:0] ADRESS_LOAD_RESET,
  output [3:0] ALU_Selector
);

  wire CMP, comparator_1_eq, decoder_no_decd_text_on_mid_1_out_3, decoder_no_decd_text_on_mid_1_out_5,
       decoder_no_decd_text_on_mid_1_out_6, decoder_no_decd_text_on_mid_1_out_7,
       decoder_no_decd_text_on_mid_1_out_8, decoder_no_decd_text_on_mid_1_out_10,
       decoder_no_decd_text_on_mid_1_out_11, decoder_no_decd_text_on_mid_1_out_12,
       decoder_no_decd_text_on_mid_1_out_13, decoder_no_decd_text_on_mid_1_out_14,
       decoder_no_decd_text_on_mid_1_out_15, decoder_no_decd_text_on_mid_1_out_16,
       decoder_no_decd_text_on_mid_1_out_17, decoder_no_decd_text_on_mid_1_out_18,
       decoder_no_decd_text_on_mid_1_out_19, decoder_no_decd_text_on_mid_1_out_20, JUMP, or_1_out, or_2_out,
       or_3_out, or_6_out, pull_resistor_11_node, pull_resistor_13_node, transistor_1_out, transistor_2_out,
       transistor_3_out, transistor_4_out, transistor_5_out, transistor_6_out, transistor_7_out,
       transistor_8_out, transistor_9_out, transistor_14_out, transistor_15_out;
  wire [1:0] pull_resistor_12_node;
  wire [4:0] demultiplexer_1_out0;
  wire [23:0] demultiplexer_2_out1;

  Demultiplexer #(.select(2), .width(5), .enable("false")) demultiplexer_1 (
    .out0(demultiplexer_1_out0), .in(Data_In[28:24]), .sel(Data_In[30:29]));  // open: out1, out2, out3
  Decoder__No_Decd_Text_on_mid decoder_no_decd_text_on_mid_1 (
    .in_1(demultiplexer_1_out0), .out_3(decoder_no_decd_text_on_mid_1_out_3),
    .out_4(Accumulator_Out_Selector[0]), .out_5(decoder_no_decd_text_on_mid_1_out_5),
    .out_6(decoder_no_decd_text_on_mid_1_out_6), .out_7(decoder_no_decd_text_on_mid_1_out_7),
    .out_8(decoder_no_decd_text_on_mid_1_out_8), .out_9(CMP), .out_10(decoder_no_decd_text_on_mid_1_out_10),
    .out_11(decoder_no_decd_text_on_mid_1_out_11), .out_12(decoder_no_decd_text_on_mid_1_out_12),
    .out_13(decoder_no_decd_text_on_mid_1_out_13), .out_14(decoder_no_decd_text_on_mid_1_out_14),
    .out_15(decoder_no_decd_text_on_mid_1_out_15), .out_16(decoder_no_decd_text_on_mid_1_out_16),
    .out_17(decoder_no_decd_text_on_mid_1_out_17), .out_18(decoder_no_decd_text_on_mid_1_out_18),
    .out_19(decoder_no_decd_text_on_mid_1_out_19), .out_20(decoder_no_decd_text_on_mid_1_out_20));  // open: out_2, out_21, out_22, out_23, out_24, out_25, out_26, out_27, out_28, out_29, out_30, out_31, out_32, out_33
  Pull_Resistor pull_resistor_1 (.node(Data_In));
  Transistor #(.\type ("n"), .gate("br")) transistor_1 (
    .in(decoder_no_decd_text_on_mid_1_out_15), .out(transistor_1_out), .gate(COMPFLAG[0]));
  Comparator #(.width(32), .mode("unsigned")) comparator_1 (
    .a(Accumulator), .b({32{1'b0}}), .eq(comparator_1_eq));  // open: gt, lt
  Transistor #(.\type ("n"), .gate("br")) transistor_2 (
    .in(decoder_no_decd_text_on_mid_1_out_16), .out(transistor_2_out), .gate(or_1_out));
  Transistor #(.\type ("n"), .gate("br")) transistor_3 (
    .in(decoder_no_decd_text_on_mid_1_out_17), .out(transistor_3_out), .gate(COMPFLAG[1]));
  or or_1 (or_1_out, COMPFLAG[0], COMPFLAG[1]);
  or or_2 (or_2_out, COMPFLAG[1], COMPFLAG[2]);
  or or_3 (or_3_out, COMPFLAG[0], COMPFLAG[2]);
  Transistor #(.gate("br")) transistor_4 (
    .in(decoder_no_decd_text_on_mid_1_out_14), .out(transistor_4_out), .gate(CARRYFLAG));
  Transistor #(.\type ("n")) transistor_5 (
    .in(comparator_1_eq), .out(transistor_5_out), .gate(decoder_no_decd_text_on_mid_1_out_11));
  Transistor transistor_6 (.in(decoder_no_decd_text_on_mid_1_out_12), .out(transistor_6_out), .gate(comparator_1_eq));
  Transistor #(.\type ("n"), .gate("br")) transistor_7 (
    .in(decoder_no_decd_text_on_mid_1_out_18), .out(transistor_7_out), .gate(or_2_out));
  Transistor #(.\type ("n"), .gate("br")) transistor_8 (
    .in(decoder_no_decd_text_on_mid_1_out_19), .out(transistor_8_out), .gate(COMPFLAG[2]));
  Transistor #(.\type ("n")) transistor_9 (
    .in(CARRYFLAG), .out(transistor_9_out), .gate(decoder_no_decd_text_on_mid_1_out_13));
  Pull_Resistor pull_resistor_2 (.node(transistor_4_out));
  Pull_Resistor pull_resistor_3 (.node(transistor_9_out));
  Pull_Resistor pull_resistor_4 (.node(transistor_5_out));
  Pull_Resistor pull_resistor_5 (.node(transistor_6_out));
  Pull_Resistor pull_resistor_6 (.node(transistor_1_out));
  Pull_Resistor pull_resistor_7 (.node(transistor_2_out));
  Pull_Resistor pull_resistor_8 (.node(transistor_3_out));
  Pull_Resistor pull_resistor_9 (.node(transistor_7_out));
  Pull_Resistor pull_resistor_10 (.node(transistor_8_out));
  Pull_Resistor pull_resistor_11 (.node(pull_resistor_11_node));
  Transistor #(.\type ("n"), .gate("br")) transistor_10 (
    .in(decoder_no_decd_text_on_mid_1_out_20), .out(pull_resistor_11_node), .gate(or_3_out));
  or or_4 (JUMP, decoder_no_decd_text_on_mid_1_out_10, transistor_4_out, transistor_9_out, transistor_5_out, transistor_6_out, transistor_1_out, transistor_2_out, transistor_3_out, transistor_7_out, transistor_8_out, pull_resistor_11_node);
  Demultiplexer #(.select(2), .width(24), .enable("false")) demultiplexer_2 (
    .out1(demultiplexer_2_out1), .out2(Adress_Out_1), .in(Data_In[23:0]), .sel(pull_resistor_12_node));  // open: out0, out3
  or or_5 (pull_resistor_12_node[1], pull_resistor_13_node, Accumulator_Out_Selector[0], JUMP);
  Pull_Resistor pull_resistor_12 (.node(pull_resistor_12_node[0]));
  Transistor transistor_11 (.in(or_6_out), .out(pull_resistor_12_node[0]), .gate(Data_In[31]));
  Pull_Resistor pull_resistor_13 (.node(pull_resistor_13_node));
  Transistor #(.\type ("n")) transistor_12 (.in(Data_In[31]), .out(pull_resistor_13_node), .gate(or_6_out));
  or or_6 (or_6_out, CMP, decoder_no_decd_text_on_mid_1_out_3);
  or or_7 (Shift__Rotator_Data[5], decoder_no_decd_text_on_mid_1_out_6, decoder_no_decd_text_on_mid_1_out_8);
  Transistor #(.\type ("n"), .width(5)) transistor_13 (
    .in(Data_In[4:0]), .out(Shift__Rotator_Data[4:0]), .gate(Shift__Rotator_Data[7]));
  Pull_Resistor pull_resistor_14 (.node(Shift__Rotator_Data[4:0]));
  Transistor #(.\type ("n")) transistor_14 (
    .in(Data_In[31]), .out(transistor_14_out), .gate(decoder_no_decd_text_on_mid_1_out_3));
  Pull_Resistor pull_resistor_15 (.node(transistor_14_out));
  Transistor #(.\type ("n")) transistor_15 (.in(Data_In[31]), .out(transistor_15_out), .gate(CMP));
  Pull_Resistor pull_resistor_16 (.node(transistor_15_out));
  or or_8 (Shift__Rotator_Data[7], decoder_no_decd_text_on_mid_1_out_5, decoder_no_decd_text_on_mid_1_out_6, decoder_no_decd_text_on_mid_1_out_7, decoder_no_decd_text_on_mid_1_out_8);
  or or_9 (Shift__Rotator_Data[6], decoder_no_decd_text_on_mid_1_out_7, decoder_no_decd_text_on_mid_1_out_8);
  assign Data_Out_1 = {{8{1'b0}}, demultiplexer_2_out1};  // Bit_Extender bit_extender_1
  buf or_10 (Data_Out_Selector[0], CMP);  // OR_Gate
  or or_11 (Data_Out_Selector[1], CMP, decoder_no_decd_text_on_mid_1_out_3);
  buf or_12 (ADRESS_DATA_DEST_SELECTOR[0], transistor_15_out);  // OR_Gate
  or or_13 (ADRESS_DATA_DEST_SELECTOR[1], transistor_15_out, transistor_14_out);
  buf or_14 (ADRESS_LOAD_RESET[0], Accumulator_Out_Selector[0]);  // OR_Gate
  buf or_15 (ALU_Selector[0], CMP);  // OR_Gate
  buf or_16 (ALU_Selector[2], CMP);  // OR_Gate
  Pull_Resistor pull_resistor_17 (.node(Data_Out_Selector));
  Pull_Resistor pull_resistor_18 (.node(Accumulator_Out_Selector));
  Pull_Resistor pull_resistor_19 (.node(ADRESS_DATA_DEST_SELECTOR));
  Pull_Resistor pull_resistor_20 (.node(ADRESS_LOAD_RESET));
  Pull_Resistor pull_resistor_21 (.node(ALU_Selector));

  // Other names for the same wires on the sheet: WSA = Data_In[31]

  // Notes on the sheet:
  //   MOV
  //   STO
  //   SHL
  //   SHR
  //   ROL
  //   ROR
  //   CMP
  //   JMP
  //   JZ
  //   JNZ
  //   JC
  //   JNC
  //   JL
  //   JLE
  //   JE
  //   JGE
  //   JG
  //   JNE
  //   MOV
  //   STO
  //   SHL
  //   SHR
  //   ROL
  //   ROR
  //   CMP
  //   JMP
  //   JZ
  //   JNZ
  //   JC
  //   JNC
  //   JL
  //   JLE
  //   JE
  //   JGE
  //   JG
  //   JNE
  //   1 = Data Out 1
  //   24bit Data Out DMX
  //   2 = Adress Out 1
  //   WSA = WILL SELECT ADRESS
  //   CSA = CAN SELECT ADRESS
  //   SHIFT/ ROTATOR OUT:
  //   8th bit = Enable
  //   0 = Shift Left (SHL)
  //   1 = Shift Right (SHR)
  //   2 = Rotate Left (ROL)
  //   3 = Rotate Right (ROR)
  //   Last 5 bits for distance
  //   DATA OUT DEST SELECTOR:
  //   0 = Nothing
  //   2 = ACCUMULATOR
  //   3 = ALU B
  //   _________
  //   0 = Nothing
  //   0 = Nothing
  //   1 = Nothing
  //   3 = ALU B
  //   0 = READ
  //   3 = RESET
  //   _________
  //   ALU Selector:
  //   0 = Nothing
  //   1 = ADD, Sum
  //   4 = DIV, Divide
  //   6 = AND
  //   _________
  //   6-7th bit = Shift/ Rotate select as follow
  //   _________
  //   1 = MEMRISTOR DATA OUT
  //   ACCUMULATOR DEST SELECTOR:
  //   1 = MEMRISTOR DATA OUT
  //   _________
  //   ADRESS DATA DEST SELECTOR:
  //   2 = ACCUMULATOR
  //   _________
  //   ADRESS LOAD/RESET SELECTOR:
  //   1 = SAVE DATA ON ADRESS
  //   2 = SUB, Substract
  //   3 = MUL, Multiplication
  //   5 = CMP, Compare
endmodule

module Decoder__No_Decd_Text_on_mid (
  input  [4:0] in_1,
  output out_2,
  output out_3,
  output out_4,
  output out_5,
  output out_6,
  output out_7,
  output out_8,
  output out_9,
  output out_10,
  output out_11,
  output out_12,
  output out_13,
  output out_14,
  output out_15,
  output out_16,
  output out_17,
  output out_18,
  output out_19,
  output out_20,
  output out_21,
  output out_22,
  output out_23,
  output out_24,
  output out_25,
  output out_26,
  output out_27,
  output out_28,
  output out_29,
  output out_30,
  output out_31,
  output out_32,
  output out_33
);

  Decoder #(.select(5), .enable("false")) decoder_1 (
    .out0(out_2), .out1(out_3), .out2(out_4), .out3(out_5), .out4(out_6), .out5(out_7), .out6(out_8),
    .out7(out_9), .out8(out_10), .out9(out_11), .out10(out_12), .out11(out_13), .out12(out_14),
    .out13(out_15), .out14(out_16), .out15(out_17), .out16(out_18), .out17(out_19), .out18(out_20),
    .out19(out_21), .out20(out_22), .out21(out_23), .out22(out_24), .out23(out_25), .out24(out_26),
    .out25(out_27), .out26(out_28), .out27(out_29), .out28(out_30), .out29(out_31), .out30(out_32),
    .out31(out_33), .sel(in_1));
endmodule

module RAM (
  input  [31:0] in_1,
  input  [23:0] RAM_Adress,
  input  [1:0] RAM_Selector,
  output [31:0] RAM_Value_Out
);

  wire not_1_out;

  Pull_Resistor pull_resistor_1 (.node(RAM_Selector));
  not not_1 (not_1_out, RAM_Selector[0]);
  RAM_part #(.addrWidth(21), .dataWidth(32), .bus("asynch")) ram_1 (
    .addr(RAM_Adress[20:0]), .data(RAM_Value_Out), .ld(not_1_out), .clr(RAM_Selector[1]));  // open: sel
  Transistor #(.width(32)) transistor_1 (.in(in_1), .out(RAM_Value_Out), .gate(not_1_out));
  Pull_Resistor pull_resistor_2 (.node(RAM_Value_Out));
  // Pins of 21 and 24 bits meet at RAM_Adress

  // Notes on the sheet:
  //   RAM Load
  //   RAM Reset
endmodule

module GPU (
  input  [31:0] DataIn,
  input  Decrementar,
  input  [4:0] RowIn,
  input  Clock,
  input  RowSpecEnable,
  input  [13:0] VSync___Actual_Logisim_Clock,
  input  [13:0] VSync___Max_FPS,
  input  Reset,
  output [31:0] out_9,
  output [31:0] out_10,
  output [31:0] out_11,
  output [31:0] out_12,
  output [31:0] out_13,
  output [31:0] out_14,
  output [31:0] out_15,
  output [31:0] out_16,
  output [31:0] out_17,
  output [31:0] out_18,
  output [31:0] out_19,
  output [31:0] out_20,
  output [4:0] RowDebug,
  output [31:0] out_22,
  output [31:0] out_23,
  output [31:0] out_24,
  output [31:0] out_25,
  output [31:0] out_26,
  output [31:0] out_27,
  output [31:0] out_28,
  output [31:0] out_29,
  output [31:0] out_30,
  output [31:0] out_31,
  output [31:0] out_32,
  output [31:0] out_33
);

  wire comparator_1_eq, controlled_buffer_1_out, counter_2_carry, counter_3_q, decoder_1_out0,
       decoder_1_out1, decoder_1_out2, decoder_1_out3, decoder_1_out4, decoder_1_out5, decoder_1_out6,
       decoder_1_out7, decoder_1_out8, decoder_1_out9, decoder_1_out10, decoder_1_out11, decoder_1_out12,
       decoder_1_out13, decoder_1_out14, decoder_1_out15, decoder_1_out16, decoder_1_out17, decoder_1_out18,
       decoder_1_out19, decoder_1_out20, decoder_1_out21, decoder_1_out22, decoder_1_out23, or_1_out,
       or_2_out, pull_resistor_4_node, pull_resistor_7_node;
  wire [13:0] counter_1_q, divider_1_out, pull_resistor_2_node, register_1_q;
  wire [31:0] controlled_buffer_2_out, controlled_buffer_3_out, controlled_buffer_4_out,
       controlled_buffer_5_out, controlled_buffer_6_out, controlled_buffer_7_out, controlled_buffer_8_out,
       controlled_buffer_9_out, controlled_buffer_10_out, controlled_buffer_11_out, controlled_buffer_12_out,
       controlled_buffer_13_out, controlled_buffer_14_out, controlled_buffer_15_out,
       controlled_buffer_16_out, controlled_buffer_17_out, controlled_buffer_18_out,
       controlled_buffer_19_out, controlled_buffer_20_out, controlled_buffer_21_out,
       controlled_buffer_22_out, controlled_buffer_23_out, controlled_buffer_24_out,
       controlled_buffer_25_out, register_2_q, register_3_q, register_4_q, register_5_q, register_6_q,
       register_7_q, register_8_q, register_9_q, register_10_q, register_11_q, register_12_q, register_13_q,
       register_14_q, register_15_q, register_16_q, register_17_q, register_18_q, register_19_q,
       register_20_q, register_21_q, register_22_q, register_23_q, register_24_q, register_25_q;

  Register #(.width(14), .trigger("high")) register_1 (
    .D(VSync___Actual_Logisim_Clock), .Q(register_1_q), .clk(1'b1));  // open: en, clr
  Pull_Resistor pull_resistor_1 (.node(register_1_q));
  Pull_Resistor pull_resistor_2 (.node(pull_resistor_2_node));
  Pull_Resistor pull_resistor_3 (.node(Clock));
  Divider #(.width(14)) divider_1 (
    .a(register_1_q), .b(pull_resistor_2_node), .out(divider_1_out));  // open: upper, rem
  Multiplier #(.width(14)) multiplier_1 (
    .a(VSync___Max_FPS), .b(14'h2), .out(pull_resistor_2_node));  // open: cin, cout
  Counter #(.width(14), .max('h3fff)) counter_1 (
    .Q(counter_1_q), .clk(Clock), .clr(or_1_out));  // open: load, D, count, carry
  Pull_Resistor pull_resistor_4 (.node(pull_resistor_4_node));
  Comparator #(.width(14)) comparator_1 (
    .a(counter_1_q), .b(divider_1_out), .gt(pull_resistor_4_node), .eq(comparator_1_eq));  // open: lt
  or or_1 (or_1_out, pull_resistor_4_node, comparator_1_eq);
  Counter #(.width(5), .max('h17)) counter_2 (
    .load(Decrementar), .D(RowIn), .count(Clock), .Q(RowDebug), .carry(counter_2_carry), .clk(Clock),
    .clr(Reset));
  or or_2 (or_2_out, RowSpecEnable, counter_2_carry);
  assign controlled_buffer_1_out = or_1_out ? counter_3_q : 1'bz;  // Controlled_Buffer controlled_buffer_1
  Counter #(.width(1), .max('h1), .ongoal("stay")) counter_3 (
    .Q(counter_3_q), .clk(or_2_out), .clr(controlled_buffer_1_out));  // open: load, D, count, carry
  Pull_Resistor pull_resistor_5 (.node(controlled_buffer_1_out));
  Decoder #(.select(5), .enable("false")) decoder_1 (
    .out0(decoder_1_out0), .out1(decoder_1_out1), .out2(decoder_1_out2), .out3(decoder_1_out3),
    .out4(decoder_1_out4), .out5(decoder_1_out5), .out6(decoder_1_out6), .out7(decoder_1_out7),
    .out8(decoder_1_out8), .out9(decoder_1_out9), .out10(decoder_1_out10), .out11(decoder_1_out11),
    .out12(decoder_1_out12), .out13(decoder_1_out13), .out14(decoder_1_out14), .out15(decoder_1_out15),
    .out16(decoder_1_out16), .out17(decoder_1_out17), .out18(decoder_1_out18), .out19(decoder_1_out19),
    .out20(decoder_1_out20), .out21(decoder_1_out21), .out22(decoder_1_out22), .out23(decoder_1_out23),
    .sel(RowDebug));  // open: out24, out25, out26, out27, out28, out29, out30, out31
  Pull_Resistor pull_resistor_6 (.node(Reset));
  Register #(.width(32), .trigger("low")) register_2 (
    .D(DataIn), .en(decoder_1_out0), .Q(register_2_q), .clk(pull_resistor_7_node), .clr(Reset));
  Register #(.width(32), .trigger("low")) register_3 (
    .D(DataIn), .en(decoder_1_out1), .Q(register_3_q), .clk(pull_resistor_7_node), .clr(Reset));
  Register #(.width(32), .trigger("low")) register_4 (
    .D(DataIn), .en(decoder_1_out2), .Q(register_4_q), .clk(pull_resistor_7_node), .clr(Reset));
  Register #(.width(32), .trigger("low")) register_5 (
    .D(DataIn), .en(decoder_1_out3), .Q(register_5_q), .clk(pull_resistor_7_node), .clr(Reset));
  Register #(.width(32), .trigger("low")) register_6 (
    .D(DataIn), .en(decoder_1_out4), .Q(register_6_q), .clk(pull_resistor_7_node), .clr(Reset));
  Register #(.width(32), .trigger("low")) register_7 (
    .D(DataIn), .en(decoder_1_out5), .Q(register_7_q), .clk(pull_resistor_7_node), .clr(Reset));
  Register #(.width(32), .trigger("low")) register_8 (
    .D(DataIn), .en(decoder_1_out6), .Q(register_8_q), .clk(pull_resistor_7_node), .clr(Reset));
  Register #(.width(32), .trigger("low")) register_9 (
    .D(DataIn), .en(decoder_1_out7), .Q(register_9_q), .clk(pull_resistor_7_node), .clr(Reset));
  Register #(.width(32), .trigger("low")) register_10 (
    .D(DataIn), .en(decoder_1_out8), .Q(register_10_q), .clk(pull_resistor_7_node), .clr(Reset));
  Register #(.width(32), .trigger("low")) register_11 (
    .D(DataIn), .en(decoder_1_out9), .Q(register_11_q), .clk(pull_resistor_7_node), .clr(Reset));
  Register #(.width(32), .trigger("low")) register_12 (
    .D(DataIn), .en(decoder_1_out10), .Q(register_12_q), .clk(pull_resistor_7_node), .clr(Reset));
  Register #(.width(32), .trigger("low")) register_13 (
    .D(DataIn), .en(decoder_1_out11), .Q(register_13_q), .clk(pull_resistor_7_node), .clr(Reset));
  Register #(.width(32), .trigger("low")) register_14 (
    .D(DataIn), .en(decoder_1_out12), .Q(register_14_q), .clk(pull_resistor_7_node), .clr(Reset));
  Register #(.width(32), .trigger("low")) register_15 (
    .D(DataIn), .en(decoder_1_out13), .Q(register_15_q), .clk(pull_resistor_7_node), .clr(Reset));
  Register #(.width(32), .trigger("low")) register_16 (
    .D(DataIn), .en(decoder_1_out14), .Q(register_16_q), .clk(pull_resistor_7_node), .clr(Reset));
  Register #(.width(32), .trigger("low")) register_17 (
    .D(DataIn), .en(decoder_1_out15), .Q(register_17_q), .clk(pull_resistor_7_node), .clr(Reset));
  Register #(.width(32), .trigger("low")) register_18 (
    .D(DataIn), .en(decoder_1_out16), .Q(register_18_q), .clk(pull_resistor_7_node), .clr(Reset));
  Register #(.width(32), .trigger("low")) register_19 (
    .D(DataIn), .en(decoder_1_out17), .Q(register_19_q), .clk(pull_resistor_7_node), .clr(Reset));
  Register #(.width(32), .trigger("low")) register_20 (
    .D(DataIn), .en(decoder_1_out18), .Q(register_20_q), .clk(pull_resistor_7_node), .clr(Reset));
  Register #(.width(32), .trigger("low")) register_21 (
    .D(DataIn), .en(decoder_1_out19), .Q(register_21_q), .clk(pull_resistor_7_node), .clr(Reset));
  Register #(.width(32), .trigger("low")) register_22 (
    .D(DataIn), .en(decoder_1_out20), .Q(register_22_q), .clk(pull_resistor_7_node), .clr(Reset));
  Register #(.width(32), .trigger("low")) register_23 (
    .D(DataIn), .en(decoder_1_out21), .Q(register_23_q), .clk(pull_resistor_7_node), .clr(Reset));
  Register #(.width(32), .trigger("low")) register_24 (
    .D(DataIn), .en(decoder_1_out22), .Q(register_24_q), .clk(pull_resistor_7_node), .clr(Reset));
  Register #(.width(32), .trigger("low")) register_25 (
    .D(DataIn), .en(decoder_1_out23), .Q(register_25_q), .clk(pull_resistor_7_node), .clr(Reset));
  assign controlled_buffer_2_out = controlled_buffer_1_out ? register_2_q : 32'bz;  // Controlled_Buffer controlled_buffer_2
  assign controlled_buffer_3_out = controlled_buffer_1_out ? register_3_q : 32'bz;  // Controlled_Buffer controlled_buffer_3
  assign controlled_buffer_4_out = controlled_buffer_1_out ? register_4_q : 32'bz;  // Controlled_Buffer controlled_buffer_4
  assign controlled_buffer_5_out = controlled_buffer_1_out ? register_5_q : 32'bz;  // Controlled_Buffer controlled_buffer_5
  assign controlled_buffer_6_out = controlled_buffer_1_out ? register_6_q : 32'bz;  // Controlled_Buffer controlled_buffer_6
  assign controlled_buffer_7_out = controlled_buffer_1_out ? register_7_q : 32'bz;  // Controlled_Buffer controlled_buffer_7
  assign controlled_buffer_8_out = controlled_buffer_1_out ? register_8_q : 32'bz;  // Controlled_Buffer controlled_buffer_8
  assign controlled_buffer_9_out = controlled_buffer_1_out ? register_9_q : 32'bz;  // Controlled_Buffer controlled_buffer_9
  assign controlled_buffer_10_out = controlled_buffer_1_out ? register_10_q : 32'bz;  // Controlled_Buffer controlled_buffer_10
  assign controlled_buffer_11_out = controlled_buffer_1_out ? register_11_q : 32'bz;  // Controlled_Buffer controlled_buffer_11
  assign controlled_buffer_12_out = controlled_buffer_1_out ? register_12_q : 32'bz;  // Controlled_Buffer controlled_buffer_12
  assign controlled_buffer_13_out = controlled_buffer_1_out ? register_13_q : 32'bz;  // Controlled_Buffer controlled_buffer_13
  assign controlled_buffer_14_out = controlled_buffer_1_out ? register_14_q : 32'bz;  // Controlled_Buffer controlled_buffer_14
  assign controlled_buffer_15_out = controlled_buffer_1_out ? register_15_q : 32'bz;  // Controlled_Buffer controlled_buffer_15
  assign controlled_buffer_16_out = controlled_buffer_1_out ? register_16_q : 32'bz;  // Controlled_Buffer controlled_buffer_16
  assign controlled_buffer_17_out = controlled_buffer_1_out ? register_17_q : 32'bz;  // Controlled_Buffer controlled_buffer_17
  assign controlled_buffer_18_out = controlled_buffer_1_out ? register_18_q : 32'bz;  // Controlled_Buffer controlled_buffer_18
  assign controlled_buffer_19_out = controlled_buffer_1_out ? register_19_q : 32'bz;  // Controlled_Buffer controlled_buffer_19
  assign controlled_buffer_20_out = controlled_buffer_1_out ? register_20_q : 32'bz;  // Controlled_Buffer controlled_buffer_20
  assign controlled_buffer_21_out = controlled_buffer_1_out ? register_21_q : 32'bz;  // Controlled_Buffer controlled_buffer_21
  assign controlled_buffer_22_out = controlled_buffer_1_out ? register_22_q : 32'bz;  // Controlled_Buffer controlled_buffer_22
  assign controlled_buffer_23_out = controlled_buffer_1_out ? register_23_q : 32'bz;  // Controlled_Buffer controlled_buffer_23
  assign controlled_buffer_24_out = controlled_buffer_1_out ? register_24_q : 32'bz;  // Controlled_Buffer controlled_buffer_24
  assign controlled_buffer_25_out = controlled_buffer_1_out ? register_25_q : 32'bz;  // Controlled_Buffer controlled_buffer_25
  Register #(.width(32), .trigger("low")) register_26 (
    .D(controlled_buffer_2_out), .Q(out_9), .clk(pull_resistor_7_node), .clr(Reset));  // open: en
  Register #(.width(32), .trigger("low")) register_27 (
    .D(controlled_buffer_3_out), .Q(out_10), .clk(pull_resistor_7_node), .clr(Reset));  // open: en
  Register #(.width(32), .trigger("low")) register_28 (
    .D(controlled_buffer_4_out), .Q(out_11), .clk(pull_resistor_7_node), .clr(Reset));  // open: en
  Register #(.width(32), .trigger("low")) register_29 (
    .D(controlled_buffer_5_out), .Q(out_12), .clk(pull_resistor_7_node), .clr(Reset));  // open: en
  Register #(.width(32), .trigger("low")) register_30 (
    .D(controlled_buffer_6_out), .Q(out_13), .clk(pull_resistor_7_node), .clr(Reset));  // open: en
  Register #(.width(32), .trigger("low")) register_31 (
    .D(controlled_buffer_7_out), .Q(out_14), .clk(pull_resistor_7_node), .clr(Reset));  // open: en
  Register #(.width(32), .trigger("low")) register_32 (
    .D(controlled_buffer_8_out), .Q(out_15), .clk(pull_resistor_7_node), .clr(Reset));  // open: en
  Register #(.width(32), .trigger("low")) register_33 (
    .D(controlled_buffer_9_out), .Q(out_16), .clk(pull_resistor_7_node), .clr(Reset));  // open: en
  Register #(.width(32), .trigger("low")) register_34 (
    .D(controlled_buffer_10_out), .Q(out_17), .clk(pull_resistor_7_node), .clr(Reset));  // open: en
  Register #(.width(32), .trigger("low")) register_35 (
    .D(controlled_buffer_11_out), .Q(out_18), .clk(pull_resistor_7_node), .clr(Reset));  // open: en
  Register #(.width(32), .trigger("low")) register_36 (
    .D(controlled_buffer_12_out), .Q(out_19), .clk(pull_resistor_7_node), .clr(Reset));  // open: en
  Register #(.width(32), .trigger("low")) register_37 (
    .D(controlled_buffer_13_out), .Q(out_20), .clk(pull_resistor_7_node), .clr(Reset));  // open: en
  Register #(.width(32), .trigger("low")) register_38 (
    .D(controlled_buffer_14_out), .Q(out_22), .clk(pull_resistor_7_node), .clr(Reset));  // open: en
  Register #(.width(32), .trigger("low")) register_39 (
    .D(controlled_buffer_15_out), .Q(out_23), .clk(pull_resistor_7_node), .clr(Reset));  // open: en
  Register #(.width(32), .trigger("low")) register_40 (
    .D(controlled_buffer_16_out), .Q(out_24), .clk(pull_resistor_7_node), .clr(Reset));  // open: en
  Register #(.width(32), .trigger("low")) register_41 (
    .D(controlled_buffer_17_out), .Q(out_25), .clk(pull_resistor_7_node), .clr(Reset));  // open: en
  Register #(.width(32), .trigger("low")) register_42 (
    .D(controlled_buffer_18_out), .Q(out_26), .clk(pull_resistor_7_node), .clr(Reset));  // open: en
  Register #(.width(32), .trigger("low")) register_43 (
    .D(controlled_buffer_19_out), .Q(out_27), .clk(pull_resistor_7_node), .clr(Reset));  // open: en
  Register #(.width(32), .trigger("low")) register_44 (
    .D(controlled_buffer_20_out), .Q(out_28), .clk(pull_resistor_7_node), .clr(Reset));  // open: en
  Register #(.width(32), .trigger("low")) register_45 (
    .D(controlled_buffer_21_out), .Q(out_29), .clk(pull_resistor_7_node), .clr(Reset));  // open: en
  Register #(.width(32), .trigger("low")) register_46 (
    .D(controlled_buffer_22_out), .Q(out_30), .clk(pull_resistor_7_node), .clr(Reset));  // open: en
  Register #(.width(32), .trigger("low")) register_47 (
    .D(controlled_buffer_23_out), .Q(out_31), .clk(pull_resistor_7_node), .clr(Reset));  // open: en
  Register #(.width(32), .trigger("low")) register_48 (
    .D(controlled_buffer_24_out), .Q(out_32), .clk(pull_resistor_7_node), .clr(Reset));  // open: en
  Register #(.width(32), .trigger("low")) register_49 (
    .D(controlled_buffer_25_out), .Q(out_33), .clk(pull_resistor_7_node), .clr(Reset));  // open: en
  Pull_Resistor pull_resistor_7 (.node(pull_resistor_7_node));

  // Notes on the sheet:
  //   FPS Limit
  //   Depois de todas as linhas terem seus valores atualizados, tudo irá se atualizar para Q' ao mesmo tempo
endmodule

module okok (
  input  [31:0] in_1,
  output [31:0] out_2,
  output [31:0] out_3,
  output [31:0] out_4,
  output [31:0] out_5,
  output [31:0] out_6,
  output [31:0] out_7,
  output [31:0] out_8,
  output [31:0] out_9,
  output [31:0] out_10,
  output [31:0] out_11,
  output [31:0] out_12,
  output [31:0] out_13,
  output [31:0] out_14,
  output [31:0] out_15,
  output [31:0] out_16,
  output [31:0] out_17,
  output [31:0] out_18,
  output [31:0] out_19,
  output [31:0] out_20,
  output [31:0] out_21,
  output [31:0] out_22,
  output [31:0] out_23,
  output [31:0] out_24,
  output [31:0] out_25
);

  Pull_Resistor pull_resistor_1 (.node(in_1));

  assign out_2 = in_1;
  assign out_3 = in_1;
  assign out_4 = in_1;
  assign out_5 = in_1;
  assign out_6 = in_1;
  assign out_7 = in_1;
  assign out_8 = in_1;
  assign out_9 = in_1;
  assign out_10 = in_1;
  assign out_11 = in_1;
  assign out_12 = in_1;
  assign out_13 = in_1;
  assign out_14 = in_1;
  assign out_15 = in_1;
  assign out_16 = in_1;
  assign out_17 = in_1;
  assign out_18 = in_1;
  assign out_19 = in_1;
  assign out_20 = in_1;
  assign out_21 = in_1;
  assign out_22 = in_1;
  assign out_23 = in_1;
  assign out_24 = in_1;
  assign out_25 = in_1;
endmodule

module Random (
  input  Reset,
  input  in_2,
  input  [6:0] in_3
);

  wire _1_out, button_1_out, button_2_out, counter_1_carry;
  wire [6:0] _3_out, adder_1_out, bit_extender_1_out, pull_resistor_1_node;

  // Probe on in_3
  Button button_1 (.out(button_1_out));
  Pull_Resistor pull_resistor_1 (.node(pull_resistor_1_node));
  Transistor #(.\type ("n"), .width(7)) transistor_1 (.in(in_3), .out(pull_resistor_1_node), .gate(button_1_out));
  Clock #(.highDuration(3), .lowDuration(3)) clock_1 ();  // open: out
  Button button_2 (.out(button_2_out));
  Counter #(.width(1), .max('h1)) counter_1 (.carry(counter_1_carry));  // open: load, D, count, Q, clk, clr
  Random_part #(.width(1), .seed(1)) _1 (.out(_1_out), .clr(button_2_out));  // open: clk, next
  Random_part #(.width(1), .seed(3)) _3 (
    .clk(pull_resistor_1_node[0]), .next(Reset), .out(_3_out[0]), .clr(button_2_out));
  Random_part #(.width(1), .seed(5)) _5 (
    .clk(pull_resistor_1_node[1]), .next(Reset), .out(_3_out[1]), .clr(button_2_out));
  Random_part #(.width(1), .seed(7)) _7 (
    .clk(pull_resistor_1_node[2]), .next(Reset), .out(_3_out[2]), .clr(button_2_out));
  Random_part #(.width(1)) _11 (.clk(pull_resistor_1_node[3]), .next(Reset), .out(_3_out[3]), .clr(button_2_out));
  Random_part #(.width(1), .seed(13)) _13 (
    .clk(pull_resistor_1_node[4]), .next(Reset), .out(_3_out[4]), .clr(button_2_out));
  Random_part #(.width(1), .seed(17)) _17 (
    .clk(pull_resistor_1_node[5]), .next(Reset), .out(_3_out[5]), .clr(button_2_out));
  Random_part #(.width(1), .seed(23)) _23 (
    .clk(pull_resistor_1_node[6]), .next(Reset), .out(_3_out[6]), .clr(button_2_out));
  // Probe on _3_out[5]
  assign bit_extender_1_out = {{6{1'b0}}, _1_out};  // Bit_Extender bit_extender_1
  // Probe on adder_1_out
  Adder #(.width(7)) adder_1 (.a(bit_extender_1_out), .b(_3_out), .out(adder_1_out));  // open: cin, cout
endmodule
