// Logisim project Logiwin Open Project.circ as structural Verilog
module Logiwin (
);

  wire C, console_back_1__4clock_2on_2off, console_back_1_clear, keyboard_1_avail, keyboard_back_1_clock,
       ON_OFF_out, P;
  wire [2:0] cpu_external_connections_1_ram_controls;
  wire [4:0] joystick_1_x, joystick_1_y;
  wire [6:0] console_back_1_data, keyboard_1_data, keyboard_back_1_out_4;
  wire [7:0] cpu_external_connections_1_external_controller_selector;
  wire [7:7] external_devices_controler_1__1fb;
  wire [9:0] joystick_back_1_output;
  wire [21:0] cpu_external_connections_1_ram_adress_1__w, cpu_external_connections_1_ram_adress_2__r;
  wire [31:0] cpu_external_connections_1_acc, cpu_external_connections_1_external,
       cpu_external_connections_1_ram_data_in____out, dual_address_ram_chip_1_ext_data_in____out,
       external_devices_controler_1_cpu_out_in, external_devices_controler_1_output_device_1;

  // DotMatrix2 dotmatrix2_1: pin names not known
  Keyboard #(.buflen(256)) keyboard_1 (
    .clk(keyboard_back_1_clock), .avail(keyboard_1_avail), .data(keyboard_1_data));  // open: re, clr
  Keyboard_Back keyboard_back_1 (
    .Keyboard_Data(keyboard_1_data), .Clock__Feedback(external_devices_controler_1__1fb[7]),
    .out_4(keyboard_back_1_out_4), .Clock(keyboard_back_1_clock), .There_is_char(keyboard_1_avail));
  Dual_Address_RAM_chip dual_address_ram_chip_1 (
    .Ext_Data_In____Out(dual_address_ram_chip_1_ext_data_in____out),
    .Ext_Data_Out____In(cpu_external_connections_1_ram_data_in____out),
    .Controls(cpu_external_connections_1_ram_controls),
    .Ext_Address_2__R(cpu_external_connections_1_ram_adress_2__r),
    .Ext_Address_1__W(cpu_external_connections_1_ram_adress_1__w));  // open: Data_In____Out, Data_Out____In, Focus, Clock, Reset__Be_careful, Address_2__READ, Address_1__WRITE
  GPU_____External_Connections gpu_external_connections_1 ();  // open: Clock, out_38, out_2, out_14, out_26, out_39, out_3, out_15, out_27, out_40, out_4, out_16, out_28, out_41, out_5, out_17, out_29, out_42, out_6, out_18, out_30, out_43, out_7, out_19, out_31, out_44, out_8, out_20, out_32, out_45, out_9, out_21, out_33, out_46, out_10, out_11, out_12, out_22, out_23, out_24, out_34, out_35, out_36, out_47, out_48, out_49, out_13, out_25, out_37, out_50
  Joystick_Back joystick_back_1 (.X(joystick_1_x), .Y(joystick_1_y), .Output(joystick_back_1_output));
  // RAM ram_1: pin names not known
  Joystick #(.bits(5)) joystick_1 (.x(joystick_1_x), .y(joystick_1_y));
  External_Devices_Controler external_devices_controler_1 (
    .Input_Device_1(keyboard_back_1_out_4), .CPU_In_Out(cpu_external_connections_1_external),
    .CPU_Out_In(external_devices_controler_1_cpu_out_in), .Input_Device_3(joystick_back_1_output),
    .Externak_Controller_Selector(cpu_external_connections_1_external_controller_selector),
    .Output_Device_1(external_devices_controler_1_output_device_1),
    ._1FB(external_devices_controler_1__1fb[7]));  // open: Input_Device_4, Output_Device_4, Input_Device_2, Output_Device_3, Output_Device_2, _2FB, _3FB, _4FB
  CPU____External_Connections cpu_external_connections_1 (
    .External(cpu_external_connections_1_external),
    .RAM_Adress_1__W(cpu_external_connections_1_ram_adress_1__w),
    .RAM_Data_In____Out(cpu_external_connections_1_ram_data_in____out),
    .RAM_Data_Out____In(dual_address_ram_chip_1_ext_data_in____out), .Acc(cpu_external_connections_1_acc),
    .Power(P), .Turn_it_on(ON_OFF_out), .Clock(C),
    .RAM_Adress_2__R(cpu_external_connections_1_ram_adress_2__r),
    .RAM_Controls(cpu_external_connections_1_ram_controls),
    .External_Controller_Selector(cpu_external_connections_1_external_controller_selector),
    .External_Input(external_devices_controler_1_cpu_out_in));
  Button ON_OFF (.out(ON_OFF_out));
  // Probe on cpu_external_connections_1_acc
  // Probe on cpu_external_connections_1_acc
  // Probe on cpu_external_connections_1_acc
  Console_Back console_back_1 (
    .Data(console_back_1_data), .Console_Data_Clear(external_devices_controler_1_output_device_1), .Power(P),
    .Clear(console_back_1_clear), ._4Clock_2On_2Off(console_back_1__4clock_2on_2off), .Clock_1_1(C));
  TTY #(.rows(20), .cols(44)) tty_1 (
    .data(console_back_1_data), .clk(console_back_1__4clock_2on_2off), .clr(console_back_1_clear));  // open: we

  // Notes on the sheet:
  //   Never store data on Address 0x000000.
  //   It will get buggy. Readme.
  //   Logiwin
  //   Working like a charm!
  //    Read Readme!
endmodule

module CPU____External_Connections (
  input  [31:0] External_Input,
  input  [31:0] RAM_Data_Out____In,
  input  Turn_it_on,
  output [7:0] External_Controller_Selector,
  output [31:0] External,
  output [31:0] Acc,
  output [31:0] RAM_Data_In____Out,
  output [21:0] RAM_Adress_1__W,
  output [21:0] RAM_Adress_2__R,
  output [2:0] RAM_Controls,
  output Clock,
  output Power
);

  wire CPU_Clock_out, cpu_core_and_bus_1_store_current_address, not_1_out, not_2_out, pull_resistor_4_node,
       pull_resistor_5_node, Second_Clock_out, t_ff_1_qn;
  wire [0:0] cpu_core_and_bus_1_adress_commands, cpu_core_and_bus_1_jump;
  wire [1:0] cpu_core_and_bus_1_adress_commands_2, cpu_core_and_bus_1_jump_2, demultiplexer_5_out1_2,
       multiplexer_1_out_2, or_1_out;
  wire [2:0] pull_resistor_3_node;
  wire [21:0] demultiplexer_5_out1, multiplexer_1_out;
  wire [23:0] adder_1_out, adder_2_out, controlled_buffer_1_out, controlled_buffer_4_out,
       cpu_core_and_bus_1_address_out, demultiplexer_5_out0, multiplexer_2_out, multiplexer_3_out,
       Program_Counter_q, register_1_q, Relative_Address_q, RTN;
  wire [24:0] cpu_core_and_bus_1_set_relative_address;
  wire [31:0] controlled_buffer_3_out, cpu_core_and_bus_1_data_in__out;

  Demultiplexer #(.select(2), .width(3), .disabled(0), .enable("false")) demultiplexer_1 (
    .out0(RAM_Controls), .in(pull_resistor_3_node), .sel(or_1_out));  // open: out1, out2, out3
  Demultiplexer #(.select(2), .width(22), .disabled(0), .enable("false")) demultiplexer_2 (
    .out0(RAM_Adress_2__R), .in(multiplexer_1_out), .sel(multiplexer_1_out_2));  // open: out1, out2, out3
  assign or_1_out = multiplexer_1_out_2 | demultiplexer_5_out1_2;  // OR_Gate or_1, 2 bits wide
  Counter #(.width(1), .max('h1), .ongoal("stay")) counter_1 (
    .Q(pull_resistor_3_node[1]), .clk(cpu_core_and_bus_1_adress_commands[0]), .clr(pull_resistor_4_node));  // open: load, D, count, carry
  Register #(.width(24)) register_1 (
    .D(Program_Counter_q), .en(not_2_out), .Q(register_1_q), .clk(cpu_core_and_bus_1_jump[0]), .clr(t_ff_1_qn));
  T_Flip_Flop t_ff_1 (.clk(Turn_it_on), .T(Turn_it_on), .Q(Power), .Qn(t_ff_1_qn));  // open: preset, reset, en
  Demultiplexer #(.select(2), .width(32), .enable("false")) demultiplexer_3 (
    .out0(RAM_Data_In____Out), .in(cpu_core_and_bus_1_data_in__out), .sel(demultiplexer_5_out1_2));  // open: out1, out2, out3
  Demultiplexer #(.select(2), .width(22), .disabled(0), .enable("false")) demultiplexer_4 (
    .out0(RAM_Adress_1__W), .in(demultiplexer_5_out1), .sel(demultiplexer_5_out1_2));  // open: out1, out2, out3
  Multiplexer #(.select(2), .width(24), .enable("false")) multiplexer_1 (
    .in0(Program_Counter_q), .in1(demultiplexer_5_out0),
    .in3({demultiplexer_5_out1_2, demultiplexer_5_out1}), .out({multiplexer_1_out_2, multiplexer_1_out}),
    .sel(cpu_core_and_bus_1_adress_commands_2));  // open: in2
  assign controlled_buffer_1_out = cpu_core_and_bus_1_jump_2[0] ? register_1_q : 24'bz;  // Controlled_Buffer controlled_buffer_1
  Adder #(.width(24)) adder_1 (
    .a(controlled_buffer_1_out), .b(RTN), .out(adder_1_out), .cin(cpu_core_and_bus_1_jump_2[0]));  // open: cout
  Clock Second_Clock (.out(Second_Clock_out));
  Pull_Resistor pull_resistor_1 (.node(Clock));
  assign Clock = Power ? Second_Clock_out : 1'bz;  // Controlled_Buffer controlled_buffer_2
  assign controlled_buffer_3_out = cpu_core_and_bus_1_jump_2[0] ? RAM_Data_Out____In : 32'bz;  // Controlled_Buffer controlled_buffer_3
  assign controlled_buffer_4_out = cpu_core_and_bus_1_store_current_address ? Program_Counter_q : 24'bz;  // Controlled_Buffer controlled_buffer_4
  Pull_Resistor pull_resistor_2 (.node(controlled_buffer_4_out));
  Pull_Resistor pull_resistor_3 (.node(pull_resistor_3_node[0]));
  assign pull_resistor_3_node[0] = pull_resistor_4_node ? cpu_core_and_bus_1_adress_commands[0] : 1'bz;  // Controlled_Buffer controlled_buffer_5
  Multiplexer #(.select(2), .width(24), .disabled(0), .enable("false")) multiplexer_2 (
    .in0(demultiplexer_5_out0), .in1(controlled_buffer_3_out[23:0]), .in2(adder_1_out),
    .out(multiplexer_2_out), .sel(cpu_core_and_bus_1_jump_2));  // open: in3
  Counter #(.width(24), .max('hffffff)) Program_Counter (
    .load(cpu_core_and_bus_1_jump[0]), .D(multiplexer_2_out), .count(not_1_out), .Q(Program_Counter_q),
    .clk(CPU_Clock_out), .clr(t_ff_1_qn));  // open: carry
  not not_1 (not_1_out, cpu_core_and_bus_1_jump[0]);
  Pull_Resistor pull_resistor_4 (.node(pull_resistor_4_node));
  Clock #(.lowDuration(3)) CPU_Clock (.out(CPU_Clock_out));
  Transistor #(.\type ("n"), .gate("br")) transistor_1 (.in(CPU_Clock_out), .out(pull_resistor_4_node), .gate(Power));
  Demultiplexer #(.width(24), .disabled(0), .enable("false")) demultiplexer_5 (
    .out0(demultiplexer_5_out0), .out1({demultiplexer_5_out1_2, demultiplexer_5_out1}), .in(adder_2_out),
    .sel(cpu_core_and_bus_1_adress_commands[0]));
  not not_2 (not_2_out, cpu_core_and_bus_1_jump_2[1]);
  Multiplexer #(.width(24), .enable("false")) multiplexer_3 (
    .in0(Program_Counter_q), .in1(cpu_core_and_bus_1_set_relative_address[23:0]), .out(multiplexer_3_out),
    .sel(pull_resistor_5_node));
  Pull_Resistor pull_resistor_5 (.node(pull_resistor_5_node));
  Register #(.width(24), .trigger("falling")) Relative_Address (
    .D(multiplexer_3_out), .Q(Relative_Address_q), .clk(cpu_core_and_bus_1_set_relative_address[24]),
    .clr(t_ff_1_qn));  // open: en
  Adder #(.width(24)) adder_2 (
    .a(Relative_Address_q), .b(cpu_core_and_bus_1_address_out), .out(adder_2_out));  // open: cin, cout
  CPU____Core_And_Bus cpu_core_and_bus_1 (
    .External_Output__Console_etc(External), .Data_IN__OUT(cpu_core_and_bus_1_data_in__out),
    .Address_Out(cpu_core_and_bus_1_address_out), .Data_OUT__IN(RAM_Data_Out____In),
    .Jump({cpu_core_and_bus_1_jump_2, cpu_core_and_bus_1_jump[0]}), .Reset(t_ff_1_qn), .ACC(Acc),
    .Adress_Commands({pull_resistor_3_node[2], cpu_core_and_bus_1_adress_commands_2, cpu_core_and_bus_1_adress_commands[0]}),
    .Return_value_adder(RTN), .Clock(pull_resistor_4_node),
    .External_Controller_Selector(External_Controller_Selector),
    .Set_Relative_Address(cpu_core_and_bus_1_set_relative_address), .External_Input(External_Input),
    .Current_Address(controlled_buffer_4_out),
    .Store_Current_Address(cpu_core_and_bus_1_store_current_address));

  // Notes on the sheet:
  //   RAM_Data_Out____In: pull=down
  //   First to Store
  //   Second to focus
  //   Third to Reset
  //   This counter is just for graphical purposes,
  //   to keep the focus on the RAM. It works.
  //   For now this jump stuff
  //    on the main memory (22-bit).
  //   will only work directly
  //   These DMX are to the future. Like adding other memories; external devices.
  //   Jump Return
  //   Sorry for the mess. So many ideas and cofusion in my head.
  //   Relative Address
  //   with given value
  //   0 = Set Absolute Address
  //   1 = Set Relative Address
  //   at the current counter
  //   2 = Set Relative Address
  //   Jump:
  //   =1 to Jump from direct value
  //   =3 to Jump from address value (1+2)
  //   Address Commands
  //   1st to Store
  //   3rd to Swap (+2nd)
  //   4th to Reset
  //   =5 to Return to Address before the Jump value (4+1)
  //   2nd to Addres Read from value
endmodule

module CPU____Core_And_Bus (
  input  Clock,
  input  [31:0] Data_OUT__IN,
  input  [31:0] External_Input,
  input  Reset,
  input  [23:0] Current_Address,
  output [2:0] Jump,
  output [31:0] ACC,
  output [3:0] Adress_Commands,
  output [23:0] Return_value_adder,
  output [7:0] External_Controller_Selector,
  output [31:0] Data_IN__OUT,
  output [31:0] External_Output__Console_etc,
  output [23:0] Address_Out,
  output Store_Current_Address,
  output [24:0] Set_Relative_Address
);

  wire bitfinder_1_found, cpu_instructions_1_accumulator_clock, pull_resistor_2_node;
  wire [1:0] cpu_instructions_1_acc_out_selector, cpu_instructions_1_exi_dmx, cpu_instructions_1_inc_dec;
  wire [1:1] cpu_instructions_1_store_current_address;
  wire [2:0] cpu_instructions_1_data_instructions_out_selector, cpu_instructions_1_data_out____in_selector;
  wire [3:0] cpu_alu_1_alu_flag;
  wire [4:0] cpu_instructions_1_alu_selector;
  wire [31:0] adder_1_out, bit_extender_1_out, buffer_1_out, buffer_2_out, buffer_3_out, buffer_4_out,
       buffer_5_out, buffer_6_out, buffer_7_out, buffer_8_out, cpu_alu_1_out,
       cpu_instructions_1_data_instructions_out, demultiplexer_1_out0, demultiplexer_1_out1,
       demultiplexer_1_out2, demultiplexer_1_out4, demultiplexer_1_out6, demultiplexer_1_out7,
       demultiplexer_2_out1, demultiplexer_2_out2, demultiplexer_3_out0, demultiplexer_3_out1,
       demultiplexer_4_out1, demultiplexer_4_out2, demultiplexer_5_out1, demultiplexer_5_out2,
       demultiplexer_5_out3, demultiplexer_5_out4, demultiplexer_5_out7, Instruction_Register_q, or_2_out,
       or_3_out, or_5_out, pull_resistor_1_node;

  Demultiplexer #(.select(3), .width(32), .enable("false")) demultiplexer_1 (
    .out0(demultiplexer_1_out0), .out1(demultiplexer_1_out1), .out2(demultiplexer_1_out2),
    .out4(demultiplexer_1_out4), .out6(demultiplexer_1_out6), .out7(demultiplexer_1_out7), .in(Data_OUT__IN),
    .sel(cpu_instructions_1_data_out____in_selector));  // open: out3, out5
  assign Data_IN__OUT = demultiplexer_5_out3 | demultiplexer_2_out2 | demultiplexer_3_out0 | adder_1_out | demultiplexer_4_out1;  // OR_Gate or_1, 32 bits wide
  Pull_Resistor pull_resistor_1 (.node(pull_resistor_1_node));
  assign pull_resistor_1_node = cpu_instructions_1_inc_dec[1] ? {32{1'b1}} : 32'bz;  // Controlled_Buffer controlled_buffer_1
  Adder #(.width(32)) adder_1 (
    .a(pull_resistor_1_node), .b(demultiplexer_1_out6), .out(adder_1_out), .cin(cpu_instructions_1_inc_dec[0]));  // open: cout
  assign buffer_1_out = bit_extender_1_out;  // Buffer buffer_1, 32 bits wide
  assign bit_extender_1_out = {{8{1'b0}}, Current_Address};  // Bit_Extender bit_extender_1
  Demultiplexer #(.select(2), .width(32), .enable("false")) demultiplexer_2 (
    .out1(demultiplexer_2_out1), .out2(demultiplexer_2_out2), .in(External_Input),
    .sel(cpu_instructions_1_exi_dmx));  // open: out0, out3
  assign buffer_2_out = buffer_3_out;  // Buffer buffer_2, 32 bits wide
  assign buffer_3_out = buffer_1_out;  // Buffer buffer_3, 32 bits wide
  assign buffer_4_out = buffer_2_out;  // Buffer buffer_4, 32 bits wide
  assign buffer_5_out = buffer_4_out;  // Buffer buffer_5, 32 bits wide
  Demultiplexer #(.width(32), .disabled(0)) demultiplexer_3 (
    .out0(demultiplexer_3_out0), .out1(demultiplexer_3_out1), .in(buffer_6_out),
    .sel(cpu_instructions_1_store_current_address[1]), .en(Store_Current_Address));
  assign buffer_6_out = buffer_5_out;  // Buffer buffer_6, 32 bits wide
  Register #(.width(32), .trigger("low")) Instruction_Register (
    .D(demultiplexer_1_out0), .Q(Instruction_Register_q), .clk(pull_resistor_2_node), .clr(Clock));  // open: en
  BitFinder #(.width(32)) bitfinder_1 (.in(Instruction_Register_q), .found(bitfinder_1_found));  // open: index
  Pull_Resistor pull_resistor_2 (.node(pull_resistor_2_node));
  Transistor #(.gate("br")) transistor_1 (.in(bitfinder_1_found), .out(pull_resistor_2_node), .gate(Reset));
  Demultiplexer #(.select(2), .width(32), .enable("false")) demultiplexer_4 (
    .out1(demultiplexer_4_out1), .out2(demultiplexer_4_out2), .in(ACC),
    .sel(cpu_instructions_1_acc_out_selector));  // open: out0, out3
  CPU____ALU cpu_alu_1 (
    .A(ACC), .B(or_2_out), .Seletor(cpu_instructions_1_alu_selector), .Out(cpu_alu_1_out),
    .ALU_Flag(cpu_alu_1_alu_flag));  // open: Out2
  assign or_2_out = demultiplexer_5_out2 | demultiplexer_1_out2;  // OR_Gate or_2, 32 bits wide
  assign or_3_out = demultiplexer_5_out1 | demultiplexer_1_out1 | demultiplexer_2_out1 | demultiplexer_3_out1 | cpu_alu_1_out;  // OR_Gate or_3, 32 bits wide
  assign buffer_7_out = or_3_out;  // Buffer buffer_7, 32 bits wide
  assign buffer_8_out = buffer_7_out;  // Buffer buffer_8, 32 bits wide
  Register #(.width(32), .trigger("falling")) Accumulator (
    .D(buffer_8_out), .Q(ACC), .clk(cpu_instructions_1_accumulator_clock), .clr(Reset));  // open: en
  assign External_Output__Console_etc = demultiplexer_5_out4 | demultiplexer_4_out2 | demultiplexer_1_out4;  // OR_Gate or_4, 32 bits wide
  Demultiplexer #(.select(3), .width(32), .enable("false")) demultiplexer_5 (
    .out1(demultiplexer_5_out1), .out2(demultiplexer_5_out2), .out3(demultiplexer_5_out3),
    .out4(demultiplexer_5_out4), .out7(demultiplexer_5_out7), .in(cpu_instructions_1_data_instructions_out),
    .sel(cpu_instructions_1_data_instructions_out_selector));  // open: out0, out5, out6
  CPU____Instructions cpu_instructions_1 (
    .Data_In(Instruction_Register_q), .Data_Instructions_Out(cpu_instructions_1_data_instructions_out),
    .Address_Out(Address_Out),
    .Data_Instructions_Out_Selector(cpu_instructions_1_data_instructions_out_selector),
    .ALU_Selector(cpu_instructions_1_alu_selector), .FLAGs(cpu_alu_1_alu_flag), .JUMP(Jump),
    .Data_Out____In_Selector(cpu_instructions_1_data_out____in_selector),
    .Accumulator_Clock(cpu_instructions_1_accumulator_clock), .Address_Commands(Adress_Commands), .Acc(ACC),
    .Return_Value_Adder(Return_value_adder), .External_Controller_Selector(External_Controller_Selector),
    .EXI_DMX(cpu_instructions_1_exi_dmx), .Inc_Dec(cpu_instructions_1_inc_dec),
    .Acc_Out_Selector(cpu_instructions_1_acc_out_selector),
    .Store_Current_Address({cpu_instructions_1_store_current_address[1], Store_Current_Address}));  // open: Set_Relative_Address
  assign or_5_out = demultiplexer_5_out7 | demultiplexer_1_out7;  // OR_Gate or_5, 32 bits wide
  Bit_Extender #(.in_width(32), .out_width(24)) bit_extender_2 (.in(or_5_out), .out(Set_Relative_Address[23:0]));

  // Notes on the sheet:
  //   These buffers exists to fix bugs on Store Current Address on Accumulator.
  //   ACC DMX
  //   Instruction Data Out DMX
  //   *
endmodule

module CPU____ALU (
  input  [31:0] A,
  input  [31:0] B,
  input  [4:0] Seletor,
  output [3:0] ALU_Flag,
  output [31:0] Out2,
  output [31:0] Out
);

  wire bitfinder_1_found, decoder_1_out1, decoder_1_out2, decoder_1_out3, decoder_1_out4, decoder_1_out5,
       or_1_out, or_2_out, or_3_out, pull_resistor_20_node, subtractor_1_bout;
  wire [2:0] pull_resistor_24_node;
  wire [4:0] bit_extender_1_out, bit_extender_2_out, bit_extender_3_out, bit_extender_4_out;
  wire [31:0] adder_1_out, and_1_out, demultiplexer_1_out1, demultiplexer_1_out2, demultiplexer_1_out3,
       demultiplexer_1_out4, demultiplexer_1_out5, demultiplexer_1_out6, demultiplexer_1_out7,
       demultiplexer_1_out8, demultiplexer_1_out9, demultiplexer_1_out10, demultiplexer_1_out11,
       demultiplexer_1_out12, demultiplexer_1_out13, demultiplexer_1_out14, demultiplexer_1_out15,
       demultiplexer_1_out30, demultiplexer_1_out31, demultiplexer_2_out1, demultiplexer_2_out2,
       demultiplexer_2_out3, demultiplexer_2_out4, demultiplexer_2_out5, demultiplexer_2_out6,
       demultiplexer_2_out7, demultiplexer_2_out8, demultiplexer_2_out9, demultiplexer_2_out10,
       demultiplexer_2_out11, demultiplexer_2_out12, demultiplexer_2_out13, demultiplexer_2_out14,
       demultiplexer_2_out15, divider_1_out, multiplier_1_out, nand_1_out, negator_1_out, nor_1_out,
       not_1_out, or_4_out, pull_resistor_23_node, shifter_1_out, shifter_2_out, shifter_3_out,
       shifter_4_out, subtractor_1_out, xnor_1_out, xor_1_out;

  Decoder #(.select(3), .disabled(0), .enable("false")) decoder_1 (
    .out1(decoder_1_out1), .out2(decoder_1_out2), .out3(decoder_1_out3), .out4(decoder_1_out4),
    .out5(decoder_1_out5), .sel(Seletor[2:0]));  // open: out0, out6, out7
  Demultiplexer #(.select(5), .width(32), .tristate("true"), .disabled(0), .enable("false")) demultiplexer_1 (
    .out1(demultiplexer_1_out1), .out2(demultiplexer_1_out2), .out3(demultiplexer_1_out3),
    .out4(demultiplexer_1_out4), .out5(demultiplexer_1_out5), .out6(demultiplexer_1_out6),
    .out7(demultiplexer_1_out7), .out8(demultiplexer_1_out8), .out9(demultiplexer_1_out9),
    .out10(demultiplexer_1_out10), .out11(demultiplexer_1_out11), .out12(demultiplexer_1_out12),
    .out13(demultiplexer_1_out13), .out14(demultiplexer_1_out14), .out15(demultiplexer_1_out15),
    .out30(demultiplexer_1_out30), .out31(demultiplexer_1_out31), .in(A), .sel(Seletor));  // open: out0, out16, out17, out18, out19, out20, out21, out22, out23, out24, out25, out26, out27, out28, out29
  Demultiplexer #(.select(5), .width(32), .tristate("true"), .disabled(0), .enable("false")) demultiplexer_2 (
    .out1(demultiplexer_2_out1), .out2(demultiplexer_2_out2), .out3(demultiplexer_2_out3),
    .out4(demultiplexer_2_out4), .out5(demultiplexer_2_out5), .out6(demultiplexer_2_out6),
    .out7(demultiplexer_2_out7), .out8(demultiplexer_2_out8), .out9(demultiplexer_2_out9),
    .out10(demultiplexer_2_out10), .out11(demultiplexer_2_out11), .out12(demultiplexer_2_out12),
    .out13(demultiplexer_2_out13), .out14(demultiplexer_2_out14), .out15(demultiplexer_2_out15), .in(B),
    .sel(Seletor));  // open: out0, out16, out17, out18, out19, out20, out21, out22, out23, out24, out25, out26, out27, out28, out29, out30, out31
  or or_1 (or_1_out, decoder_1_out1, decoder_1_out2, or_2_out);
  or or_2 (or_2_out, decoder_1_out3, decoder_1_out4);
  Pull_Resistor pull_resistor_1 (.node(demultiplexer_1_out2));
  Pull_Resistor pull_resistor_2 (.node(demultiplexer_1_out4));
  Pull_Resistor pull_resistor_3 (.node(demultiplexer_1_out6));
  Pull_Resistor pull_resistor_4 (.node(demultiplexer_1_out7));
  Pull_Resistor pull_resistor_5 (.node(demultiplexer_1_out8));
  Pull_Resistor #(.pull(1)) pull_resistor_6 (.node(demultiplexer_1_out9));
  Pull_Resistor #(.pull(1)) pull_resistor_7 (.node(demultiplexer_1_out11));
  Pull_Resistor pull_resistor_8 (.node(demultiplexer_1_out13));
  Pull_Resistor pull_resistor_9 (.node(demultiplexer_2_out2));
  Pull_Resistor pull_resistor_10 (.node(demultiplexer_2_out7));
  Pull_Resistor pull_resistor_11 (.node(demultiplexer_2_out8));
  Pull_Resistor #(.pull(1)) pull_resistor_12 (.node(demultiplexer_2_out9));
  Pull_Resistor #(.pull(1)) pull_resistor_13 (.node(demultiplexer_2_out10));
  Pull_Resistor pull_resistor_14 (.node(demultiplexer_2_out11));
  Pull_Resistor pull_resistor_15 (.node(demultiplexer_1_out5));
  Pull_Resistor pull_resistor_16 (.node(demultiplexer_2_out12));
  Pull_Resistor pull_resistor_17 (.node(demultiplexer_2_out13));
  Pull_Resistor pull_resistor_18 (.node(demultiplexer_2_out14));
  Pull_Resistor pull_resistor_19 (.node(demultiplexer_2_out15));
  Pull_Resistor pull_resistor_20 (.node(pull_resistor_20_node));
  Bit_Extender #(.in_width(32), .out_width(5)) bit_extender_1 (.in(demultiplexer_2_out12), .out(bit_extender_1_out));
  Bit_Extender #(.in_width(32), .out_width(5)) bit_extender_2 (.in(demultiplexer_2_out13), .out(bit_extender_2_out));
  Bit_Extender #(.in_width(32), .out_width(5)) bit_extender_3 (.in(demultiplexer_2_out14), .out(bit_extender_3_out));
  Bit_Extender #(.in_width(32), .out_width(5)) bit_extender_4 (.in(demultiplexer_2_out15), .out(bit_extender_4_out));
  Pull_Resistor #(.pull(1)) pull_resistor_21 (.node(demultiplexer_1_out30));
  Pull_Resistor pull_resistor_22 (.node(demultiplexer_1_out31));
  Pull_Resistor pull_resistor_23 (.node(pull_resistor_23_node));
  or or_3 (or_3_out, subtractor_1_bout, pull_resistor_20_node, bitfinder_1_found);
  Adder #(.width(32)) adder_1 (
    .a(demultiplexer_1_out1), .b(demultiplexer_2_out1), .out(adder_1_out), .cout(pull_resistor_20_node));  // open: cin
  Subtractor #(.width(32)) subtractor_1 (
    .a(demultiplexer_1_out2), .b(demultiplexer_2_out2), .out(subtractor_1_out), .bout(subtractor_1_bout));  // open: bin
  Multiplier #(.width(32)) multiplier_1 (
    .a(demultiplexer_1_out3), .b(demultiplexer_2_out3), .out(multiplier_1_out), .cout(pull_resistor_23_node));  // open: cin
  Divider #(.width(32)) divider_1 (
    .a(demultiplexer_1_out4), .b(demultiplexer_2_out4), .out(divider_1_out), .rem(pull_resistor_23_node));  // open: upper
  Pull_Resistor pull_resistor_24 (.node(pull_resistor_24_node));
  Comparator #(.width(32), .mode("unsigned")) comparator_1 (
    .a(demultiplexer_1_out5), .b(demultiplexer_2_out5), .gt(pull_resistor_24_node[2]),
    .eq(pull_resistor_24_node[1]), .lt(pull_resistor_24_node[0]));
  assign and_1_out = demultiplexer_1_out6 & demultiplexer_2_out6;  // AND_Gate and_1, 32 bits wide
  assign or_4_out = demultiplexer_1_out7 | demultiplexer_2_out7;  // OR_Gate or_4, 32 bits wide
  assign xor_1_out = demultiplexer_1_out8 ^ demultiplexer_2_out8;  // XOR_Gate xor_1, 32 bits wide
  assign nand_1_out = ~(demultiplexer_1_out9 & demultiplexer_2_out9);  // NAND_Gate nand_1, 32 bits wide
  assign nor_1_out = ~(demultiplexer_1_out10 | demultiplexer_2_out10);  // NOR_Gate nor_1, 32 bits wide
  assign xnor_1_out = ~(demultiplexer_1_out11 ^ demultiplexer_2_out11);  // XNOR_Gate xnor_1, 32 bits wide
  Shifter #(.width(32)) shifter_1 (.in(demultiplexer_1_out12), .\dist (bit_extender_1_out), .out(shifter_1_out));
  Shifter #(.width(32), .shift("lr")) shifter_2 (
    .in(demultiplexer_1_out13), .\dist (bit_extender_2_out), .out(shifter_2_out));
  Shifter #(.width(32), .shift("rl")) shifter_3 (
    .in(demultiplexer_1_out14), .\dist (bit_extender_3_out), .out(shifter_3_out));
  Shifter #(.width(32), .shift("rr")) shifter_4 (
    .in(demultiplexer_1_out15), .\dist (bit_extender_4_out), .out(shifter_4_out));
  assign not_1_out = ~demultiplexer_1_out30;  // NOT_Gate not_1, 32 bits wide
  Negator #(.width(32)) negator_1 (.in(demultiplexer_1_out31), .out(negator_1_out));
  Register #(.width(1), .trigger("high")) Carry_Flag (.en(or_3_out), .Q(ALU_Flag[3]), .clk(or_1_out));  // open: D, clr
  BitFinder #(.width(32)) bitfinder_1 (.in(pull_resistor_23_node), .found(bitfinder_1_found));  // open: index
  Register #(.width(3), .trigger("high")) CMP_Flag (
    .D(pull_resistor_24_node), .Q(ALU_Flag[2:0]), .clk(decoder_1_out5));  // open: en, clr
  Pull_Resistor pull_resistor_25 (.node(shifter_1_out));
  Pull_Resistor pull_resistor_26 (.node(shifter_2_out));
  Pull_Resistor pull_resistor_27 (.node(shifter_3_out));
  Pull_Resistor pull_resistor_28 (.node(shifter_4_out));
  Register #(.width(32)) register_1 (.D(pull_resistor_23_node), .Q(Out2), .clk(or_2_out));  // open: en, clr
  Pull_Resistor pull_resistor_29 (.node(adder_1_out));
  Pull_Resistor pull_resistor_30 (.node(subtractor_1_out));
  Pull_Resistor pull_resistor_31 (.node(multiplier_1_out));
  Pull_Resistor pull_resistor_32 (.node(divider_1_out));
  assign Out = adder_1_out | subtractor_1_out | multiplier_1_out | divider_1_out | and_1_out | or_4_out | xor_1_out | nand_1_out | nor_1_out | xnor_1_out | demultiplexer_1_out5 | shifter_1_out | shifter_2_out | shifter_3_out | shifter_4_out | not_1_out | negator_1_out;  // OR_Gate or_5, 32 bits wide

  // Notes on the sheet:
  //   ALU Selector:
  //   6 = AND
  //   7 = OR
  //   8 = XOR
  //   9 = NAND
  //   10 = NOR
  //   12 = SHL
  //   13 = SHR
  //   14 = ROL
  //   15 = ROR
  //   0 = Nothing
  //   1 = ADD, Sum
  //   2 = SUB, Substract
  //   3 = MUL, Multiplication
  //   4 = DIV, Divide
  //   5 = CMP, Compare
  //   11 = XNOR
  //   16~29 = Unused
  //   30 = NOT
  //   31 = NEG
  //   NOT
  //   NEG
  //   This wire is to keep the value
  //   on acc when comparing
  //   _________
  //   The Carry Flag can mean:
  //   Carry out from ADD
  //   Burrow out from SUB
  //   There is Carry out from MUL
  //   There is Remain from DIV
  //   _________
endmodule

module CPU____Instructions (
  input  [31:0] Data_In,
  input  [31:0] Acc,
  input  [3:0] FLAGs,
  output Accumulator_Clock,
  output [7:0] External_Controller_Selector,
  output [4:0] ALU_Selector,
  output [2:0] Data_Instructions_Out_Selector,
  output [1:0] Acc_Out_Selector,
  output [2:0] Data_Out____In_Selector,
  output [31:0] Data_Instructions_Out,
  output [23:0] Address_Out,
  output [23:0] Return_Value_Adder,
  output [1:0] EXI_DMX,
  output [1:0] Set_Relative_Address,
  output [1:0] Store_Current_Address,
  output [3:0] Address_Commands,
  output [1:0] Inc_Dec,
  output [2:0] JUMP
);

  wire ALU, ALU_0, ALU_1, bitfinder_1_found, comparator_1_eq, decoder_1_out2, decoder_2_out2, decoder_2_out4,
       decoder_5_out1, demultiplexer_2_out1, ERS, EXI, EXO, EXO_0, EXO_1, INC_DEC_1bit, JMP_0, MOV, MOV_0,
       MOV_1, or_1_out, or_3_out, or_4_out, or_5_out, or_6_out, pull_resistor_4_node, pull_resistor_6_node,
       pull_resistor_7_node, pull_resistor_9_node, pull_resistor_10_node, pull_resistor_11_node,
       pull_resistor_12_node, pull_resistor_15_node, SRA, SRA_0, SRA_1, STO_0, STO_1, SWP, transistor_4_out,
       transistor_5_out;
  wire [1:0] or_8_out;
  wire [4:0] demultiplexer_3_out0, demultiplexer_3_out2;
  wire [10:0] JUMPCodes;
  wire [23:0] demultiplexer_4_out1, pull_resistor_1_node;
  wire [31:0] controlled_buffer_2_out;

  or or_1 (or_1_out, EXI, EXO, SRA_1, Store_Current_Address[0]);
  Pull_Resistor pull_resistor_1 (.node(pull_resistor_1_node));
  Transistor #(.\type ("n"), .width(24)) transistor_1 (.in(Data_In[23:0]), .out(pull_resistor_1_node), .gate(or_1_out));
  Demultiplexer #(.disabled(0), .enable("false")) demultiplexer_1 (
    .out0(EXI_DMX[0]), .out1(EXI_DMX[1]), .in(EXI), .sel(bitfinder_1_found));
  Demultiplexer #(.disabled(0), .enable("false")) demultiplexer_2 (
    .out0(Store_Current_Address[1]), .out1(demultiplexer_2_out1), .in(Store_Current_Address[0]),
    .sel(bitfinder_1_found));
  Demultiplexer #(.select(2), .width(5), .enable("false")) demultiplexer_3 (
    .out0(demultiplexer_3_out0), .out1(ALU_Selector), .out2(demultiplexer_3_out2), .in(Data_In[28:24]),
    .sel(Data_In[30:29]));  // open: out3
  Decoder #(.select(2), .enable("false")) decoder_1 (
    .out2(decoder_1_out2), .sel(Data_In[30:29]));  // open: out0, out1, out3
  BitFinder #(.width(24)) bitfinder_1 (.in(pull_resistor_1_node), .found(bitfinder_1_found));  // open: index
  Transistor #(.\type ("n")) transistor_2 (.in(SRA_1), .out(Set_Relative_Address[0]), .gate(bitfinder_1_found));
  Pull_Resistor pull_resistor_2 (.node(Set_Relative_Address));
  Pull_Resistor pull_resistor_3 (.node(Acc_Out_Selector[1]));
  Transistor transistor_3 (.in(EXO), .out(Acc_Out_Selector[1]), .gate(bitfinder_1_found));
  Pull_Resistor pull_resistor_4 (.node(pull_resistor_4_node));
  assign pull_resistor_4_node = FLAGs[0] ? JUMPCodes[5] : 1'bz;  // Controlled_Buffer controlled_buffer_1
  Pull_Resistor pull_resistor_5 (.node(EXI_DMX[1]));
  or or_2 (INC_DEC_1bit, Inc_Dec[0], Inc_Dec[1]);
  or or_3 (or_3_out, JUMPCodes[1], JUMPCodes[2]);
  assign controlled_buffer_2_out = or_3_out ? Acc : 32'bz;  // Controlled_Buffer controlled_buffer_2
  Comparator #(.width(32), .mode("unsigned")) comparator_1 (
    .a(controlled_buffer_2_out), .b({32{1'b0}}), .eq(comparator_1_eq));  // open: gt, lt
  Pull_Resistor pull_resistor_6 (.node(pull_resistor_6_node));
  assign pull_resistor_6_node = or_4_out ? JUMPCodes[6] : 1'bz;  // Controlled_Buffer controlled_buffer_3
  Pull_Resistor pull_resistor_7 (.node(pull_resistor_7_node));
  assign pull_resistor_7_node = FLAGs[1] ? JUMPCodes[7] : 1'bz;  // Controlled_Buffer controlled_buffer_4
  or or_4 (or_4_out, FLAGs[0], FLAGs[1]);
  or or_5 (or_5_out, FLAGs[1], FLAGs[2]);
  or or_6 (or_6_out, FLAGs[0], FLAGs[2]);
  Decoder #(.select(5), .enable("false")) decoder_2 (
    .out1(MOV), .out2(decoder_2_out2), .out3(ERS), .out4(decoder_2_out4), .out8(JUMPCodes[0]),
    .out9(JUMPCodes[1]), .out10(JUMPCodes[2]), .out11(JUMPCodes[3]), .out12(JUMPCodes[4]),
    .out13(JUMPCodes[5]), .out14(JUMPCodes[6]), .out15(JUMPCodes[7]), .out16(JUMPCodes[8]),
    .out17(JUMPCodes[9]), .out18(JUMPCodes[10]), .out19(JUMP[2]), .out20(External_Controller_Selector[0]),
    .out21(External_Controller_Selector[1]), .out22(External_Controller_Selector[2]),
    .out23(External_Controller_Selector[3]), .out24(External_Controller_Selector[4]),
    .out25(External_Controller_Selector[5]), .out26(External_Controller_Selector[6]),
    .out27(External_Controller_Selector[7]), .out28(Inc_Dec[0]), .out29(Inc_Dec[1]),
    .out30(Store_Current_Address[0]), .out31(SRA), .sel(demultiplexer_3_out0));  // open: out0, out5, out6, out7
  Decoder #(.select(5), .disabled(0)) decoder_3 (
    .sel(demultiplexer_3_out2), .en(decoder_1_out2));  // open: out0, out1, out2, out3, out4, out5, out6, out7, out8, out9, out10, out11, out12, out13, out14, out15, out16, out17, out18, out19, out20, out21, out22, out23, out24, out25, out26, out27, out28, out29, out30, out31
  Pull_Resistor pull_resistor_8 (.node(comparator_1_eq));
  Pull_Resistor pull_resistor_9 (.node(pull_resistor_9_node));
  assign pull_resistor_9_node = JUMPCodes[1] ? comparator_1_eq : 1'bz;  // Controlled_Buffer controlled_buffer_5
  Pull_Resistor pull_resistor_10 (.node(pull_resistor_10_node));
  assign pull_resistor_10_node = JUMPCodes[2] ? ~comparator_1_eq : 1'bz;  // Controlled_Inverter controlled_inverter_1
  Pull_Resistor pull_resistor_11 (.node(pull_resistor_11_node));
  assign pull_resistor_11_node = or_5_out ? JUMPCodes[8] : 1'bz;  // Controlled_Buffer controlled_buffer_6
  Pull_Resistor pull_resistor_12 (.node(pull_resistor_12_node));
  assign pull_resistor_12_node = FLAGs[2] ? JUMPCodes[9] : 1'bz;  // Controlled_Buffer controlled_buffer_7
  or or_7 (Acc_Out_Selector[0], decoder_2_out2, SWP);
  assign SWP = Data_In[31] ? decoder_2_out4 : 1'bz;  // Controlled_Buffer controlled_buffer_8
  Pull_Resistor pull_resistor_13 (.node(SWP));
  Demultiplexer #(.select(2), .width(24), .enable("false")) demultiplexer_4 (
    .out1(demultiplexer_4_out1), .out2(Address_Out), .out3(Return_Value_Adder), .in(Data_In[23:0]),
    .sel(or_8_out));  // open: out0
  or or_8 (or_8_out[0], EXO_0, MOV_0, ALU_0, JUMP[2]);
  or or_9 (or_8_out[1], MOV_1, JUMP[0], EXO_1, ERS, STO_0, ALU_1, demultiplexer_2_out1, INC_DEC_1bit);
  Transistor #(.gate("br")) transistor_4 (.in(JUMPCodes[4]), .out(transistor_4_out), .gate(FLAGs[3]));
  Transistor #(.\type ("n")) transistor_5 (.in(FLAGs[3]), .out(transistor_5_out), .gate(JUMPCodes[3]));
  Pull_Resistor pull_resistor_14 (.node(transistor_5_out));
  Pull_Resistor pull_resistor_15 (.node(pull_resistor_15_node));
  assign pull_resistor_15_node = or_6_out ? JUMPCodes[10] : 1'bz;  // Controlled_Buffer controlled_buffer_9
  BitFinder #(.width(4)) bitfinder_2 (.in(External_Controller_Selector[3:0]), .found(EXO));  // open: index
  BitFinder #(.width(4)) bitfinder_3 (.in(External_Controller_Selector[7:4]), .found(EXI));  // open: index
  assign Data_Instructions_Out = {{8{1'b0}}, demultiplexer_4_out1};  // Bit_Extender bit_extender_1
  or or_10 (JUMP[0], JUMPCodes[0], transistor_4_out, transistor_5_out, pull_resistor_9_node, pull_resistor_10_node, pull_resistor_4_node, pull_resistor_6_node, pull_resistor_7_node, pull_resistor_11_node, pull_resistor_12_node, pull_resistor_15_node, JUMP[2]);
  or or_11 (Accumulator_Clock, EXI_DMX[0], Store_Current_Address[1], ALU, MOV, SWP);
  BitFinder #(.width(5)) bitfinder_4 (.in(ALU_Selector), .found(ALU));  // open: index
  Decoder #(.disabled(0)) decoder_4 (.out0(ALU_0), .out1(ALU_1), .sel(Data_In[31]), .en(ALU));
  Decoder #(.disabled(0)) decoder_5 (.out0(MOV_0), .out1(decoder_5_out1), .sel(Data_In[31]), .en(MOV));
  Decoder #(.disabled(0)) decoder_6 (.out0(JMP_0), .out1(JUMP[1]), .sel(Data_In[31]), .en(JUMP[0]));
  Decoder #(.disabled(0)) decoder_7 (.out0(STO_0), .out1(STO_1), .sel(Data_In[31]), .en(Acc_Out_Selector[0]));
  Decoder #(.disabled(0)) decoder_8 (.out0(EXO_0), .out1(EXO_1), .sel(Data_In[31]), .en(EXO));
  Decoder #(.disabled(0)) decoder_9 (.out0(SRA_0), .out1(SRA_1), .sel(Data_In[31]), .en(SRA));
  or or_12 (MOV_1, decoder_5_out1, SWP);
  or or_13 (Address_Commands[2], INC_DEC_1bit, SWP);
  or Store_Or_Gate (Address_Commands[0], demultiplexer_2_out1, ERS, INC_DEC_1bit, EXI_DMX[1], Acc_Out_Selector[0]);
  Pull_Resistor pull_resistor_16 (.node(Address_Commands[3]));
  or or_14 (Address_Commands[1], ALU_1, MOV_1, JUMP[1], EXO_1, INC_DEC_1bit);
  buf or_15 (Data_Instructions_Out_Selector[0], MOV_0);  // OR_Gate
  buf or_16 (Data_Instructions_Out_Selector[1], ALU_0);  // OR_Gate
  buf or_17 (Data_Instructions_Out_Selector[2], EXO_0);  // OR_Gate
  buf or_18 (Data_Out____In_Selector[0], MOV_1);  // OR_Gate
  or or_19 (Data_Out____In_Selector[1], ALU_1, INC_DEC_1bit);
  or or_20 (Data_Out____In_Selector[2], INC_DEC_1bit, EXO_1);

  // Other names for the same wires on the sheet: STO = Acc_Out_Selector[0];
  //   Addres_Read_from_value = Address_Commands[1]; _32_prime_bit = Data_In[31]; EXI_ACC = EXI_DMX[0];
  //   EXO_t[3:0] = External_Controller_Selector[3:0]; EXI_t[3:0] = External_Controller_Selector[7:4]; JMP = JUMP[0];
  //   JMP_1 = JUMP[1]; RTN = JUMP[2]; SCA = Store_Current_Address[0]; SCA_ACC = Store_Current_Address[1]

  // Notes on the sheet:
  //   Data_In: pull=down
  //   Store Current Address
  //   1 = Store on given Address
  //   3 = Store on Accumulator
  //   JL
  //   JLE
  //   INC
  //   DEC
  //   ---Jump Codes Instruction---
  //   JE
  //   JGE
  //   MOV
  //   STO
  //   ERS
  //   SWP
  //   JMP
  //   JZ
  //   JNZ
  //   JC
  //   JNC
  //   JL
  //   JLE
  //   JE
  //   JGE
  //   JG
  //   JNE
  //   RTN
  //   TXT
  //   KEY
  //   SCA
  //   SRA
  //   External Input DMX
  //   0 = Nothing
  //   1 = Accumulator
  //   3 = Data In -> Out
  //   JG
  //   JNE
  //   24bit "Data In" DMX
  //   0 = Nothing
  //   1 = Data Out
  //   2 = Adress
  //   Set Relative Address
  //   1 = Use the current Address
  //   3 = Use the given value
  //   3 = Special (only rtn for now)
  //   Jump:
  //   =1 to Jump from direct value
  //   =3 to Jump from address value (1+2)
  //   =5 to Return to Address before the Jump value (4+1)
  //   Note that SWP will also trigger Address Read from value
  //   XYZ 0 Usually stands for direct data mode
  //   While XYZ 1 will usually stands for indirect data mode.
  //   0 = Nothing
  //   2 = ALU B
  //   0 = Nothing
  //   _________
  //   23th & 24th chooses the memory device:
  //   0 = RAM
  //   1~22bits for the address value
  //   _________
  //   Address Commands
  //   1st bit to Store
  //   2nd/3rd bit Addres Read from value
  //   4th to Reset the device
  //   _________
  //   ALU Selector:
  //   0 = Nothing
  //   1 = ADD, Sum
  //   2 = SUB, Substract
  //   3 = MUL, Multiplication
  //   4 = DIV, Divide
  //   5 = CMP, Compare
  //   6 = AND
  //   7 = OR
  //   8 = XOR
  //   9 = NND (NAND)
  //   10 = NOR
  //   11 = XNR (XNOR)
  //   12 = SHL
  //   13 = SHR
  //   14 = ROL
  //   15 = ROR
  //   _________
  //   _________
  //   Data Instructions Out Dest Selector:
  //   1 = ACCUMULATOR
  //   3 = Data In > Out
  //   4 = Console text
  //   5 = Return Value Adder
  //   _________
  //   ACCUMULATOR DEST SELECTOR:
  //   1 = DATA OUT
  //   2 = External Devices Controller
  //   _________
  //   Data Out -> In Selector
  //   0 = Instructions
  //   1 = Accumulator
  //   2 = ALU B
  //   4 = Console
  //   6 = Inc/Dec
  //   30 = NOT
  //   31 = NEG
  //   16~29 = Unused
endmodule

module Console_Back (
  input  [31:0] Console_Data_Clear,
  input  Power,
  input  Clock_1_1,
  output [6:0] Data,
  output Clear,
  output _4Clock_2On_2Off
);

  wire bitfinder_1_found, buffer_1_out, buffer_2_out, buffer_3_out, counter_1_carry, d_ff_1_q,
       n2signals_turn_off_1_out_2, n2signals_turn_off_2_out_2, not_1_out, not_2_out, or_1_out, or_2_out,
       pull_resistor_2_node, transistor_1_out, transistor_4_out, transistor_5_out;
  wire [1:0] counter_1_q;
  wire [31:0] register_1_q;

  Transistor #(.\type ("n"), .gate("br")) transistor_1 (
    .in(bitfinder_1_found), .out(transistor_1_out), .gate(d_ff_1_q));
  Pull_Resistor pull_resistor_1 (.node(transistor_1_out));
  BitFinder #(.width(32)) bitfinder_1 (.in(Console_Data_Clear), .found(bitfinder_1_found));  // open: index
  D_Flip_Flop d_ff_1 (
    .clk(bitfinder_1_found), .D(bitfinder_1_found), .Q(d_ff_1_q), .reset(or_1_out));  // open: Qn, preset, en
  Pull_Resistor pull_resistor_2 (.node(pull_resistor_2_node));
  Transistor #(.\type ("n")) transistor_2 (.in(Clock_1_1), .out(pull_resistor_2_node), .gate(transistor_1_out));
  Register #(.width(32), .trigger("high")) register_1 (
    .D(Console_Data_Clear), .Q(register_1_q), .clk(pull_resistor_2_node), .clr(or_1_out));  // open: en
  or or_1 (or_1_out, not_1_out, counter_1_carry);
  buf buffer_1 (buffer_1_out, pull_resistor_2_node);
  buf buffer_2 (buffer_2_out, buffer_1_out);
  Transistor #(.gate("br")) transistor_3 (.in(not_1_out), .out(Clear), .gate(buffer_3_out));
  Pull_Resistor pull_resistor_3 (.node(Clear));
  not not_1 (not_1_out, Power);
  not not_2 (not_2_out, buffer_2_out);
  buf buffer_3 (buffer_3_out, not_1_out);
  Transistor #(.gate("br")) transistor_4 (.in(buffer_2_out), .out(transistor_4_out), .gate(transistor_5_out));
  Pull_Resistor pull_resistor_4 (.node(transistor_4_out));
  _2Signals_Turn_OFF u_2signals_turn_off_1 (.in_1(transistor_4_out), .out_2(n2signals_turn_off_1_out_2));
  Transistor transistor_5 (.in(not_2_out), .out(transistor_5_out), .gate(buffer_2_out));
  Pull_Resistor pull_resistor_5 (.node(transistor_5_out));
  _2Signals_Turn_OFF u_2signals_turn_off_2 (.in_1(transistor_5_out), .out_2(n2signals_turn_off_2_out_2));
  Multiplexer #(.select(2), .width(7), .disabled(0), .enable("false")) multiplexer_1 (
    .in0(register_1_q[30:24]), .in1(register_1_q[22:16]), .in2(register_1_q[14:8]), .in3(register_1_q[6:0]),
    .out(Data), .sel(counter_1_q));
  Counter #(.width(2), .max('h3)) counter_1 (
    .Q(counter_1_q), .carry(counter_1_carry), .clk(or_2_out), .clr(not_1_out));  // open: load, D, count
  assign _4Clock_2On_2Off = Power ? or_2_out : 1'bz;  // Controlled_Buffer controlled_buffer_1
  or or_2 (or_2_out, n2signals_turn_off_1_out_2, n2signals_turn_off_2_out_2);
  Pull_Resistor pull_resistor_6 (.node(_4Clock_2On_2Off));

  // Notes on the sheet:
  //   All these delayers for one problem:
  //   32th, 24th, 16th, 8th bits aren't used.
  //   But all bits in these intervals (7-bit sized) means a character.
  //   The writing on the console is made from left to right, first the 31~25 bit and so on.
  //   There is a propagation problem when using the Address mode (instead of direct data)
  //   The "Data Out -> In" MUX will change the destination, but will briefly keep it data.
  //   That the console (and any other device) will receive a very fast data equal to the original instruction.
  //   I don't know how to fix this yet, and it is giving me some headache. Maybe it will force me to change the clock system.
  //   Tips are welcomed.
endmodule

module Dual_Address_RAM_chip (
  input  [31:0] Data_In____Out,
  input  [31:0] Ext_Data_Out____In,
  input  [2:0] Controls,
  input  [21:0] Ext_Address_2__R,
  input  [21:0] Ext_Address_1__W,
  output [31:0] Ext_Data_In____Out,
  output [31:0] Data_Out____In,
  output Store,
  output Clock,
  output Focus,
  output Reset__Be_careful,
  output [21:0] Address_2__READ,
  output [21:0] Address_1__WRITE
);

  not not_1 (Focus, Controls[1]);

  assign Address_1__WRITE = Ext_Address_1__W;
  assign Address_2__READ = Ext_Address_2__R;
  assign Clock = Controls[0];
  assign Data_Out____In = Ext_Data_Out____In;
  assign Ext_Data_In____Out = Data_In____Out;
  assign Store = Controls[0];

  // Notes on the sheet:
  //   Labels texts are big here so you can read from the subcircuit appearance screen.
  //   See how I do everything for you guys? :) Just Mod mod mod mod mod and share!!
  //    [=CPU OUT -> IN]
  //    [=CPU IN -> OUT]
  //   *
  //   First to focus
  //   Sencond to Store
  //   Third to Reset
endmodule

module Keyboard_Back (
  input  There_is_char,
  input  [6:0] Keyboard_Data,
  input  Clock__Feedback,
  output [6:0] out_4,
  output Clock
);

  wire counter_1_q;

  Counter #(.width(1), .max('h1), .ongoal("stay")) counter_1 (
    .count(There_is_char), .Q(counter_1_q), .clk(Clock__Feedback), .clr(Clock));  // open: load, D, carry
  Register #(.width(1), .trigger("falling")) register_1 (
    .D(1'b1), .en(counter_1_q), .Q(Clock), .clk(Clock__Feedback), .clr(Clock));
  Transistor #(.\type ("n"), .width(7)) transistor_1 (.in(Keyboard_Data), .out(out_4), .gate(counter_1_q));
  Pull_Resistor pull_resistor_1 (.node(out_4));

  // Notes on the sheet:
  //   out_4: pull=down
  //   This reg fixes clock ignoring the first character.
  //   A lot time after getting some letters eating bugs, I got this working system. I surely don't know why it works, but it does.
  //   Did some random stuff, and         , it worked :O
  //   voilà
endmodule

module External_Devices_Controler (
  input  [6:0] Input_Device_1,
  input  [9:0] Input_Device_3,
  input  [31:0] Input_Device_4,
  input  [31:0] CPU_In_Out,
  input  [31:0] Input_Device_2,
  input  [7:0] Externak_Controller_Selector,
  output [31:0] Output_Device_1,
  output [31:0] Output_Device_2,
  output [31:0] Output_Device_3,
  output [31:0] CPU_Out_In,
  output [31:0] Output_Device_4,
  output _1FB,
  output _2FB,
  output _3FB,
  output _4FB
);

  wire [31:0] bit_extender_1_out, bit_extender_2_out, pull_resistor_1_node;

  assign bit_extender_1_out = {{25{1'b0}}, Input_Device_1};  // Bit_Extender bit_extender_1
  assign bit_extender_2_out = {{22{1'b0}}, Input_Device_3};  // Bit_Extender bit_extender_2
  Pull_Resistor pull_resistor_1 (.node(pull_resistor_1_node));
  Multiplexer #(.select(4), .width(32), .disabled(0), .enable("false")) multiplexer_1 (
    .in0(pull_resistor_1_node), .in1(bit_extender_1_out), .in2(Input_Device_2), .in4(bit_extender_2_out),
    .in8(Input_Device_4), .out(CPU_Out_In), .sel(Externak_Controller_Selector[7:4]));  // open: in3, in5, in6, in7, in9, in10, in11, in12, in13, in14, in15
  Decoder #(.select(4), .enable("false")) decoder_1 (
    .out1(_1FB), .out2(_2FB), .out4(_3FB), .out8(_4FB), .sel(Externak_Controller_Selector[7:4]));  // open: out0, out3, out5, out6, out7, out9, out10, out11, out12, out13, out14, out15
  Demultiplexer #(.select(4), .width(32), .enable("false")) demultiplexer_1 (
    .out1(Output_Device_1), .out2(Output_Device_2), .out4(Output_Device_3), .out8(Output_Device_4),
    .in(CPU_In_Out), .sel(Externak_Controller_Selector[3:0]));  // open: out0, out3, out5, out6, out7, out9, out10, out11, out12, out13, out14, out15

  // Notes on the sheet:
  //   Input_Device_1: pull=down
  //   By default, Keyboard
  //   Joystick
  //   FB = Feedback
  //   The feedback will send the external device a signal when it is acessed.
  //   For now it will use this immediate value to DMX as I think it's faster than putting OR gates on the CPU instruction
  //   to generate the specific DMX selector. But on the future that should change to be possible to hold more devices.
  //   Prob will be sound.
  //   Will probably be the GPU.
  //   By default, Console
  //   (or should I treat it as an Address?)
endmodule

module _2Signals_Turn_OFF (
  input  in_1,
  output out_2
);

  wire buffer_1_out, buffer_2_out, counter_1_q, or_1_out, pull_resistor_2_node;

  Transistor #(.gate("br")) transistor_1 (.in(or_1_out), .out(out_2), .gate(buffer_1_out));
  Pull_Resistor pull_resistor_1 (.node(out_2));
  buf buffer_1 (buffer_1_out, or_1_out);
  or or_1 (or_1_out, pull_resistor_2_node, counter_1_q);
  Pull_Resistor pull_resistor_2 (.node(pull_resistor_2_node));
  Transistor #(.gate("br")) transistor_2 (.in(in_1), .out(pull_resistor_2_node), .gate(counter_1_q));
  buf buffer_2 (buffer_2_out, or_1_out);
  Counter #(.width(1), .max('h1), .ongoal("stay")) counter_1 (
    .Q(counter_1_q), .clk(in_1), .clr(buffer_2_out));  // open: load, D, count, carry
endmodule

module Joystick_Back (
  input  [4:0] X,
  input  [4:0] Y,
  output [9:0] Output
);


  assign Output = {Y, X};
endmodule

module GPU_____External_Connections (
  input  Clock,
  output [7:0] out_2,
  output [7:0] out_3,
  output [7:0] out_4,
  output [7:0] out_5,
  output [7:0] out_6,
  output [7:0] out_7,
  output [7:0] out_8,
  output [7:0] out_9,
  output [7:0] out_10,
  output [7:0] out_11,
  output [7:0] out_12,
  output [7:0] out_13,
  output [7:0] out_14,
  output [7:0] out_15,
  output [7:0] out_16,
  output [7:0] out_17,
  output [7:0] out_18,
  output [7:0] out_19,
  output [7:0] out_20,
  output [7:0] out_21,
  output [7:0] out_22,
  output [7:0] out_23,
  output [7:0] out_24,
  output [7:0] out_25,
  output [7:0] out_26,
  output [7:0] out_27,
  output [7:0] out_28,
  output [7:0] out_29,
  output [7:0] out_30,
  output [7:0] out_31,
  output [7:0] out_32,
  output [7:0] out_33,
  output [7:0] out_34,
  output [7:0] out_35,
  output [7:0] out_36,
  output [7:0] out_37,
  output out_38,
  output [7:0] out_39,
  output [7:0] out_40,
  output [7:0] out_41,
  output [7:0] out_42,
  output [7:0] out_43,
  output [7:0] out_44,
  output [7:0] out_45,
  output [7:0] out_46,
  output [7:0] out_47,
  output [7:0] out_48,
  output [7:0] out_49,
  output [7:0] out_50
);

  wire ram_2_p1, ram_4_p1;
  wire [7:0] A, ram_2_p2;
  wire [31:0] undriven;

  Counter #(.ongoal("stay")) \Nº_Columns_current_object  ();  // open: load, D, count, Q, carry, clk, clr
  Counter #(.ongoal("stay")) \Nº_Columns_current_object_2  ();  // open: load, D, count, Q, carry, clk, clr
  GPU_____Color_replacer gpu_color_replacer_1 (.Object_color(undriven));  // open: out_5, Back_color_1, Back_color_2, out_6, Back_color_3, out_7
  GPU_____Color_replacer gpu_color_replacer_2 (.Object_color(undriven));  // open: out_5, Back_color_1, Back_color_2, out_6, Back_color_3, out_7
  GPU_____Color_replacer gpu_color_replacer_3 (.Object_color(undriven));  // open: out_5, Back_color_1, Back_color_2, out_6, Back_color_3, out_7
  // RAM ram_1: pin names not known
  // RAM ram_2: pin names not known; wires that end beside it: ram_2_p1, ram_2_p2, A
  GPU_____Color_replacer gpu_color_replacer_4 (.Object_color(undriven));  // open: out_5, Back_color_1, Back_color_2, out_6, Back_color_3, out_7
  GPU_____Color_replacer gpu_color_replacer_5 (.Object_color(undriven));  // open: out_5, Back_color_1, Back_color_2, out_6, Back_color_3, out_7
  GPU_____Color_replacer gpu_color_replacer_6 (.Object_color(undriven));  // open: out_5, Back_color_1, Back_color_2, out_6, Back_color_3, out_7
  Counter #(.max('hf)) counter_1 (.Q(ram_2_p2), .carry(out_38), .clk(Clock));  // open: load, D, count, clr
  // RAM ram_3: pin names not known
  // RAM ram_4: pin names not known; wires that end beside it: ram_4_p1, ram_2_p2, A
  // RAM ram_5: pin names not known
  // RAM ram_6: pin names not known; wires that end beside it: ram_4_p1, ram_2_p2, A
  // RAM ram_7: pin names not known; wires that end beside it: ram_4_p1, ram_2_p2, A
  // RAM ram_8: pin names not known; wires that end beside it: ram_4_p1, ram_2_p2, A
  // RAM ram_9: pin names not known; wires that end beside it: ram_4_p1, ram_2_p2, A
  // RAM ram_10: pin names not known; wires that end beside it: ram_4_p1, ram_2_p2, A
  // RAM ram_11: pin names not known; wires that end beside it: ram_4_p1, ram_2_p2, A
  // RAM ram_12: pin names not known; wires that end beside it: ram_4_p1, ram_2_p2, A
  // RAM ram_13: pin names not known; wires that end beside it: ram_4_p1, ram_2_p2, A
  // RAM ram_14: pin names not known; wires that end beside it: ram_4_p1, ram_2_p2, A
  // RAM ram_15: pin names not known; wires that end beside it: ram_4_p1, ram_2_p2, A, ram_2_p1
  // RAM ram_16: pin names not known; wires that end beside it: ram_4_p1

  // Notes on the sheet:
  //   Instructions RAM
  //   DATA RAM
endmodule

module GPU_____Color_replacer (
  input  [7:0] Back_color_1,
  input  [31:0] Object_color,
  input  [7:0] Back_color_2,
  input  [7:0] Back_color_3,
  output [7:0] out_5,
  output [7:0] out_6,
  output [7:0] out_7
);

  wire comparator_1_gt, comparator_2_gt, comparator_3_gt, comparator_4_gt, comparator_5_gt, comparator_6_gt,
       comparator_7_gt, comparator_8_gt, comparator_9_gt;
  wire [2:0] adder_1_out, adder_2_out, adder_3_out, adder_4_out, adder_5_out, adder_6_out, adder_7_out,
       adder_8_out, adder_9_out, bit_extender_2_out, bit_extender_4_out, bit_extender_6_out, divider_1_out,
       divider_1_rem, divider_2_out, divider_2_rem, divider_3_out, divider_3_rem, divider_4_out,
       divider_4_rem, divider_5_out, divider_5_rem, divider_6_out, divider_6_rem, divider_7_out,
       divider_7_rem, divider_8_out, divider_8_rem, divider_9_out, divider_9_rem, divider_10_out,
       divider_10_rem, divider_11_out, divider_11_rem, divider_12_out, divider_12_rem, divider_13_out,
       divider_13_rem, divider_14_out, divider_14_rem, divider_15_out, divider_15_rem, divider_16_out,
       divider_16_rem, divider_17_out, divider_17_rem, divider_18_out, divider_18_rem, multiplier_1_cout,
       multiplier_1_out, multiplier_2_cout, multiplier_2_out, multiplier_3_cout, multiplier_3_out,
       multiplier_4_cout, multiplier_4_out, multiplier_5_cout, multiplier_5_out, multiplier_6_cout,
       multiplier_6_out, multiplier_7_cout, multiplier_7_out, multiplier_8_cout, multiplier_8_out,
       multiplier_9_cout, multiplier_9_out, multiplier_10_cout, multiplier_10_out, multiplier_11_cout,
       multiplier_11_out, multiplier_12_cout, multiplier_12_out, multiplier_13_cout, multiplier_13_out,
       multiplier_14_cout, multiplier_14_out, multiplier_15_cout, multiplier_15_out, multiplier_16_cout,
       multiplier_16_out, multiplier_17_cout, multiplier_17_out, multiplier_18_cout, multiplier_18_out,
       subtractor_1_out, subtractor_2_out, subtractor_3_out;
  wire [2:2] adder_12_out, adder_15_out, adder_18_out;
  wire [11:0] bit_extender_1_out, bit_extender_3_out, bit_extender_5_out;

  assign bit_extender_1_out = {{2{1'b0}}, Object_color[9:0]};  // Bit_Extender bit_extender_1
  assign bit_extender_2_out = {{1{1'b0}}, Back_color_1[1:0]};  // Bit_Extender bit_extender_2
  assign bit_extender_3_out = {{2{1'b0}}, Object_color[19:10]};  // Bit_Extender bit_extender_3
  assign bit_extender_4_out = {{1{1'b0}}, Back_color_2[1:0]};  // Bit_Extender bit_extender_4
  assign bit_extender_5_out = {{2{1'b0}}, Object_color[29:20]};  // Bit_Extender bit_extender_5
  assign bit_extender_6_out = {{1{1'b0}}, Back_color_3[1:0]};  // Bit_Extender bit_extender_6
  Multiplier #(.width(3)) multiplier_1 (
    .a(Back_color_1[7:5]), .b(subtractor_1_out), .out(multiplier_1_out), .cout(multiplier_1_cout));  // open: cin
  Subtractor #(.width(3)) subtractor_1 (
    .a(3'b011), .b(bit_extender_1_out[10:8]), .out(subtractor_1_out));  // open: bin, bout
  Multiplier #(.width(3)) multiplier_2 (
    .a(bit_extender_1_out[10:8]), .b(bit_extender_1_out[7:5]), .out(multiplier_2_out),
    .cout(multiplier_2_cout));  // open: cin
  Divider #(.width(3)) divider_1 (
    .a(multiplier_2_out), .b(3'b011), .out(divider_1_out), .upper(multiplier_2_cout), .rem(divider_1_rem));
  Multiplier #(.width(3)) multiplier_3 (
    .a(Back_color_1[4:2]), .b(subtractor_1_out), .out(multiplier_3_out), .cout(multiplier_3_cout));  // open: cin
  Multiplier #(.width(3)) multiplier_4 (
    .a(bit_extender_1_out[4:2]), .b(bit_extender_1_out[10:8]), .out(multiplier_4_out),
    .cout(multiplier_4_cout));  // open: cin
  Divider #(.width(3)) divider_2 (
    .a(multiplier_4_out), .b(3'b011), .out(divider_2_out), .upper(multiplier_4_cout), .rem(divider_2_rem));
  Multiplier #(.width(3)) multiplier_5 (
    .a(subtractor_1_out), .b(bit_extender_2_out), .out(multiplier_5_out), .cout(multiplier_5_cout));  // open: cin
  Multiplier #(.width(3)) multiplier_6 (
    .a(bit_extender_1_out[10:8]), .b({bit_extender_1_out[11], bit_extender_1_out[1:0]}),
    .out(multiplier_6_out), .cout(multiplier_6_cout));  // open: cin
  Divider #(.width(3)) divider_3 (
    .a(multiplier_6_out), .b(3'b011), .out(divider_3_out), .upper(multiplier_6_cout), .rem(divider_3_rem));
  Multiplier #(.width(3)) multiplier_7 (
    .a(Back_color_2[7:5]), .b(subtractor_2_out), .out(multiplier_7_out), .cout(multiplier_7_cout));  // open: cin
  Subtractor #(.width(3)) subtractor_2 (
    .a(3'b011), .b(bit_extender_3_out[10:8]), .out(subtractor_2_out));  // open: bin, bout
  Multiplier #(.width(3)) multiplier_8 (
    .a(bit_extender_3_out[10:8]), .b(bit_extender_3_out[7:5]), .out(multiplier_8_out),
    .cout(multiplier_8_cout));  // open: cin
  Divider #(.width(3)) divider_4 (
    .a(multiplier_8_out), .b(3'b011), .out(divider_4_out), .upper(multiplier_8_cout), .rem(divider_4_rem));
  Multiplier #(.width(3)) multiplier_9 (
    .a(Back_color_2[4:2]), .b(subtractor_2_out), .out(multiplier_9_out), .cout(multiplier_9_cout));  // open: cin
  Multiplier #(.width(3)) multiplier_10 (
    .a(bit_extender_3_out[4:2]), .b(bit_extender_3_out[10:8]), .out(multiplier_10_out),
    .cout(multiplier_10_cout));  // open: cin
  Divider #(.width(3)) divider_5 (
    .a(multiplier_10_out), .b(3'b011), .out(divider_5_out), .upper(multiplier_10_cout), .rem(divider_5_rem));
  Multiplier #(.width(3)) multiplier_11 (
    .a(subtractor_2_out), .b(bit_extender_4_out), .out(multiplier_11_out), .cout(multiplier_11_cout));  // open: cin
  Multiplier #(.width(3)) multiplier_12 (
    .a(bit_extender_3_out[10:8]), .b({bit_extender_3_out[11], bit_extender_3_out[1:0]}),
    .out(multiplier_12_out), .cout(multiplier_12_cout));  // open: cin
  Divider #(.width(3)) divider_6 (
    .a(multiplier_12_out), .b(3'b011), .out(divider_6_out), .upper(multiplier_12_cout), .rem(divider_6_rem));
  Multiplier #(.width(3)) multiplier_13 (
    .a(Back_color_3[7:5]), .b(subtractor_3_out), .out(multiplier_13_out), .cout(multiplier_13_cout));  // open: cin
  Subtractor #(.width(3)) subtractor_3 (
    .a(3'b011), .b(bit_extender_5_out[10:8]), .out(subtractor_3_out));  // open: bin, bout
  Multiplier #(.width(3)) multiplier_14 (
    .a(bit_extender_5_out[10:8]), .b(bit_extender_5_out[7:5]), .out(multiplier_14_out),
    .cout(multiplier_14_cout));  // open: cin
  Divider #(.width(3)) divider_7 (
    .a(multiplier_14_out), .b(3'b011), .out(divider_7_out), .upper(multiplier_14_cout), .rem(divider_7_rem));
  Multiplier #(.width(3)) multiplier_15 (
    .a(Back_color_3[4:2]), .b(subtractor_3_out), .out(multiplier_15_out), .cout(multiplier_15_cout));  // open: cin
  Multiplier #(.width(3)) multiplier_16 (
    .a(bit_extender_5_out[4:2]), .b(bit_extender_5_out[10:8]), .out(multiplier_16_out),
    .cout(multiplier_16_cout));  // open: cin
  Divider #(.width(3)) divider_8 (
    .a(multiplier_16_out), .b(3'b011), .out(divider_8_out), .upper(multiplier_16_cout), .rem(divider_8_rem));
  Multiplier #(.width(3)) multiplier_17 (
    .a(subtractor_3_out), .b(bit_extender_6_out), .out(multiplier_17_out), .cout(multiplier_17_cout));  // open: cin
  Multiplier #(.width(3)) multiplier_18 (
    .a(bit_extender_5_out[10:8]), .b({bit_extender_5_out[11], bit_extender_5_out[1:0]}),
    .out(multiplier_18_out), .cout(multiplier_18_cout));  // open: cin
  Divider #(.width(3)) divider_9 (
    .a(multiplier_18_out), .b(3'b011), .out(divider_9_out), .upper(multiplier_18_cout), .rem(divider_9_rem));
  Divider #(.width(3)) divider_10 (
    .a(multiplier_1_out), .b(3'b011), .out(divider_10_out), .upper(multiplier_1_cout), .rem(divider_10_rem));
  Adder #(.width(3)) adder_1 (.a(divider_10_rem), .b(divider_1_rem), .out(adder_1_out));  // open: cin, cout
  Comparator #(.width(3), .mode("unsigned")) comparator_1 (
    .a(adder_1_out), .b(3'b001), .gt(comparator_1_gt));  // open: eq, lt
  Divider #(.width(3)) divider_11 (
    .a(multiplier_3_out), .b(3'b011), .out(divider_11_out), .upper(multiplier_3_cout), .rem(divider_11_rem));
  Adder #(.width(3)) adder_2 (.a(divider_11_rem), .b(divider_2_rem), .out(adder_2_out));  // open: cin, cout
  Divider #(.width(3)) divider_12 (
    .a(multiplier_5_out), .b(3'b011), .out(divider_12_out), .upper(multiplier_5_cout), .rem(divider_12_rem));
  Adder #(.width(3)) adder_3 (.a(divider_12_rem), .b(divider_3_rem), .out(adder_3_out));  // open: cin, cout
  Comparator #(.width(3), .mode("unsigned")) comparator_2 (
    .a(adder_3_out), .b(3'b001), .gt(comparator_2_gt));  // open: eq, lt
  Divider #(.width(3)) divider_13 (
    .a(multiplier_7_out), .b(3'b011), .out(divider_13_out), .upper(multiplier_7_cout), .rem(divider_13_rem));
  Adder #(.width(3)) adder_4 (.a(divider_13_rem), .b(divider_4_rem), .out(adder_4_out));  // open: cin, cout
  Comparator #(.width(3), .mode("unsigned")) comparator_3 (
    .a(adder_4_out), .b(3'b001), .gt(comparator_3_gt));  // open: eq, lt
  Divider #(.width(3)) divider_14 (
    .a(multiplier_9_out), .b(3'b011), .out(divider_14_out), .upper(multiplier_9_cout), .rem(divider_14_rem));
  Adder #(.width(3)) adder_5 (.a(divider_14_rem), .b(divider_5_rem), .out(adder_5_out));  // open: cin, cout
  Divider #(.width(3)) divider_15 (
    .a(multiplier_11_out), .b(3'b011), .out(divider_15_out), .upper(multiplier_11_cout), .rem(divider_15_rem));
  Adder #(.width(3)) adder_6 (.a(divider_15_rem), .b(divider_6_rem), .out(adder_6_out));  // open: cin, cout
  Comparator #(.width(3), .mode("unsigned")) comparator_4 (
    .a(adder_6_out), .b(3'b001), .gt(comparator_4_gt));  // open: eq, lt
  Divider #(.width(3)) divider_16 (
    .a(multiplier_13_out), .b(3'b011), .out(divider_16_out), .upper(multiplier_13_cout), .rem(divider_16_rem));
  Adder #(.width(3)) adder_7 (.a(divider_16_rem), .b(divider_7_rem), .out(adder_7_out));  // open: cin, cout
  Comparator #(.width(3), .mode("unsigned")) comparator_5 (
    .a(adder_7_out), .b(3'b001), .gt(comparator_5_gt));  // open: eq, lt
  Divider #(.width(3)) divider_17 (
    .a(multiplier_15_out), .b(3'b011), .out(divider_17_out), .upper(multiplier_15_cout), .rem(divider_17_rem));
  Adder #(.width(3)) adder_8 (.a(divider_17_rem), .b(divider_8_rem), .out(adder_8_out));  // open: cin, cout
  Divider #(.width(3)) divider_18 (
    .a(multiplier_17_out), .b(3'b011), .out(divider_18_out), .upper(multiplier_17_cout), .rem(divider_18_rem));
  Adder #(.width(3)) adder_9 (.a(divider_18_rem), .b(divider_9_rem), .out(adder_9_out));  // open: cin, cout
  Comparator #(.width(3), .mode("unsigned")) comparator_6 (
    .a(adder_9_out), .b(3'b001), .gt(comparator_6_gt));  // open: eq, lt
  Adder #(.width(3)) adder_10 (
    .a(divider_10_out), .b(divider_1_out), .out(out_5[7:5]), .cin(comparator_1_gt));  // open: cout
  Comparator #(.width(3), .mode("unsigned")) comparator_7 (
    .a(adder_2_out), .b(3'b001), .gt(comparator_7_gt));  // open: eq, lt
  Adder #(.width(3)) adder_11 (
    .a(divider_11_out), .b(divider_2_out), .out(out_5[4:2]), .cin(comparator_7_gt));  // open: cout
  Adder #(.width(3)) adder_12 (
    .a(divider_12_out), .b(divider_3_out), .out({adder_12_out[2], out_5[1:0]}), .cin(comparator_2_gt));  // open: cout
  Adder #(.width(3)) adder_13 (
    .a(divider_13_out), .b(divider_4_out), .out(out_6[7:5]), .cin(comparator_3_gt));  // open: cout
  Comparator #(.width(3), .mode("unsigned")) comparator_8 (
    .a(adder_5_out), .b(3'b001), .gt(comparator_8_gt));  // open: eq, lt
  Adder #(.width(3)) adder_14 (
    .a(divider_14_out), .b(divider_5_out), .out(out_6[4:2]), .cin(comparator_8_gt));  // open: cout
  Adder #(.width(3)) adder_15 (
    .a(divider_15_out), .b(divider_6_out), .out({adder_15_out[2], out_6[1:0]}), .cin(comparator_4_gt));  // open: cout
  Adder #(.width(3)) adder_16 (
    .a(divider_16_out), .b(divider_7_out), .out(out_7[7:5]), .cin(comparator_5_gt));  // open: cout
  Comparator #(.width(3), .mode("unsigned")) comparator_9 (
    .a(adder_8_out), .b(3'b001), .gt(comparator_9_gt));  // open: eq, lt
  Adder #(.width(3)) adder_17 (
    .a(divider_17_out), .b(divider_8_out), .out(out_7[4:2]), .cin(comparator_9_gt));  // open: cout
  Adder #(.width(3)) adder_18 (
    .a(divider_18_out), .b(divider_9_out), .out({adder_18_out[2], out_7[1:0]}), .cin(comparator_6_gt));  // open: cout

  // Notes on the sheet:
  //   This will do a weighted average between the current pixel color and the new pixel color, taking count its transparency
  //   Final Color = Oldcolor(1-New Color Opacity)/3 + New Color*Opacity/3
  //   Opacity is a inputted value between 0 and 3, and due to the math, will stands between 0 and 1.
  //   Again, it's a mess just because it seems that the fewer the wire nodes, faster the simulation will be.
  //   Final color values are rounded to nearest integer.
endmodule

module Tools (
);


  // Notes on the sheet:
  //   just a separator
endmodule

module Text_to_Hex_tool_for_you (
  input  Reset
);

  wire Clock_out, counter_1_carry, or_1_out, or_2_out;
  wire [6:0] keyboard_1_data;
  wire [7:0] counter_2_q;
  wire [31:0] adder_1_out, bit_extender_1_out, register_1_q, shifter_1_out;

  Keyboard #(.buflen(255)) keyboard_1 (.clk(Clock_out), .clr(Reset), .data(keyboard_1_data));  // open: re, avail
  assign bit_extender_1_out = {{25{1'b0}}, keyboard_1_data};  // Bit_Extender bit_extender_1
  Adder #(.width(32)) adder_1 (.a(bit_extender_1_out), .b(register_1_q), .out(adder_1_out));  // open: cin, cout
  Shifter #(.width(32)) shifter_1 (.in(adder_1_out), .\dist (5'b01000), .out(shifter_1_out));
  Button Clock (.out(Clock_out));
  Counter #(.max('h4), .ongoal("stay")) counter_1 (
    .carry(counter_1_carry), .clk(Clock_out), .clr(or_1_out));  // open: load, D, count, Q
  or or_1 (or_1_out, counter_1_carry, Reset);
  Register #(.width(32)) register_1 (.D(shifter_1_out), .Q(register_1_q), .clk(Clock_out), .clr(or_2_out));  // open: en
  or or_2 (or_2_out, counter_1_carry, Reset);
  Counter #(.ongoal("stay")) counter_2 (
    .Q(counter_2_q), .clk(counter_1_carry), .clr(Reset));  // open: load, D, count, carry
  // RAM ram_1: pin names not known; wires that end beside it: counter_2_q, adder_1_out, counter_1_carry, Reset

  // Notes on the sheet:
  //   I used this for the "Logiwin Open blablabla" on the main screen
  //   This is temporary.
  //   Type the desired text in the keyboard. For each 4 clocks, 1 grouped (4-characters) ASCII will pops out in this RAM
endmodule

module Temporary (
);


  // Notes on the sheet:
  //   just a separator
endmodule

module GPU_2__primitive__used_on_Mario (
  input  [7:0] Row_Selector,
  input  [7:0] Pixel_Color,
  input  Reset,
  input  Power,
  input  [4:0] Column_Selector,
  input  Clock,
  input  Done_with_this_pixel,
  output [4:0] Column_Screen_Selector,
  output [7:0] out_9,
  output [7:0] out_10,
  output [7:0] out_11,
  output [7:0] out_12,
  output [7:0] out_13,
  output [7:0] out_14,
  output [7:0] out_15,
  output [7:0] out_16,
  output [7:0] out_17,
  output [7:0] out_18,
  output [7:0] out_19,
  output [7:0] out_20,
  output [7:0] out_21,
  output [7:0] out_22,
  output [7:0] out_23,
  output [7:0] out_24,
  output [7:0] out_25,
  output [7:0] out_26,
  output [7:0] out_27,
  output [7:0] out_28,
  output [7:0] out_29,
  output [7:0] out_30,
  output [7:0] out_31,
  output [7:0] out_32,
  output [7:0] out_33,
  output [7:0] out_34,
  output [7:0] out_35,
  output [7:0] out_36,
  output [7:0] out_37,
  output [7:0] out_38,
  output [7:0] out_39,
  output [7:0] out_40,
  output Reset_2,
  output Update_Screen
);

  wire buffer_1_out, buffer_2_out, counter_1_carry, decoder_1_out0, decoder_1_out1, decoder_1_out2,
       decoder_1_out3, decoder_1_out4, decoder_1_out5, decoder_1_out6, decoder_1_out7, decoder_1_out8,
       decoder_1_out9, decoder_1_out10, decoder_1_out11, decoder_1_out12, decoder_1_out13, decoder_1_out14,
       decoder_1_out15, decoder_1_out16, decoder_1_out17, decoder_1_out18, decoder_1_out19, decoder_1_out20,
       decoder_1_out21, decoder_1_out22, decoder_1_out23, decoder_1_out24, decoder_1_out25, decoder_1_out26,
       decoder_1_out27, decoder_1_out28, decoder_1_out29, decoder_1_out30, decoder_1_out31, not_1_out,
       or_3_out, pull_resistor_4_node, pull_resistor_6_node, register_1_q, transistor_3_out;
  wire [7:0] bit_extender_1_out, or_2_out, pull_resistor_1_node, transistor_2_out;

  Counter #(.width(5), .max('h17), .ongoal("stay"), .trigger("falling")) counter_1 (
    .count(register_1_q), .Q(Column_Screen_Selector), .carry(counter_1_carry), .clk(Clock), .clr(Reset_2));  // open: load, D
  Pull_Resistor #(.pull(1)) pull_resistor_1 (.node(pull_resistor_1_node));
  buf buffer_1 (buffer_1_out, counter_1_carry);
  Transistor #(.gate("br")) transistor_1 (.in(counter_1_carry), .out(Update_Screen), .gate(buffer_1_out));
  Pull_Resistor pull_resistor_2 (.node(Update_Screen));
  assign bit_extender_1_out = {{3{1'b0}}, Column_Screen_Selector};  // Bit_Extender bit_extender_1
  or or_1 (Reset_2, Reset, not_1_out);
  not not_1 (not_1_out, Power);
  Transistor #(.width(8)) transistor_2 (.in(pull_resistor_1_node), .out(transistor_2_out), .gate(Power));
  Pull_Resistor pull_resistor_3 (.node(transistor_2_out));
  buf buffer_2 (buffer_2_out, Power);
  assign or_2_out = bit_extender_1_out | transistor_2_out;  // OR_Gate or_2, 8 bits wide
  Register #(.width(1), .trigger("high")) register_1 (
    .D(or_3_out), .Q(register_1_q), .clk(or_3_out), .clr(pull_resistor_4_node));  // open: en
  Transistor transistor_3 (.in(Power), .out(transistor_3_out), .gate(buffer_2_out));
  Pull_Resistor pull_resistor_4 (.node(pull_resistor_4_node));
  Transistor #(.gate("br")) transistor_4 (.in(counter_1_carry), .out(pull_resistor_4_node), .gate(or_3_out));
  or or_3 (or_3_out, transistor_3_out, pull_resistor_6_node);
  Pull_Resistor pull_resistor_5 (.node(transistor_3_out));
  Pull_Resistor pull_resistor_6 (.node(pull_resistor_6_node));
  Transistor #(.\type ("n"), .gate("br")) transistor_5 (
    .in(Clock), .out(pull_resistor_6_node), .gate(Done_with_this_pixel));
  Decoder #(.select(5), .disabled(0)) decoder_1 (
    .out0(decoder_1_out0), .out1(decoder_1_out1), .out2(decoder_1_out2), .out3(decoder_1_out3),
    .out4(decoder_1_out4), .out5(decoder_1_out5), .out6(decoder_1_out6), .out7(decoder_1_out7),
    .out8(decoder_1_out8), .out9(decoder_1_out9), .out10(decoder_1_out10), .out11(decoder_1_out11),
    .out12(decoder_1_out12), .out13(decoder_1_out13), .out14(decoder_1_out14), .out15(decoder_1_out15),
    .out16(decoder_1_out16), .out17(decoder_1_out17), .out18(decoder_1_out18), .out19(decoder_1_out19),
    .out20(decoder_1_out20), .out21(decoder_1_out21), .out22(decoder_1_out22), .out23(decoder_1_out23),
    .out24(decoder_1_out24), .out25(decoder_1_out25), .out26(decoder_1_out26), .out27(decoder_1_out27),
    .out28(decoder_1_out28), .out29(decoder_1_out29), .out30(decoder_1_out30), .out31(decoder_1_out31),
    .sel(Column_Selector), .en(pull_resistor_6_node));
  // RAM ram_1: pin names not known; wires that end beside it: Row_Selector, decoder_1_out0, Reset, out_9, Row_Selector
  // RAM ram_2: pin names not known; wires that end beside it: decoder_1_out1, Reset, out_10, Row_Selector
  // RAM ram_3: pin names not known; wires that end beside it: decoder_1_out2, Reset, out_11, Row_Selector
  // RAM ram_4: pin names not known; wires that end beside it: decoder_1_out3, Reset, out_12, Row_Selector
  // RAM ram_5: pin names not known; wires that end beside it: decoder_1_out4, Reset, out_13, Row_Selector
  // RAM ram_6: pin names not known; wires that end beside it: decoder_1_out5, Reset, out_14, Row_Selector
  // RAM ram_7: pin names not known; wires that end beside it: decoder_1_out6, Reset, out_15, Row_Selector
  // RAM ram_8: pin names not known; wires that end beside it: decoder_1_out7, Reset, out_16, Row_Selector
  // RAM ram_9: pin names not known; wires that end beside it: decoder_1_out8, Reset, out_17, Row_Selector
  // RAM ram_10: pin names not known; wires that end beside it: decoder_1_out9, Reset, out_18, Row_Selector
  // RAM ram_11: pin names not known; wires that end beside it: decoder_1_out10, Reset, out_19, Row_Selector
  // RAM ram_12: pin names not known; wires that end beside it: decoder_1_out11, Reset, out_20, Row_Selector
  // RAM ram_13: pin names not known; wires that end beside it: decoder_1_out12, Reset, out_21, Row_Selector
  // RAM ram_14: pin names not known; wires that end beside it: decoder_1_out13, Reset, out_22, Row_Selector
  // RAM ram_15: pin names not known; wires that end beside it: decoder_1_out14, Reset, out_23, Row_Selector
  // RAM ram_16: pin names not known; wires that end beside it: decoder_1_out15, Reset, out_24, Row_Selector
  // RAM ram_17: pin names not known; wires that end beside it: decoder_1_out16, Reset, out_25, Row_Selector
  // RAM ram_18: pin names not known; wires that end beside it: decoder_1_out17, Reset, out_26, Row_Selector
  // RAM ram_19: pin names not known; wires that end beside it: decoder_1_out18, Reset, out_27, Row_Selector
  // RAM ram_20: pin names not known; wires that end beside it: decoder_1_out19, Reset, out_28, Row_Selector
  // RAM ram_21: pin names not known; wires that end beside it: decoder_1_out20, Reset, out_29, Row_Selector
  // RAM ram_22: pin names not known; wires that end beside it: decoder_1_out21, Reset, out_30, Row_Selector
  // RAM ram_23: pin names not known; wires that end beside it: decoder_1_out22, Reset, out_31, Row_Selector
  // RAM ram_24: pin names not known; wires that end beside it: decoder_1_out23, Reset, out_32, Row_Selector
  // RAM ram_25: pin names not known; wires that end beside it: decoder_1_out24, Reset, out_33, Row_Selector
  // RAM ram_26: pin names not known; wires that end beside it: decoder_1_out25, Reset, out_34, Row_Selector
  // RAM ram_27: pin names not known; wires that end beside it: decoder_1_out26, Reset, out_35, Row_Selector
  // RAM ram_28: pin names not known; wires that end beside it: decoder_1_out27, Reset, out_36, Row_Selector
  // RAM ram_29: pin names not known; wires that end beside it: decoder_1_out28, Reset, out_37, Row_Selector
  // RAM ram_30: pin names not known; wires that end beside it: decoder_1_out29, Reset, out_38, Row_Selector
  // RAM ram_31: pin names not known; wires that end beside it: decoder_1_out30, Reset, out_39, Row_Selector, {Pixel_Color[1:0], Pixel_Color[4:2], Pixel_Color[7:5]}
  // RAM ram_32: pin names not known; wires that end beside it: decoder_1_out31, Reset, out_40, Row_Selector, or_2_out

  // Notes on the sheet:
  //   That one is to load the Mario on load
  //   But won't have an use on future.
  //   This above is to avoid some visual bugs
endmodule

module Unused__wait_for_the_future (
);


  // Notes on the sheet:
  //   just a separator
endmodule

module Soundboard_w__Speakers__not_used_yet (
  input  [31:0] In,
  input  in_2
);

  wire bitfinder_1_found, pull_resistor_1_node, pull_resistor_4_node, pull_resistor_5_node,
       pull_resistor_7_node, pull_resistor_11_node, undriven, undriven_2, undriven_7;
  wire [3:0] undriven_3, undriven_4, undriven_5;
  wire [4:0] pull_resistor_9_node, undriven_6;
  wire [6:0] bit_extender_2_out, bit_extender_4_out, bit_extender_6_out, bit_extender_7_out;
  wire [7:0] counter_1_q;
  wire [13:0] random_1_out, random_2_out, random_3_out;
  wire [15:0] bit_extender_1_out, bit_extender_3_out, bit_extender_5_out, bit_extender_8_out,
       pull_resistor_8_node, transistor_1_out, transistor_2_out, transistor_3_out;
  wire [17:0] rom_1_data;

  RAM #(.addrWidth(12), .dataWidth(32)) ram_1 ();  // open: addr, data, sel, clk, ld, clr
  Pull_Resistor pull_resistor_1 (.node(pull_resistor_1_node));
  Random #(.width(14)) random_1 (.clk(undriven), .out(random_1_out));  // open: next, clr
  Random #(.width(14)) random_2 (.clk(undriven_2), .out(random_2_out));  // open: next, clr
  assign bit_extender_1_out = {{2{1'b0}}, random_1_out};  // Bit_Extender bit_extender_1
  // Probe on bit_extender_1_out
  Transistor #(.\type ("n"), .width(16)) transistor_1 (
    .in(bit_extender_1_out), .out(transistor_1_out), .gate(pull_resistor_1_node));
  Pull_Resistor pull_resistor_2 (.node(transistor_1_out));
  assign bit_extender_2_out = {{3{1'b0}}, undriven_3};  // Bit_Extender bit_extender_2
  assign bit_extender_3_out = {{2{1'b0}}, random_2_out};  // Bit_Extender bit_extender_3
  // Probe on bit_extender_3_out
  Transistor #(.\type ("n"), .width(16)) transistor_2 (
    .in(bit_extender_3_out), .out(transistor_2_out), .gate(pull_resistor_1_node));
  Pull_Resistor pull_resistor_3 (.node(transistor_2_out));
  assign bit_extender_4_out = {{3{1'b0}}, undriven_4};  // Bit_Extender bit_extender_4
  Pull_Resistor #(.pull(1)) pull_resistor_4 (.node(pull_resistor_4_node));
  Pull_Resistor #(.pull(1)) pull_resistor_5 (.node(pull_resistor_5_node));
  Random #(.width(14)) random_3 (.out(random_3_out));  // open: clk, next, clr
  assign bit_extender_5_out = {{2{1'b0}}, random_3_out};  // Bit_Extender bit_extender_5
  // Probe on bit_extender_5_out
  Transistor #(.\type ("n"), .width(16)) transistor_3 (
    .in(bit_extender_5_out), .out(transistor_3_out), .gate(pull_resistor_1_node));
  Pull_Resistor pull_resistor_6 (.node(transistor_3_out));
  Pull_Resistor #(.pull(1)) pull_resistor_7 (.node(pull_resistor_7_node));
  assign bit_extender_6_out = {{3{1'b0}}, undriven_5};  // Bit_Extender bit_extender_6
  Counter #(.max('h12), .ongoal("load")) counter_1 (
    .Q(counter_1_q), .clk(undriven_7));  // open: load, D, count, carry, clr
  ROM #(.dataWidth(18)) rom_1 (.addr(counter_1_q), .data(rom_1_data));  // open: sel
  Pull_Resistor pull_resistor_8 (.node(pull_resistor_8_node));
  BitFinder #(.width(16)) bitfinder_1 (.in(pull_resistor_8_node), .found(bitfinder_1_found));  // open: index
  assign bit_extender_7_out = {{2{1'b0}}, pull_resistor_9_node};  // Bit_Extender bit_extender_7
  Pull_Resistor pull_resistor_9 (.node(pull_resistor_9_node));
  Transistor #(.\type ("n"), .width(5)) transistor_4 (
    .in(undriven_6), .out(pull_resistor_9_node), .gate(bitfinder_1_found));
  // Probe on pull_resistor_9_node
  Pull_Resistor pull_resistor_10 ();  // open: node
  assign bit_extender_8_out = {{2{1'b0}}, rom_1_data[13:0]};  // Bit_Extender bit_extender_8
  // Probe on bit_extender_8_out
  Pull_Resistor #(.pull(1)) pull_resistor_11 (.node(pull_resistor_11_node));

  // Notes on the sheet:
  //    It will consist of 4 channels sound system, but i am having some problems with this mod for now.
  //   contents of rom_1 (hex, n*v repeats v):
  //   0 93 dc 126 174 126 dc
  //   Still working on it! I use the only available sound mod that i found, the "buzzer".
  //   (Removed the mod for now from the circ, later I will update it)
  //   Sound format:
  //   First 14 bits for frequency
  //   14~18  for volume
endmodule

module RGB_fix (
  input  [7:0] in_1,
  output [7:0] out_2
);


  assign out_2 = {in_1[1:0], in_1[4:2], in_1[7:5]};
endmodule

module Old_mario_gpu (
  input  [7:0] RGB__3_3_2,
  input  Update_that_pixel
);

  wire button_2_out, button_3_out, button_4_out, button_5_out, button_out, C, decoder_2_out0, decoder_2_out1,
       decoder_2_out2, decoder_2_out3, decoder_2_out4, decoder_2_out5, decoder_2_out6, decoder_2_out7,
       decoder_2_out8, decoder_2_out9, decoder_2_out10, decoder_2_out11, decoder_2_out12, decoder_2_out13,
       decoder_2_out14, decoder_2_out15, decoder_2_out16, decoder_2_out17, decoder_2_out18, decoder_2_out19,
       decoder_2_out20, decoder_2_out21, decoder_2_out22, decoder_2_out23, decoder_2_out24, decoder_2_out25,
       decoder_2_out26, decoder_2_out27, decoder_2_out28, decoder_2_out29, decoder_2_out30, decoder_2_out31,
       dotmatrix2_1_p1, or_1_out, or_2_out, or_3_out, P;
  wire [4:0] bit_extender_1_out, Column_q;
  wire [7:0] Row_q;
  wire [23:0] decoder_1_out23;

  Decoder #(.select(5), .enable("false")) decoder_1 (
    .out0(decoder_1_out23[23]), .out1(decoder_1_out23[22]), .out2(decoder_1_out23[21]),
    .out3(decoder_1_out23[20]), .out4(decoder_1_out23[19]), .out5(decoder_1_out23[18]),
    .out6(decoder_1_out23[17]), .out7(decoder_1_out23[16]), .out8(decoder_1_out23[15]),
    .out9(decoder_1_out23[14]), .out10(decoder_1_out23[13]), .out11(decoder_1_out23[12]),
    .out12(decoder_1_out23[11]), .out13(decoder_1_out23[10]), .out14(decoder_1_out23[9]),
    .out15(decoder_1_out23[8]), .out16(decoder_1_out23[7]), .out17(decoder_1_out23[6]),
    .out18(decoder_1_out23[5]), .out19(decoder_1_out23[4]), .out20(decoder_1_out23[3]),
    .out21(decoder_1_out23[2]), .out22(decoder_1_out23[1]), .out23(decoder_1_out23[0]),
    .sel(bit_extender_1_out));  // open: out24, out25, out26, out27, out28, out29, out30, out31
  Button button (.out(button_out));
  Counter #(.width(5), .max('h1f), .ongoal("stay")) Column (
    .load(button_out), .count(or_1_out), .Q(Column_q), .clk(or_1_out));  // open: D, carry, clr
  or or_1 (or_1_out, button_out, button_2_out);
  Button button_2 (.out(button_2_out));
  Button button_3 (.out(button_3_out));
  Button button_4 (.out(button_4_out));
  or or_2 (or_2_out, button_4_out, button_5_out);
  Button button_5 (.out(button_5_out));
  Counter #(.ongoal("stay")) Row (
    .load(button_4_out), .count(or_2_out), .Q(Row_q), .clk(or_2_out));  // open: D, carry, clr
  Bit_Extender #(.out_width(5)) bit_extender_1 (.in(Row_q), .out(bit_extender_1_out));
  // Probe on RGB__3_3_2
  or or_3 (or_3_out, Update_that_pixel, button_3_out);
  Button Reset ();  // open: out
  Decoder #(.select(5), .enable("false")) decoder_2 (
    .out0(decoder_2_out0), .out1(decoder_2_out1), .out2(decoder_2_out2), .out3(decoder_2_out3),
    .out4(decoder_2_out4), .out5(decoder_2_out5), .out6(decoder_2_out6), .out7(decoder_2_out7),
    .out8(decoder_2_out8), .out9(decoder_2_out9), .out10(decoder_2_out10), .out11(decoder_2_out11),
    .out12(decoder_2_out12), .out13(decoder_2_out13), .out14(decoder_2_out14), .out15(decoder_2_out15),
    .out16(decoder_2_out16), .out17(decoder_2_out17), .out18(decoder_2_out18), .out19(decoder_2_out19),
    .out20(decoder_2_out20), .out21(decoder_2_out21), .out22(decoder_2_out22), .out23(decoder_2_out23),
    .out24(decoder_2_out24), .out25(decoder_2_out25), .out26(decoder_2_out26), .out27(decoder_2_out27),
    .out28(decoder_2_out28), .out29(decoder_2_out29), .out30(decoder_2_out30), .out31(decoder_2_out31),
    .sel(Column_q));
  DotMatrix #(.matrixcols(32), .matrixrows(1)) dotmatrix_1 (
    .col0(decoder_2_out0), .col1(decoder_2_out1), .col2(decoder_2_out2), .col3(decoder_2_out3),
    .col4(decoder_2_out4), .col5(decoder_2_out5), .col6(decoder_2_out6), .col7(decoder_2_out7),
    .col8(decoder_2_out8), .col9(decoder_2_out9), .col10(decoder_2_out10), .col11(decoder_2_out11),
    .col12(decoder_2_out12), .col13(decoder_2_out13), .col14(decoder_2_out14), .col15(decoder_2_out15),
    .col16(decoder_2_out16), .col17(decoder_2_out17), .col18(decoder_2_out18), .col19(decoder_2_out19),
    .col20(decoder_2_out20), .col21(decoder_2_out21), .col22(decoder_2_out22), .col23(decoder_2_out23),
    .col24(decoder_2_out24), .col25(decoder_2_out25), .col26(decoder_2_out26), .col27(decoder_2_out27),
    .col28(decoder_2_out28), .col29(decoder_2_out29), .col30(decoder_2_out30), .col31(decoder_2_out31));
  DotMatrix #(.matrixcols(1), .matrixrows(24)) dotmatrix_2 (.col0(decoder_1_out23));
  // DotMatrix2 dotmatrix2_1: pin names not known; wires that end beside it: dotmatrix2_1_p1
  GPU_2__primitive__used_on_Mario gpu_2_primitive_used_on_mario_1 (
    .Clock(C), .Row_Selector(Row_q), .Pixel_Color(RGB__3_3_2), .Column_Selector(Column_q),
    .Done_with_this_pixel(or_3_out), .Reset(dotmatrix2_1_p1), .Power(P));  // open: out_9, out_10, out_11, out_12, out_13, out_14, out_15, out_16, out_17, out_18, out_19, out_20, out_21, out_22, out_23, out_24, Column_Screen_Selector, out_25, out_26, out_27, out_28, out_29, out_30, out_31, out_32, out_33, out_34, out_35, out_36, out_37, out_38, out_39, out_40, Update_Screen, Reset_2
  // Probe on nothing

  // Notes on the sheet:
  //   Size and colors may not represent the officials ones.  Also, this coin is not from this Mario version. Who cares?
  //   Just a primitive way to draw stuff. Turn main computer On first and make sure Tick Frequency is on the max.
  //   Select Row and Column, select color (RGB 8-bit 3-3-2), and when ready push "Update that Pixel", or just leave it On
  //   There will be easier ways to draw stuff, like a Paint Brush program, but I just wanted to draw a Mario. Deal with it.
  //   Actually, made this to think about how GPU should work, and how to make it the most clock eficienccy way.
  //   Yeah I know this row is bugged. I won't mind it, as will only be a waste of time, as I won't use this "GPU".
endmodule
